// Logisim project Lancelot_m1.circ as structural Verilog: 22 circuits, main circuit main
module main (
  input  RESET_BTN,
  input  CLOCK_ENABLE,
  output [15:0] out_3,
  output [15:0] out_4,
  output [15:0] out_5,
  output [15:0] out_6,
  output [15:0] out_7,
  output [15:0] out_8,
  output [15:0] out_9,
  output [15:0] out_10,
  output [15:0] out_11
);

  wire A_AND_B, A_NAND_B, A_NOR_B, A_NOT, A_OR_B, A_XOR_B, alu_1_equal, alu_1_greater, alu_1_lesser,
       alu_1_zero, clock_1_out, CNT_ENB, CNT_OUT, cpu_clock_1_clock, decoder_1_out6, DIV, FLAGS_RESET,
       FLAGS_SET, HALT, INSTRUCT_WRITE, JUMP, KB_REG_POP, KB_REG_READ, MAR_READ, MAR_WRITE, MODULO, MUL,
       not_1_out, not_2_out, not_3_out, OPERAND_READ_TO_L, OPERAND_READ_TO_U, or_1_out, or_2_out, or_3_out,
       or_4_out, or_5_out, or_6_out, or_7_out, or_8_out, or_9_out, RAM_READ, RAM_WRITE, REG_A_READ,
       REG_A_WRITE, REG_B_READ, REG_B_WRITE, REG_C_READ, REG_C_WRITE, REG_D_READ, REG_D_WRITE, STACK_DOWN,
       STACK_DOWN_BY, STACK_POINTER_OUT, STACK_READ, STACK_UP, STACK_UP_BY, STACK_WRITE, STEP_CNT_RESET, SUB,
       SUM, TTY_WRITE;
  wire [3:0] alu_opcode_encoder_1_out_12;
  wire [6:0] keyboard_1_data;
  wire [7:0] instruction_register_1_operand_to_lower_bits_of_bus,
       instruction_register_1_operand_to_upper_bits_of_bus;
  wire [15:0] adder_16_bit_1_sum, multiplexer_1_out, multiplexer_2_out, multiplexer_3_out, ram_1_dout,
       register_16_bit_1_default_output, register_16_bit_2_default_output, twos_comp_16_bit_1_data_out;
  wire [15:11] rom_3_data;

  ROM #(.addrWidth(16), .dataWidth(16)) rom_1 (
    .addr({out_10[15:12], out_8[15:8], out_10[3:0]}),
    .data({HALT, JUMP, STACK_READ, TTY_WRITE, KB_REG_READ, FLAGS_SET, REG_D_READ, REG_C_READ, REG_B_READ, REG_A_READ, OPERAND_READ_TO_L, OPERAND_READ_TO_U, MAR_READ, RAM_READ, CNT_ENB, CNT_OUT}));
  ROM #(.addrWidth(16), .dataWidth(16)) rom_2 (
    .addr({out_10[15:12], out_8[15:8], out_10[3:0]}),
    .data({STACK_DOWN_BY, STACK_UP_BY, STACK_POINTER_OUT, STEP_CNT_RESET, STACK_DOWN, STACK_UP, STACK_WRITE, KB_REG_POP, FLAGS_RESET, REG_D_WRITE, REG_C_WRITE, REG_B_WRITE, REG_A_WRITE, INSTRUCT_WRITE, MAR_WRITE, RAM_WRITE}));
  ROM #(.addrWidth(16), .dataWidth(16)) rom_3 (
    .addr({out_10[15:12], out_8[15:8], out_10[3:0]}),
    .data({rom_3_data, A_NOR_B, A_NAND_B, A_XOR_B, A_OR_B, A_AND_B, A_NOT, MODULO, DIV, MUL, SUB, SUM}));
  Clock clock_1 (.out(clock_1_out));
  CPU_CLOCK cpu_clock_1 (
    .INPUT_CLOCK(clock_1_out), .CLOCK_ENABLE(CLOCK_ENABLE), .HALT(HALT), .CLOCK(cpu_clock_1_clock));
  not not_1 (not_1_out, cpu_clock_1_clock);
  or or_1 (or_1_out, decoder_1_out6, STEP_CNT_RESET, RESET_BTN);
  or or_2 (or_2_out, STACK_UP, STACK_DOWN);
  not not_2 (not_2_out, or_2_out);
  or or_3 (or_3_out, STACK_DOWN_BY, STACK_UP_BY);
  REGISTER_16_BIT register_16_bit_1 (
    .WRITE(not_2_out), .CLOCK(not_2_out), .RESET(RESET_BTN), .DATA_IN(register_16_bit_2_default_output),
    .DEFAULT_OUTPUT(register_16_bit_1_default_output));
  Multiplexer #(.width(16)) multiplexer_1 (
    .in0(16'h1),
    .in1({instruction_register_1_operand_to_upper_bits_of_bus, instruction_register_1_operand_to_lower_bits_of_bus}),
    .out(multiplexer_1_out), .sel(or_3_out));
  STEP_COUNTER step_counter_1 (.RESET(or_1_out), .CLOCK(not_1_out), .DATA_OUT(out_10[3:0]));
  Multiplexer #(.width(16)) multiplexer_2 (
    .in0(multiplexer_1_out), .in1(twos_comp_16_bit_1_data_out), .out(multiplexer_2_out), .sel(or_4_out));
  TWOS_COMP_16_BIT twos_comp_16_bit_1 (.DATA_IN(multiplexer_1_out), .DATA_OUT(twos_comp_16_bit_1_data_out));
  or or_4 (or_4_out, not_3_out, STACK_DOWN);
  not not_3 (not_3_out, STACK_UP);
  Decoder #(.select(4)) decoder_1 (
    .out6(decoder_1_out6), .sel(out_10[3:0]));  // open: out0, out1, out2, out3, out4, out5, out7, out8, out9, out10, out11, out12, out13, out14, out15, en
  ADDER_16_BIT adder_16_bit_1 (
    .A(register_16_bit_1_default_output), .B(multiplexer_2_out), .SUM(adder_16_bit_1_sum));  // open: CARRY_IN, CARRY_OUT
  REGISTER_16_BIT register_16_bit_2 (
    .WRITE(or_2_out), .CLOCK(or_2_out), .RESET(RESET_BTN), .DATA_IN(adder_16_bit_1_sum),
    .DEFAULT_OUTPUT(register_16_bit_2_default_output));
  SUBTRACTOR_16_BIT subtractor_16_bit_1 (
    .A({16{1'b1}}), .B(register_16_bit_2_default_output), .SUB(out_5));  // open: BORROW_IN, BORROW_OUT
  or or_5 (or_5_out, STACK_WRITE, STACK_READ);
  Multiplexer #(.width(16)) multiplexer_3 (.in0(out_6), .in1(out_5), .out(multiplexer_3_out), .sel(or_5_out));
  RAM #(.addrWidth(16), .dataWidth(16), .enables("line"), .\type ("nonvolatile")) ram_1 (
    .addr(multiplexer_3_out), .we(or_6_out), .clk(cpu_clock_1_clock),
    .din({instruction_register_1_operand_to_upper_bits_of_bus, instruction_register_1_operand_to_lower_bits_of_bus}),
    .dout(ram_1_dout));
  or or_6 (or_6_out, STACK_WRITE, RAM_WRITE);
  or or_7 (or_7_out, STACK_READ, RAM_READ);
  INSTRUCTION_REGISTER instruction_register_1 (
    .INSTRUCTION_WRITE(INSTRUCT_WRITE), .CLOCK(cpu_clock_1_clock),
    .INSTRUCTION_IN({instruction_register_1_operand_to_upper_bits_of_bus, instruction_register_1_operand_to_lower_bits_of_bus}),
    .RESET(RESET_BTN), .READ_OPERAND_TO_UPPER_BITS_OF_BUS(OPERAND_READ_TO_U),
    .READ_OPERAND_TO_LOWER_BITS_OF_BUS(OPERAND_READ_TO_L),
    .OPERAND_TO_UPPER_BITS_OF_BUS(instruction_register_1_operand_to_upper_bits_of_bus),
    .OPERAND_TO_LOWER_BITS_OF_BUS(instruction_register_1_operand_to_lower_bits_of_bus),
    .INSTRUCTION_OUT(out_8));
  MEMORY_ADDRESS_REGISTER memory_address_register_1 (
    .ADDRESS_IN({instruction_register_1_operand_to_upper_bits_of_bus, instruction_register_1_operand_to_lower_bits_of_bus}),
    .CLOCK(cpu_clock_1_clock), .RESET(RESET_BTN), .ADDRESS_READ(MAR_READ), .ADDRESS_WRITE(MAR_WRITE),
    .BUS_OUT({instruction_register_1_operand_to_upper_bits_of_bus, instruction_register_1_operand_to_lower_bits_of_bus}),
    .DEFAULT_OUT(out_6));
  assign {instruction_register_1_operand_to_upper_bits_of_bus, instruction_register_1_operand_to_lower_bits_of_bus} = STACK_POINTER_OUT ? out_5 : 16'bz;  // Controlled_Buffer controlled_buffer_1
  assign {instruction_register_1_operand_to_upper_bits_of_bus, instruction_register_1_operand_to_lower_bits_of_bus} = or_7_out ? ram_1_dout : 16'bz;  // Controlled_Buffer controlled_buffer_2
  LedBar #(.matrixcols(16)) ledbar_1 (
    .led0(instruction_register_1_operand_to_upper_bits_of_bus[7]),
    .led1(instruction_register_1_operand_to_upper_bits_of_bus[6]),
    .led2(instruction_register_1_operand_to_upper_bits_of_bus[5]),
    .led3(instruction_register_1_operand_to_upper_bits_of_bus[4]),
    .led4(instruction_register_1_operand_to_upper_bits_of_bus[3]),
    .led5(instruction_register_1_operand_to_upper_bits_of_bus[2]),
    .led6(instruction_register_1_operand_to_upper_bits_of_bus[1]),
    .led7(instruction_register_1_operand_to_upper_bits_of_bus[0]),
    .led8(instruction_register_1_operand_to_lower_bits_of_bus[7]),
    .led9(instruction_register_1_operand_to_lower_bits_of_bus[6]),
    .led10(instruction_register_1_operand_to_lower_bits_of_bus[5]),
    .led11(instruction_register_1_operand_to_lower_bits_of_bus[4]),
    .led12(instruction_register_1_operand_to_lower_bits_of_bus[3]),
    .led13(instruction_register_1_operand_to_lower_bits_of_bus[2]),
    .led14(instruction_register_1_operand_to_lower_bits_of_bus[1]),
    .led15(instruction_register_1_operand_to_lower_bits_of_bus[0]));
  Pull_Resistor pull_resistor_1 (.node(instruction_register_1_operand_to_upper_bits_of_bus[7]));
  Pull_Resistor pull_resistor_2 (.node(instruction_register_1_operand_to_upper_bits_of_bus[6]));
  Pull_Resistor pull_resistor_3 (.node(instruction_register_1_operand_to_upper_bits_of_bus[5]));
  Pull_Resistor pull_resistor_4 (.node(instruction_register_1_operand_to_upper_bits_of_bus[4]));
  Pull_Resistor pull_resistor_5 (.node(instruction_register_1_operand_to_upper_bits_of_bus[3]));
  Pull_Resistor pull_resistor_6 (.node(instruction_register_1_operand_to_upper_bits_of_bus[2]));
  Pull_Resistor pull_resistor_7 (.node(instruction_register_1_operand_to_upper_bits_of_bus[1]));
  Pull_Resistor pull_resistor_8 (.node(instruction_register_1_operand_to_upper_bits_of_bus[0]));
  Pull_Resistor pull_resistor_9 (.node(instruction_register_1_operand_to_lower_bits_of_bus[7]));
  Pull_Resistor pull_resistor_10 (.node(instruction_register_1_operand_to_lower_bits_of_bus[6]));
  Pull_Resistor pull_resistor_11 (.node(instruction_register_1_operand_to_lower_bits_of_bus[5]));
  Pull_Resistor pull_resistor_12 (.node(instruction_register_1_operand_to_lower_bits_of_bus[4]));
  Pull_Resistor pull_resistor_13 (.node(instruction_register_1_operand_to_lower_bits_of_bus[3]));
  Pull_Resistor pull_resistor_14 (.node(instruction_register_1_operand_to_lower_bits_of_bus[2]));
  Pull_Resistor pull_resistor_15 (.node(instruction_register_1_operand_to_lower_bits_of_bus[1]));
  Pull_Resistor pull_resistor_16 (.node(instruction_register_1_operand_to_lower_bits_of_bus[0]));
  TTY #(.cols(64), .rows(24)) tty_1 (
    .data(instruction_register_1_operand_to_lower_bits_of_bus[6:0]), .clk(cpu_clock_1_clock), .we(TTY_WRITE),
    .clr(RESET_BTN));
  Keyboard keyboard_1 (.clk(KB_REG_POP), .clr(RESET_BTN), .data(keyboard_1_data));  // open: re, avail
  PROGRAM_COUNTER program_counter_1 (
    .COUNTER_ENABLE(CNT_ENB), .CLOCK(cpu_clock_1_clock), .RESET(RESET_BTN), .READ(CNT_OUT), .JUMP(JUMP),
    .JUMP_ADDRESS({instruction_register_1_operand_to_upper_bits_of_bus, instruction_register_1_operand_to_lower_bits_of_bus}),
    .DEFAULT_OUTPUT(out_3),
    .BUS_OUTPUT({instruction_register_1_operand_to_upper_bits_of_bus, instruction_register_1_operand_to_lower_bits_of_bus}));
  GENERAL_REGISTER general_register_1 (
    .WRITE(REG_A_WRITE), .CLOCK(cpu_clock_1_clock), .RESET(RESET_BTN), .READ(REG_A_READ),
    .DATA_IN({instruction_register_1_operand_to_upper_bits_of_bus, instruction_register_1_operand_to_lower_bits_of_bus}),
    .DEFAULT_OUTPUT(out_4),
    .BUS_OUTPUT({instruction_register_1_operand_to_upper_bits_of_bus, instruction_register_1_operand_to_lower_bits_of_bus}));
  GENERAL_REGISTER general_register_2 (
    .WRITE(REG_B_WRITE), .CLOCK(cpu_clock_1_clock), .RESET(RESET_BTN), .READ(REG_B_READ),
    .DATA_IN({instruction_register_1_operand_to_upper_bits_of_bus, instruction_register_1_operand_to_lower_bits_of_bus}),
    .DEFAULT_OUTPUT(out_7),
    .BUS_OUTPUT({instruction_register_1_operand_to_upper_bits_of_bus, instruction_register_1_operand_to_lower_bits_of_bus}));
  GENERAL_REGISTER general_register_3 (
    .WRITE(REG_C_WRITE), .CLOCK(cpu_clock_1_clock), .RESET(RESET_BTN), .READ(REG_C_READ),
    .DATA_IN({instruction_register_1_operand_to_upper_bits_of_bus, instruction_register_1_operand_to_lower_bits_of_bus}),
    .DEFAULT_OUTPUT(out_9),
    .BUS_OUTPUT({instruction_register_1_operand_to_upper_bits_of_bus, instruction_register_1_operand_to_lower_bits_of_bus}));
  GENERAL_REGISTER general_register_4 (
    .WRITE(REG_D_WRITE), .CLOCK(cpu_clock_1_clock), .RESET(RESET_BTN), .READ(REG_D_READ),
    .DATA_IN({instruction_register_1_operand_to_upper_bits_of_bus, instruction_register_1_operand_to_lower_bits_of_bus}),
    .DEFAULT_OUTPUT(out_11),
    .BUS_OUTPUT({instruction_register_1_operand_to_upper_bits_of_bus, instruction_register_1_operand_to_lower_bits_of_bus}));
  assign instruction_register_1_operand_to_lower_bits_of_bus[6:0] = KB_REG_READ ? keyboard_1_data : 7'bz;  // Controlled_Buffer controlled_buffer_3
  ALU_OPCODE_ENCODER alu_opcode_encoder_1 (
    .SUM(SUM), .SUB(SUB), .MUL(MUL), .DIV(DIV), .MODULO(MODULO), .A_NOT(A_NOT), .A_AND_B(A_AND_B),
    .A_OR_B(A_OR_B), .A_XOR_B(A_XOR_B), .A_NAND_B(A_NAND_B), .A_NOR_B(A_NOR_B),
    .out_12(alu_opcode_encoder_1_out_12));
  ALU alu_1 (
    .OPCODE(alu_opcode_encoder_1_out_12), .A(out_4), .B(out_7), .ALU_READ(or_8_out), .GREATER(alu_1_greater),
    .EQUAL(alu_1_equal), .LESSER(alu_1_lesser),
    .DATA_OUT({instruction_register_1_operand_to_upper_bits_of_bus, instruction_register_1_operand_to_lower_bits_of_bus}),
    .ZERO(alu_1_zero));
  or or_8 (or_8_out, A_NOR_B, A_NAND_B, A_XOR_B, A_OR_B, A_AND_B, A_NOT, MODULO, DIV, MUL, SUB, SUM);
  FLAGS_REGISTER flags_register_1 (
    .GREATER(alu_1_greater), .SET_CMP_FLAGS(FLAGS_SET), .EQUALS(alu_1_equal), .CLOCK(cpu_clock_1_clock),
    .RESET(or_9_out), .LESSER(alu_1_lesser), .ZERO(alu_1_zero), .SET_ZERO_FLAG(or_8_out),
    .GREATER_FLAG(out_10[12]), .EQUAL_FLAG(out_10[13]), .LESSER_FLAG(out_10[14]), .ZERO_FLAG(out_10[15]));
  or or_9 (or_9_out, RESET_BTN, FLAGS_RESET);

  assign out_10[11:4] = out_8[15:8];

  // Other names for the same wires on the sheet: CUA[15:0] = {out_10[15:12], out_8[15:8], out_10[3:0]};
  //   IR[15:0] = out_8; GREATER_FLAG = out_10[12]; EQUAL_TO_FLAG = out_10[13]; LESSER_FLAG = out_10[14];
  //   ZERO_FLAG = out_10[15]; MAR[15:0] = out_6; PC[15:0] = out_3; REG_A[15:0] = out_4; REG_B[15:0] = out_7;
  //   REG_C[15:0] = out_9; REG_D[15:0] = out_11; RESET = RESET_BTN; STACK_POINTER[15:0] = out_5

  // Notes on the sheet:
  //   contents of rom_1 (hex, n*v repeats v):
  //   1 6 14*0 1 6 1 6 12*0 1 6 1 6 12*0 1 6 1 6 12*0 1 6 1 6 12*0 1 6 1 1006 12*0 1 6 1 6 40 4 10*0 1 6 1
  //   6 80 4 10*0 1 6 1 6 100 4 10*0 1 6 1 6 200 4 10*0 1 6 1 6 200 4 10*0 1 6 2000 13*0 1 6 2000 13*0 1 6
  //   2000 13*0 1 6 2000 13*0 1 6 3000 13*0 1 6 1 6 200 40 10*0 1 6 1 6 200 80 10*0 1 6 1 6 200 100 10*0 1
  //   6 1 6 80 200 10*0 1 6 1 6 200 800 10*0 1 6 0 40 0 800 10*0 1 6 0 80 12*0 1 6 0 100 12*0 1 6 0 200
  //   12*0 1 6 0 800 12*0 1 6 80 13*0 1 6 100 13*0 1 6 200 13*0 1 6 40 13*0 1 6 100 13*0 1 6 200 13*0 1 6
  //   40 13*0 1 6 80 13*0 1 6 200 13*0 1 6 40 13*0 1 6 80 13*0 1 6 100 13*0 1 6 800 13*0 1 6 800 13*0 1 6
  //   800 13*0 1 6 800 13*0 1 6 1040 13*0 1 6 1080 13*0 1 6 1100 13*0 1 6 1200 13*0 1 6 14*0 1 6 14*0 1 6
  //   14*0 1 6 14*0 1 6 14*0 1 6 14*0 1 6 14*0 1 6 14*0 1 6 14*0 1 6 14*0 1 6 14*0 1 6 400 13*0 1 6 0 1
  //   12*0 1 6 6000 13*0 1 6 1 4006 12*0 1 6 4040 13*0 1 6 4080 13*0 1 6 4100 13*0 1 6 4200 13*0 1 6 1
  //   13*0 1 6 80 4 12*0 1 6 100 4 12*0 1 6 200 4 12*0 1 6 14*0 1 6 14*0 1 6 14*0 1 6 80 40 12*0 1 6 100
  //   40 12*0 1 6 200 40 12*0 1 6 14*0 1 6 200 13*0 1 6 200 13*0 1 6 14*0 1 6 14*0 1 6 14*0 1 6 14*0 1 6
  //   14*0 1 6 14*0 1 6 14*0 1 6 14*0 1 6 14*0 1 6 14*0 1 6 14*0 1 6 14*0 1 6 14*0 1 6 14*0 1 6 14*0 1 6
  //   14*0 1 6 14*0 1 6 14*0 1 6 14*0 1 6 14*0 1 6 14*0 1 6 14*0 1 6 14*0 1 6 14*0 1 6 14*0 1 6 14*0 1 6
  //   14*0 1 6 14*0 1 6 14*0 1 6 14*0 1 6 14*0 1 6 14*0 1 6 14*0 1 6 14*0 1 6 14*0 1 6 14*0 1 6 14*0 1 6
  //   14*0 1 6 14*0 1 6 14*0 1 6 14*0 1 6 14*0 1 6 14*0 1 6 14*0 1 6 14*0 1 6 14*0 1 6 14*0 1 6 14*0 1 6
  //   14*0 1 6 14*0 1 6 14*0 1 6 14*0 1 6 14*0 1 6 14*0 1 6 14*0 1 6 14*0 1 6 14*0 1 6 14*0 1 6 14*0 1 6
  //   14*0 1 6 14*0 1 6 14*0 1 6 14*0 1 6 14*0 1 6 14*0 1 6 14*0 1 6 14*0 1 6 14*0 1 6 14*0 1 6 14*0 1 6
  //   14*0 1 6 14*0 1 6 14*0 1 6 14*0 1 6 14*0 1 6 14*0 1 6 14*0 1 6 14*0 1 6 14*0 1 6 14*0 1 6 14*0 1 6
  //   14*0 1 6 14*0 1 6 14*0 1 6 14*0 1 6 14*0 1 6 14*0 1 6 14*0 1 6 14*0 1 6 14*0 1 6 14*0 1 6 14*0 1 6
  //   14*0 1 6 14*0 1 6 14*0 1 6 14*0 1 6 14*0 1 6 14*0 1 6 14*0 1 6 14*0 1 6 14*0 1 6 14*0 1 6 14*0 1 6
  //   14*0 1 6 14*0 1 6 14*0 1 6 14*0 1 6 14*0 1 6 14*0 1 6 14*0 1 6 14*0 1 6 14*0 1 6 14*0 1 6 14*0 1 6
  //   14*0 1 6 14*0 1 6 14*0 1 6 14*0 1 6 14*0 1 6 14*0 1 6 14*0 1 6 14*0 1 6 14*0 1 6 14*0 1 6 14*0 1 6
  //   14*0 1 6 14*0 1 6 14*0 1 6 14*0 1 6 14*0 1 6 14*0 1 6 14*0 1 6 14*0 1 6 14*0 1 6 14*0 1 6 14*0 1 6
  //   14*0 1 6 14*0 1 6 14*0 1 6 14*0 1 6 14*0 1 6 14*0 1 6 14*0 1 6 14*0 1 6 14*0 1 6 14*0 1 6 14*0 1 6
  //   14*0 1 6 14*0 1 6 14*0 1 6 14*0 1 6 14*0 1 6 14*0 1 6 14*0 1 6 14*0 1 6 14*0 1 6 14*0 1 6 14*0 1 6
  //   14*0 1 6 14*0 1 6 14*0 1 6 14*0 1 6 14*0 1 6 14*0 1 6 14*0 1 6 14*0 1 6 14*0 1 6 14*0 1 6 14*0 1 6
  //   14*0 1 6 14*0 1 6 14*0 1 6 14*0 1 6 2 13*0 1 6 2 13*0 1 6 2 13*0 1 6 2 13*0 1 6 8000 13*0 1 6 14*0 1
  //   6 1 6 12*0 1 6 1 6 12*0 1 6 1 6 12*0 1 6 1 6 12*0 1 6 1 1006 12*0 1 6 1 6 40 4 10*0 1 6 1 6 80 4
  //   10*0 1 6 1 6 100 4 10*0 1 6 1 6 200 4 10*0 1 6 1 6 200 4 10*0 1 6 2000 13*0 1 6 2000 13*0 1 6 2000
  //   13*0 1 6 2000 13*0 1 6 3000 13*0 1 6 1 6 200 40 10*0 1 6 1 6 200 80 10*0 1 6 1 6 200 100 10*0 1 6 1
  //   6 80 200 10*0 1 6 1 6 200 800 10*0 1 6 0 40 12*0 1 6 0 80 12*0 1 6 0 100 12*0 1 6 0 200 12*0 1 6 0
  //   800 12*0 1 6 80 13*0 1 6 100 13*0 1 6 200 13*0 1 6 40 13*0 1 6 100 13*0 1 6 200 13*0 1 6 40 13*0 1 6
  //   80 13*0 1 6 200 13*0 1 6 40 13*0 1 6 80 13*0 1 6 100 13*0 1 6 800 13*0 1 6 800 13*0 1 6 800 13*0 1 6
  //   800 13*0 1 6 1040 13*0 1 6 1080 13*0 1 6 1100 13*0 1 6 1200 13*0 1 6 14*0 1 6 14*0 1 6 14*0 1 6 14*0
  //   1 6 14*0 1 6 14*0 1 6 14*0 1 6 14*0 1 6 14*0 1 6 14*0 1 6 14*0 1 6 400 13*0 1 6 0 1 12*0 1 6 6000
  //   13*0 1 6 1 4006 12*0 1 6 4040 13*0 1 6 4080 13*0 1 6 4100 13*0 1 6 4200 13*0 1 6 1 13*0 1 6 80 4
  //   12*0 1 6 100 4 12*0 1 6 200 4 12*0 1 6 14*0 1 6 14*0 1 6 14*0 1 6 80 40 12*0 1 6 100 40 12*0 1 6 200
  //   40 12*0 1 6 14*0 1 6 200 13*0 1 6 200 13*0 1 6 14*0 1 6 14*0 1 6 14*0 1 6 14*0 1 6 14*0 1 6 14*0 1 6
  //   14*0 1 6 14*0 1 6 14*0 1 6 14*0 1 6 14*0 1 6 14*0 1 6 14*0 1 6 14*0 1 6 14*0 1 6 14*0 1 6 14*0 1 6
  //   14*0 1 6 14*0 1 6 14*0 1 6 14*0 1 6 14*0 1 6 14*0 1 6 14*0 1 6 14*0 1 6 14*0 1 6 14*0 1 6 14*0 1 6
  //   14*0 1 6 14*0 1 6 14*0 1 6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
  //   contents of rom_2 (hex, n*v repeats v):
  //   2 4 14*0 2 4 2 8 1000 11*0 2 4 2 10 1000 11*0 2 4 2 20 1000 11*0 2 4 2 40 1000 11*0 2 4 2 0 1000
  //   11*0 2 4 2 8 2 8 10*0 2 4 402 10 2 10 10*0 2 4 402 20 2 20 10*0 2 4 402 40 2 40 10*0 2 4 402 40 2 40
  //   10*0 2 4 8 800 1000 11*0 2 4 10 800 1000 11*0 2 4 20 800 1000 11*0 2 4 40 800 1000 11*0 2 4 0 800
  //   1000 11*0 2 4 2 40 2 1 10*0 2 4 402 40 2 1 10*0 2 4 402 40 2 1 10*0 2 4 402 10 2 1 10*0 2 4 402 40 2
  //   1 10*0 2 4 400 200 1000 801 10*0 2 4 400 200 1000 11*0 2 4 400 200 1000 11*0 2 4 400 200 1000 11*0 2
  //   4 400 200 100 1000 10*0 2 4 8 1000 12*0 2 4 8 1000 12*0 2 4 8 1000 12*0 2 4 10 1000 12*0 2 4 10 1000
  //   12*0 2 4 10 1000 12*0 2 4 20 1000 12*0 2 4 20 1000 12*0 2 4 20 1000 12*0 2 4 40 1000 12*0 2 4 40
  //   1000 12*0 2 4 40 1000 12*0 2 4 8 100 1000 11*0 2 4 10 100 1000 11*0 2 4 20 100 1000 11*0 2 4 40 100
  //   1000 11*0 2 4 0 1000 12*0 2 4 0 1000 12*0 2 4 0 1000 12*0 2 4 0 1000 12*0 2 4 20 1000 12*0 2 4 20
  //   1000 12*0 2 4 20 1000 12*0 2 4 20 1000 12*0 2 4 20 1000 12*0 2 4 20 1000 12*0 2 4 20 1000 12*0 2 4
  //   20 1000 1000 11*0 2 4 20 1000 12*0 2 4 20 1000 1000 11*0 2 4 20 1000 12*0 2 4 0 1000 12*0 2 4 400
  //   200 1000 11*0 2 4 0 800 1000 11*0 2 4 2 0 1000 11*0 2 4 0 1000 12*0 2 4 0 1000 12*0 2 4 0 1000 12*0
  //   2 4 0 1000 12*0 2 4 8 1000 12*0 2 4 2 8 1000 11*0 2 4 2 8 1000 11*0 2 4 2 8 1000 11*0 2 4 0 400 1000
  //   11*0 2 4 800 1000 1000 11*0 2 4 100 1000 12*0 2 4 2 1 1000 11*0 2 4 2 1 1000 11*0 2 4 2 1 1000 11*0
  //   2 4 2008 1000 12*0 2 4 4400 1000 1000 11*0 2 4 8800 1000 1000 11*0 2 4 14*0 2 4 14*0 2 4 14*0 2 4
  //   14*0 2 4 14*0 2 4 14*0 2 4 14*0 2 4 14*0 2 4 14*0 2 4 14*0 2 4 14*0 2 4 14*0 2 4 14*0 2 4 14*0 2 4
  //   14*0 2 4 14*0 2 4 14*0 2 4 14*0 2 4 14*0 2 4 14*0 2 4 14*0 2 4 14*0 2 4 14*0 2 4 14*0 2 4 14*0 2 4
  //   14*0 2 4 14*0 2 4 14*0 2 4 14*0 2 4 14*0 2 4 14*0 2 4 14*0 2 4 14*0 2 4 14*0 2 4 14*0 2 4 14*0 2 4
  //   14*0 2 4 14*0 2 4 14*0 2 4 14*0 2 4 14*0 2 4 14*0 2 4 14*0 2 4 14*0 2 4 14*0 2 4 14*0 2 4 14*0 2 4
  //   14*0 2 4 14*0 2 4 14*0 2 4 14*0 2 4 14*0 2 4 14*0 2 4 14*0 2 4 14*0 2 4 14*0 2 4 14*0 2 4 14*0 2 4
  //   14*0 2 4 14*0 2 4 14*0 2 4 14*0 2 4 14*0 2 4 14*0 2 4 14*0 2 4 14*0 2 4 14*0 2 4 14*0 2 4 14*0 2 4
  //   14*0 2 4 14*0 2 4 14*0 2 4 14*0 2 4 14*0 2 4 14*0 2 4 14*0 2 4 14*0 2 4 14*0 2 4 14*0 2 4 14*0 2 4
  //   14*0 2 4 14*0 2 4 14*0 2 4 14*0 2 4 14*0 2 4 14*0 2 4 14*0 2 4 14*0 2 4 14*0 2 4 14*0 2 4 14*0 2 4
  //   14*0 2 4 14*0 2 4 14*0 2 4 14*0 2 4 14*0 2 4 14*0 2 4 14*0 2 4 14*0 2 4 14*0 2 4 14*0 2 4 14*0 2 4
  //   14*0 2 4 14*0 2 4 14*0 2 4 14*0 2 4 14*0 2 4 14*0 2 4 14*0 2 4 14*0 2 4 14*0 2 4 14*0 2 4 14*0 2 4
  //   14*0 2 4 14*0 2 4 14*0 2 4 14*0 2 4 14*0 2 4 14*0 2 4 14*0 2 4 14*0 2 4 14*0 2 4 14*0 2 4 14*0 2 4
  //   14*0 2 4 14*0 2 4 14*0 2 4 14*0 2 4 14*0 2 4 14*0 2 4 14*0 2 4 14*0 2 4 14*0 2 4 14*0 2 4 14*0 2 4
  //   14*0 2 4 14*0 2 4 14*0 2 4 14*0 2 4 14*0 2 4 14*0 2 4 14*0 2 4 14*0 2 4 14*0 2 4 14*0 2 4 14*0 2 4
  //   14*0 2 4 14*0 2 4 14*0 2 4 14*0 2 4 14*0 2 4 14*0 2 4 14*0 2 4 14*0 2 4 14*0 2 4 14*0 2 4 14*0 2 4
  //   14*0 2 4 14*0 2 4 14*0 2 4 14*0 2 4 14*0 2 4 14*0 2 4 14*0 2 4 14*0 2 4 14*0 2 4 14*0 2 4 14*0 2 4
  //   14*0 2 4 14*0 2 4 14*0 2 4 14*0 2 4 14*0 2 4 0 1000 12*0 2 4 0 1000 12*0 2 4 0 1000 12*0 2 4 0 1000
  //   12*0 2 4 14*0 2 4 14*0 2 4 2 8 1000 11*0 2 4 2 10 1000 11*0 2 4 2 20 1000 11*0 2 4 2 40 1000 11*0 2
  //   4 2 0 1000 11*0 2 4 2 8 2 8 10*0 2 4 402 10 2 10 10*0 2 4 402 20 2 20 10*0 2 4 402 40 2 40 10*0 2 4
  //   402 40 2 40 10*0 2 4 8 800 1000 11*0 2 4 10 800 1000 11*0 2 4 20 800 1000 11*0 2 4 40 800 1000 11*0
  //   2 4 0 800 1000 11*0 2 4 2 40 2 1 10*0 2 4 402 40 2 1 10*0 2 4 402 40 2 1 10*0 2 4 402 10 2 1 10*0 2
  //   4 402 40 2 1 10*0 2 4 400 200 1000 11*0 2 4 400 200 1000 11*0 2 4 400 200 1000 11*0 2 4 400 200 1000
  //   11*0 2 4 400 200 100 1000 10*0 2 4 8 1000 12*0 2 4 8 1000 12*0 2 4 8 1000 12*0 2 4 10 1000 12*0 2 4
  //   10 1000 12*0 2 4 10 1000 12*0 2 4 20 1000 12*0 2 4 20 1000 12*0 2 4 20 1000 12*0 2 4 40 1000 12*0 2
  //   4 40 1000 12*0 2 4 40 1000 12*0 2 4 8 100 1000 11*0 2 4 10 100 1000 11*0 2 4 20 100 1000 11*0 2 4 40
  //   100 1000 11*0 2 4 0 1000 12*0 2 4 0 1000 12*0 2 4 0 1000 12*0 2 4 0 1000 12*0 2 4 20 1000 12*0 2 4
  //   20 1000 12*0 2 4 20 1000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
  //   contents of rom_3 (hex, n*v repeats v):
  //   738*0 1 15*0 2 15*0 4 15*0 8 15*0 10 15*0 20 15*0 40 15*0 80 15*0 180 15*0 240 15*0 480 3935*0 1
  //   15*0 2 15*0 4 15*0 8 15*0 10 15*0 20 15*0 40 15*0 80 15*0 180 15*0 240 15*0 480 3935*0 1 15*0 2 15*0
  //   4 15*0 8 15*0 10 15*0 20 15*0 40 15*0 80 15*0 180 15*0 240 15*0 480 8031*0 1 15*0 2 15*0 4 15*0 8
  //   15*0 10 15*0 20 15*0 40 15*0 80 15*0 180 15*0 240 15*0 480 16223*0 1 15*0 2 15*0 4 15*0 8 15*0 10
  //   15*0 20 15*0 40 15*0 80 15*0 180 15*0 240 15*0 480 3935*0 1 15*0 2 15*0 4 15*0 8 15*0 10 15*0 20
  //   15*0 40 15*0 80 15*0 180 15*0 240 15*0 480 3935*0 1 15*0 2 15*0 4 15*0 8 15*0 10 15*0 20 15*0 40
  //   15*0 80 15*0 180 15*0 240 15*0 480 8031*0 1 15*0 2 15*0 4 15*0 8 15*0 10 15*0 20 15*0 40 15*0 80
  //   15*0 180 15*0 240 15*0 480
  //   ROM 1
  //   ROM 2
  //   ROM 3
  //   STATUS WINDOW
  //   MAKE SURE TO RESET BEFORE STARTING THE SIMULATION
  //   REG A
  //   REG B
  //   REG C
  //   REG D
  //   TTY
  //   KEYBOARD
endmodule

module Adder (
  input  A,
  input  B,
  input  Cin,
  output Out,
  output Cout
);

  wire and_1_out, and_2_out, xor_1_out;

  xor xor_1 (xor_1_out, A, B);
  and and_1 (and_1_out, A, B);
  and and_2 (and_2_out, xor_1_out, Cin);
  xor xor_2 (Out, xor_1_out, Cin);
  or or_1 (Cout, and_1_out, and_2_out);
endmodule

module REGISTER_1_BIT (
  input  STORE,
  input  DATA_IN,
  input  CLOCK,
  input  RESET,
  output DATA_OUT
);

  wire and_1_out, and_2_out, and_3_out, nand_1_out, nand_2_out, nand_4_out, not_1_out, not_2_out, not_3_out,
       or_1_out, or_2_out, or_3_out;

  and and_1 (and_1_out, DATA_OUT, not_1_out);
  not not_1 (not_1_out, STORE);
  and and_2 (and_2_out, STORE, DATA_IN);
  or or_1 (or_1_out, and_1_out, and_2_out);
  not not_2 (not_2_out, RESET);
  or or_2 (or_2_out, CLOCK, RESET);
  and and_3 (and_3_out, or_1_out, not_2_out);
  not not_3 (not_3_out, or_1_out);
  or or_3 (or_3_out, not_3_out, RESET);
  nand nand_1 (nand_1_out, and_3_out, or_2_out);
  nand nand_2 (nand_2_out, or_2_out, or_3_out);
  nand nand_3 (DATA_OUT, nand_1_out, nand_4_out);
  nand nand_4 (nand_4_out, DATA_OUT, nand_2_out);
endmodule

module REGISTER_8_BIT (
  input  [7:0] DATA_IN,
  input  STORE,
  input  CLOCK,
  input  RESET,
  output [7:0] DATA_OUT
);

  REGISTER_1_BIT register_1_bit_1 (
    .STORE(STORE), .DATA_IN(DATA_IN[0]), .CLOCK(CLOCK), .RESET(RESET), .DATA_OUT(DATA_OUT[0]));
  REGISTER_1_BIT register_1_bit_2 (
    .STORE(STORE), .DATA_IN(DATA_IN[1]), .CLOCK(CLOCK), .RESET(RESET), .DATA_OUT(DATA_OUT[1]));
  REGISTER_1_BIT register_1_bit_3 (
    .STORE(STORE), .DATA_IN(DATA_IN[2]), .CLOCK(CLOCK), .RESET(RESET), .DATA_OUT(DATA_OUT[2]));
  REGISTER_1_BIT register_1_bit_4 (
    .STORE(STORE), .DATA_IN(DATA_IN[3]), .CLOCK(CLOCK), .RESET(RESET), .DATA_OUT(DATA_OUT[3]));
  REGISTER_1_BIT register_1_bit_5 (
    .STORE(STORE), .DATA_IN(DATA_IN[4]), .CLOCK(CLOCK), .RESET(RESET), .DATA_OUT(DATA_OUT[4]));
  REGISTER_1_BIT register_1_bit_6 (
    .STORE(STORE), .DATA_IN(DATA_IN[5]), .CLOCK(CLOCK), .RESET(RESET), .DATA_OUT(DATA_OUT[5]));
  REGISTER_1_BIT register_1_bit_7 (
    .STORE(STORE), .DATA_IN(DATA_IN[6]), .CLOCK(CLOCK), .RESET(RESET), .DATA_OUT(DATA_OUT[6]));
  REGISTER_1_BIT register_1_bit_8 (
    .STORE(STORE), .DATA_IN(DATA_IN[7]), .CLOCK(CLOCK), .RESET(RESET), .DATA_OUT(DATA_OUT[7]));
endmodule

module MULTIPLIER_16_BIT (
  input  [15:0] A,
  input  [15:0] B,
  output [15:0] MUL
);

  wire adder_1_out, adder_2_out, adder_3_out, adder_4_out, adder_5_out, adder_6_out, adder_7_out,
       adder_8_out, adder_9_out, adder_10_out, adder_11_out, adder_12_out, adder_13_out, adder_14_out,
       adder_16_cout, adder_16_out, adder_17_cout, adder_17_out, adder_18_cout, adder_18_out, adder_19_cout,
       adder_19_out, adder_20_cout, adder_20_out, adder_21_cout, adder_21_out, adder_22_cout, adder_22_out,
       adder_23_cout, adder_23_out, adder_24_cout, adder_24_out, adder_25_cout, adder_25_out, adder_26_cout,
       adder_26_out, adder_27_cout, adder_27_out, adder_28_cout, adder_28_out, adder_29_cout, adder_30_cout,
       adder_30_out, adder_31_cout, adder_31_out, adder_32_cout, adder_32_out, adder_33_cout, adder_33_out,
       adder_34_cout, adder_34_out, adder_35_cout, adder_35_out, adder_36_cout, adder_36_out, adder_37_cout,
       adder_37_out, adder_38_cout, adder_38_out, adder_39_cout, adder_39_out, adder_40_cout, adder_40_out,
       adder_41_cout, adder_41_out, adder_42_cout, adder_43_cout, adder_43_out, adder_44_cout, adder_44_out,
       adder_45_cout, adder_45_out, adder_46_cout, adder_46_out, adder_47_cout, adder_47_out, adder_48_cout,
       adder_48_out, adder_49_cout, adder_49_out, adder_50_cout, adder_50_out, adder_51_cout, adder_51_out,
       adder_52_cout, adder_52_out, adder_53_cout, adder_53_out, adder_54_cout, adder_55_cout, adder_55_out,
       adder_56_cout, adder_56_out, adder_57_cout, adder_57_out, adder_58_cout, adder_58_out, adder_59_cout,
       adder_59_out, adder_60_cout, adder_60_out, adder_61_cout, adder_61_out, adder_62_cout, adder_62_out,
       adder_63_cout, adder_63_out, adder_64_cout, adder_64_out, adder_65_cout, adder_66_cout, adder_66_out,
       adder_67_cout, adder_67_out, adder_68_cout, adder_68_out, adder_69_cout, adder_69_out, adder_70_cout,
       adder_70_out, adder_71_cout, adder_71_out, adder_72_cout, adder_72_out, adder_73_cout, adder_73_out,
       adder_74_cout, adder_74_out, adder_75_cout, adder_76_cout, adder_76_out, adder_77_cout, adder_77_out,
       adder_78_cout, adder_78_out, adder_79_cout, adder_79_out, adder_80_cout, adder_80_out, adder_81_cout,
       adder_81_out, adder_82_cout, adder_82_out, adder_83_cout, adder_83_out, adder_84_cout, adder_85_cout,
       adder_85_out, adder_86_cout, adder_86_out, adder_87_cout, adder_87_out, adder_88_cout, adder_88_out,
       adder_89_cout, adder_89_out, adder_90_cout, adder_90_out, adder_91_cout, adder_91_out, adder_92_cout,
       adder_93_cout, adder_93_out, adder_94_cout, adder_94_out, adder_95_cout, adder_95_out, adder_96_cout,
       adder_96_out, adder_97_cout, adder_97_out, adder_98_cout, adder_98_out, adder_99_cout, adder_100_cout,
       adder_100_out, adder_101_cout, adder_101_out, adder_102_cout, adder_102_out, adder_103_cout,
       adder_103_out, adder_104_cout, adder_104_out, adder_105_cout, adder_106_cout, adder_106_out,
       adder_107_cout, adder_107_out, adder_108_cout, adder_108_out, adder_109_cout, adder_109_out,
       adder_110_cout, adder_111_cout, adder_111_out, adder_112_cout, adder_112_out, adder_113_cout,
       adder_113_out, adder_114_cout, adder_115_cout, adder_115_out, adder_116_cout, adder_116_out,
       adder_117_cout, adder_118_cout, adder_118_out, adder_119_cout, adder_120_cout, and_1_out, and_2_out,
       and_3_out, and_4_out, and_5_out, and_6_out, and_7_out, and_8_out, and_9_out, and_10_out, and_11_out,
       and_12_out, and_13_out, and_14_out, and_15_out, and_16_out, and_17_out, and_18_out, and_19_out,
       and_20_out, and_21_out, and_22_out, and_23_out, and_24_out, and_25_out, and_26_out, and_27_out,
       and_28_out, and_29_out, and_30_out, and_31_out, and_32_out, and_33_out, and_34_out, and_35_out,
       and_36_out, and_37_out, and_38_out, and_39_out, and_40_out, and_41_out, and_42_out, and_43_out,
       and_44_out, and_45_out, and_46_out, and_47_out, and_48_out, and_49_out, and_50_out, and_51_out,
       and_52_out, and_53_out, and_54_out, and_55_out, and_56_out, and_57_out, and_58_out, and_59_out,
       and_60_out, and_61_out, and_62_out, and_63_out, and_64_out, and_65_out, and_66_out, and_67_out,
       and_68_out, and_69_out, and_70_out, and_71_out, and_72_out, and_73_out, and_74_out, and_75_out,
       and_76_out, and_77_out, and_78_out, and_79_out, and_80_out, and_81_out, and_82_out, and_83_out,
       and_84_out, and_85_out, and_86_out, and_87_out, and_88_out, and_89_out, and_90_out, and_91_out,
       and_92_out, and_93_out, and_94_out, and_95_out, and_96_out, and_97_out, and_98_out, and_99_out,
       and_100_out, and_101_out, and_102_out, and_103_out, and_104_out, and_105_out, and_106_out,
       and_107_out, and_108_out, and_109_out, and_110_out, and_111_out, and_112_out, and_113_out,
       and_114_out, and_115_out, and_116_out, and_117_out, and_118_out, and_119_out, and_120_out,
       and_121_out, and_122_out, and_123_out, and_124_out, and_125_out, and_126_out, and_127_out,
       and_128_out, and_129_out, and_130_out, and_131_out, and_132_out, and_133_out, and_134_out,
       and_135_out, xor_1_out;
  wire [15:0] and_136_out, multiplexer_1_out, multiplexer_3_out, twos_comp_16_bit_1_data_out,
       twos_comp_16_bit_2_data_out, twos_comp_16_bit_3_data_out;

  and and_1 (and_1_out, multiplexer_3_out[0], multiplexer_1_out[15]);
  and and_2 (and_2_out, multiplexer_3_out[1], multiplexer_1_out[14]);
  Adder adder_1 (.B(and_2_out), .Cin(adder_16_cout), .A(and_1_out), .Out(adder_1_out));  // open: Cout
  and and_3 (and_3_out, multiplexer_3_out[2], multiplexer_1_out[13]);
  Adder adder_2 (.B(and_3_out), .Cin(adder_17_cout), .A(adder_1_out), .Out(adder_2_out));  // open: Cout
  and and_4 (and_4_out, multiplexer_3_out[3], multiplexer_1_out[12]);
  Adder adder_3 (.B(and_4_out), .Cin(adder_18_cout), .A(adder_2_out), .Out(adder_3_out));  // open: Cout
  and and_5 (and_5_out, multiplexer_3_out[4], multiplexer_1_out[11]);
  Adder adder_4 (.B(and_5_out), .Cin(adder_19_cout), .A(adder_3_out), .Out(adder_4_out));  // open: Cout
  and and_6 (and_6_out, multiplexer_3_out[5], multiplexer_1_out[10]);
  Adder adder_5 (.B(and_6_out), .Cin(adder_20_cout), .A(adder_4_out), .Out(adder_5_out));  // open: Cout
  and and_7 (and_7_out, multiplexer_3_out[6], multiplexer_1_out[9]);
  Adder adder_6 (.B(and_7_out), .Cin(adder_21_cout), .A(adder_5_out), .Out(adder_6_out));  // open: Cout
  and and_8 (and_8_out, multiplexer_3_out[7], multiplexer_1_out[8]);
  Adder adder_7 (.B(and_8_out), .Cin(adder_22_cout), .A(adder_6_out), .Out(adder_7_out));  // open: Cout
  and and_9 (and_9_out, multiplexer_3_out[8], multiplexer_1_out[7]);
  Adder adder_8 (.B(and_9_out), .Cin(adder_23_cout), .A(adder_7_out), .Out(adder_8_out));  // open: Cout
  and and_10 (and_10_out, multiplexer_3_out[9], multiplexer_1_out[6]);
  Adder adder_9 (.B(and_10_out), .Cin(adder_24_cout), .A(adder_8_out), .Out(adder_9_out));  // open: Cout
  and and_11 (and_11_out, multiplexer_3_out[10], multiplexer_1_out[5]);
  Adder adder_10 (.B(and_11_out), .Cin(adder_25_cout), .A(adder_9_out), .Out(adder_10_out));  // open: Cout
  and and_12 (and_12_out, multiplexer_3_out[11], multiplexer_1_out[4]);
  Adder adder_11 (.B(and_12_out), .Cin(adder_26_cout), .A(adder_10_out), .Out(adder_11_out));  // open: Cout
  and and_13 (and_13_out, multiplexer_3_out[12], multiplexer_1_out[3]);
  Adder adder_12 (.B(and_13_out), .Cin(adder_27_cout), .A(adder_11_out), .Out(adder_12_out));  // open: Cout
  and and_14 (and_14_out, multiplexer_3_out[13], multiplexer_1_out[2]);
  Adder adder_13 (.B(and_14_out), .Cin(adder_28_cout), .A(adder_12_out), .Out(adder_13_out));  // open: Cout
  and and_15 (and_15_out, multiplexer_3_out[14], multiplexer_1_out[1]);
  Adder adder_14 (.B(and_15_out), .Cin(adder_29_cout), .A(adder_13_out), .Out(adder_14_out));  // open: Cout
  and and_16 (and_16_out, multiplexer_3_out[15], multiplexer_1_out[0]);
  Adder adder_15 (.B(and_16_out), .A(adder_14_out), .Out(and_136_out[15]));  // open: Cin, Cout
  buf and_17 (and_17_out, multiplexer_1_out[14]);  // AND_Gate
  and and_18 (and_18_out, multiplexer_3_out[1], multiplexer_1_out[13]);
  Adder adder_16 (.B(and_18_out), .Cin(adder_30_cout), .A(and_17_out), .Out(adder_16_out), .Cout(adder_16_cout));
  and and_19 (and_19_out, multiplexer_3_out[2], multiplexer_1_out[12]);
  Adder adder_17 (.B(and_19_out), .Cin(adder_31_cout), .A(adder_16_out), .Out(adder_17_out), .Cout(adder_17_cout));
  and and_20 (and_20_out, multiplexer_3_out[3], multiplexer_1_out[11]);
  Adder adder_18 (.B(and_20_out), .Cin(adder_32_cout), .A(adder_17_out), .Out(adder_18_out), .Cout(adder_18_cout));
  and and_21 (and_21_out, multiplexer_3_out[4], multiplexer_1_out[10]);
  Adder adder_19 (.B(and_21_out), .Cin(adder_33_cout), .A(adder_18_out), .Out(adder_19_out), .Cout(adder_19_cout));
  and and_22 (and_22_out, multiplexer_3_out[5], multiplexer_1_out[9]);
  Adder adder_20 (.B(and_22_out), .Cin(adder_34_cout), .A(adder_19_out), .Out(adder_20_out), .Cout(adder_20_cout));
  and and_23 (and_23_out, multiplexer_3_out[6], multiplexer_1_out[8]);
  Adder adder_21 (.B(and_23_out), .Cin(adder_35_cout), .A(adder_20_out), .Out(adder_21_out), .Cout(adder_21_cout));
  and and_24 (and_24_out, multiplexer_3_out[7], multiplexer_1_out[7]);
  Adder adder_22 (.B(and_24_out), .Cin(adder_36_cout), .A(adder_21_out), .Out(adder_22_out), .Cout(adder_22_cout));
  and and_25 (and_25_out, multiplexer_3_out[8], multiplexer_1_out[6]);
  Adder adder_23 (.B(and_25_out), .Cin(adder_37_cout), .A(adder_22_out), .Out(adder_23_out), .Cout(adder_23_cout));
  and and_26 (and_26_out, multiplexer_3_out[9], multiplexer_1_out[5]);
  Adder adder_24 (.B(and_26_out), .Cin(adder_38_cout), .A(adder_23_out), .Out(adder_24_out), .Cout(adder_24_cout));
  and and_27 (and_27_out, multiplexer_3_out[10], multiplexer_1_out[4]);
  Adder adder_25 (.B(and_27_out), .Cin(adder_39_cout), .A(adder_24_out), .Out(adder_25_out), .Cout(adder_25_cout));
  and and_28 (and_28_out, multiplexer_3_out[11], multiplexer_1_out[3]);
  Adder adder_26 (.B(and_28_out), .Cin(adder_40_cout), .A(adder_25_out), .Out(adder_26_out), .Cout(adder_26_cout));
  and and_29 (and_29_out, multiplexer_3_out[12], multiplexer_1_out[2]);
  Adder adder_27 (.B(and_29_out), .Cin(adder_41_cout), .A(adder_26_out), .Out(adder_27_out), .Cout(adder_27_cout));
  and and_30 (and_30_out, multiplexer_3_out[13], multiplexer_1_out[1]);
  Adder adder_28 (.B(and_30_out), .Cin(adder_42_cout), .A(adder_27_out), .Out(adder_28_out), .Cout(adder_28_cout));
  and and_31 (and_31_out, multiplexer_3_out[14], multiplexer_1_out[0]);
  Adder adder_29 (.B(and_31_out), .A(adder_28_out), .Out(and_136_out[14]), .Cout(adder_29_cout));  // open: Cin
  buf and_32 (and_32_out, multiplexer_1_out[13]);  // AND_Gate
  and and_33 (and_33_out, multiplexer_3_out[1], multiplexer_1_out[12]);
  Adder adder_30 (.B(and_33_out), .Cin(adder_43_cout), .A(and_32_out), .Out(adder_30_out), .Cout(adder_30_cout));
  and and_34 (and_34_out, multiplexer_3_out[2], multiplexer_1_out[11]);
  Adder adder_31 (.B(and_34_out), .Cin(adder_44_cout), .A(adder_30_out), .Out(adder_31_out), .Cout(adder_31_cout));
  and and_35 (and_35_out, multiplexer_3_out[3], multiplexer_1_out[10]);
  Adder adder_32 (.B(and_35_out), .Cin(adder_45_cout), .A(adder_31_out), .Out(adder_32_out), .Cout(adder_32_cout));
  and and_36 (and_36_out, multiplexer_3_out[4], multiplexer_1_out[9]);
  Adder adder_33 (.B(and_36_out), .Cin(adder_46_cout), .A(adder_32_out), .Out(adder_33_out), .Cout(adder_33_cout));
  and and_37 (and_37_out, multiplexer_3_out[5], multiplexer_1_out[8]);
  Adder adder_34 (.B(and_37_out), .Cin(adder_47_cout), .A(adder_33_out), .Out(adder_34_out), .Cout(adder_34_cout));
  and and_38 (and_38_out, multiplexer_3_out[6], multiplexer_1_out[7]);
  Adder adder_35 (.B(and_38_out), .Cin(adder_48_cout), .A(adder_34_out), .Out(adder_35_out), .Cout(adder_35_cout));
  and and_39 (and_39_out, multiplexer_3_out[7], multiplexer_1_out[6]);
  Adder adder_36 (.B(and_39_out), .Cin(adder_49_cout), .A(adder_35_out), .Out(adder_36_out), .Cout(adder_36_cout));
  and and_40 (and_40_out, multiplexer_3_out[8], multiplexer_1_out[5]);
  Adder adder_37 (.B(and_40_out), .Cin(adder_50_cout), .A(adder_36_out), .Out(adder_37_out), .Cout(adder_37_cout));
  and and_41 (and_41_out, multiplexer_3_out[9], multiplexer_1_out[4]);
  Adder adder_38 (.B(and_41_out), .Cin(adder_51_cout), .A(adder_37_out), .Out(adder_38_out), .Cout(adder_38_cout));
  and and_42 (and_42_out, multiplexer_3_out[10], multiplexer_1_out[3]);
  Adder adder_39 (.B(and_42_out), .Cin(adder_52_cout), .A(adder_38_out), .Out(adder_39_out), .Cout(adder_39_cout));
  and and_43 (and_43_out, multiplexer_3_out[11], multiplexer_1_out[2]);
  Adder adder_40 (.B(and_43_out), .Cin(adder_53_cout), .A(adder_39_out), .Out(adder_40_out), .Cout(adder_40_cout));
  and and_44 (and_44_out, multiplexer_3_out[12], multiplexer_1_out[1]);
  Adder adder_41 (.B(and_44_out), .Cin(adder_54_cout), .A(adder_40_out), .Out(adder_41_out), .Cout(adder_41_cout));
  and and_45 (and_45_out, multiplexer_3_out[13], multiplexer_1_out[0]);
  Adder adder_42 (.B(and_45_out), .A(adder_41_out), .Out(and_136_out[13]), .Cout(adder_42_cout));  // open: Cin
  buf and_46 (and_46_out, multiplexer_1_out[12]);  // AND_Gate
  and and_47 (and_47_out, multiplexer_3_out[1], multiplexer_1_out[11]);
  Adder adder_43 (.B(and_47_out), .Cin(adder_55_cout), .A(and_46_out), .Out(adder_43_out), .Cout(adder_43_cout));
  and and_48 (and_48_out, multiplexer_3_out[2], multiplexer_1_out[10]);
  Adder adder_44 (.B(and_48_out), .Cin(adder_56_cout), .A(adder_43_out), .Out(adder_44_out), .Cout(adder_44_cout));
  and and_49 (and_49_out, multiplexer_3_out[3], multiplexer_1_out[9]);
  Adder adder_45 (.B(and_49_out), .Cin(adder_57_cout), .A(adder_44_out), .Out(adder_45_out), .Cout(adder_45_cout));
  and and_50 (and_50_out, multiplexer_3_out[4], multiplexer_1_out[8]);
  Adder adder_46 (.B(and_50_out), .Cin(adder_58_cout), .A(adder_45_out), .Out(adder_46_out), .Cout(adder_46_cout));
  and and_51 (and_51_out, multiplexer_3_out[5], multiplexer_1_out[7]);
  Adder adder_47 (.B(and_51_out), .Cin(adder_59_cout), .A(adder_46_out), .Out(adder_47_out), .Cout(adder_47_cout));
  and and_52 (and_52_out, multiplexer_3_out[6], multiplexer_1_out[6]);
  Adder adder_48 (.B(and_52_out), .Cin(adder_60_cout), .A(adder_47_out), .Out(adder_48_out), .Cout(adder_48_cout));
  and and_53 (and_53_out, multiplexer_3_out[7], multiplexer_1_out[5]);
  Adder adder_49 (.B(and_53_out), .Cin(adder_61_cout), .A(adder_48_out), .Out(adder_49_out), .Cout(adder_49_cout));
  and and_54 (and_54_out, multiplexer_3_out[8], multiplexer_1_out[4]);
  Adder adder_50 (.B(and_54_out), .Cin(adder_62_cout), .A(adder_49_out), .Out(adder_50_out), .Cout(adder_50_cout));
  and and_55 (and_55_out, multiplexer_3_out[9], multiplexer_1_out[3]);
  Adder adder_51 (.B(and_55_out), .Cin(adder_63_cout), .A(adder_50_out), .Out(adder_51_out), .Cout(adder_51_cout));
  and and_56 (and_56_out, multiplexer_3_out[10], multiplexer_1_out[2]);
  Adder adder_52 (.B(and_56_out), .Cin(adder_64_cout), .A(adder_51_out), .Out(adder_52_out), .Cout(adder_52_cout));
  and and_57 (and_57_out, multiplexer_3_out[11], multiplexer_1_out[1]);
  Adder adder_53 (.B(and_57_out), .Cin(adder_65_cout), .A(adder_52_out), .Out(adder_53_out), .Cout(adder_53_cout));
  and and_58 (and_58_out, multiplexer_3_out[12], multiplexer_1_out[0]);
  Adder adder_54 (.B(and_58_out), .A(adder_53_out), .Out(and_136_out[12]), .Cout(adder_54_cout));  // open: Cin
  buf and_59 (and_59_out, multiplexer_1_out[11]);  // AND_Gate
  and and_60 (and_60_out, multiplexer_3_out[1], multiplexer_1_out[10]);
  Adder adder_55 (.B(and_60_out), .Cin(adder_66_cout), .A(and_59_out), .Out(adder_55_out), .Cout(adder_55_cout));
  and and_61 (and_61_out, multiplexer_3_out[2], multiplexer_1_out[9]);
  Adder adder_56 (.B(and_61_out), .Cin(adder_67_cout), .A(adder_55_out), .Out(adder_56_out), .Cout(adder_56_cout));
  and and_62 (and_62_out, multiplexer_3_out[3], multiplexer_1_out[8]);
  Adder adder_57 (.B(and_62_out), .Cin(adder_68_cout), .A(adder_56_out), .Out(adder_57_out), .Cout(adder_57_cout));
  and and_63 (and_63_out, multiplexer_3_out[4], multiplexer_1_out[7]);
  Adder adder_58 (.B(and_63_out), .Cin(adder_69_cout), .A(adder_57_out), .Out(adder_58_out), .Cout(adder_58_cout));
  and and_64 (and_64_out, multiplexer_3_out[5], multiplexer_1_out[6]);
  Adder adder_59 (.B(and_64_out), .Cin(adder_70_cout), .A(adder_58_out), .Out(adder_59_out), .Cout(adder_59_cout));
  and and_65 (and_65_out, multiplexer_3_out[6], multiplexer_1_out[5]);
  Adder adder_60 (.B(and_65_out), .Cin(adder_71_cout), .A(adder_59_out), .Out(adder_60_out), .Cout(adder_60_cout));
  and and_66 (and_66_out, multiplexer_3_out[7], multiplexer_1_out[4]);
  Adder adder_61 (.B(and_66_out), .Cin(adder_72_cout), .A(adder_60_out), .Out(adder_61_out), .Cout(adder_61_cout));
  and and_67 (and_67_out, multiplexer_3_out[8], multiplexer_1_out[3]);
  Adder adder_62 (.B(and_67_out), .Cin(adder_73_cout), .A(adder_61_out), .Out(adder_62_out), .Cout(adder_62_cout));
  and and_68 (and_68_out, multiplexer_3_out[9], multiplexer_1_out[2]);
  Adder adder_63 (.B(and_68_out), .Cin(adder_74_cout), .A(adder_62_out), .Out(adder_63_out), .Cout(adder_63_cout));
  and and_69 (and_69_out, multiplexer_3_out[10], multiplexer_1_out[1]);
  Adder adder_64 (.B(and_69_out), .Cin(adder_75_cout), .A(adder_63_out), .Out(adder_64_out), .Cout(adder_64_cout));
  and and_70 (and_70_out, multiplexer_3_out[11], multiplexer_1_out[0]);
  Adder adder_65 (.B(and_70_out), .A(adder_64_out), .Out(and_136_out[11]), .Cout(adder_65_cout));  // open: Cin
  buf and_71 (and_71_out, multiplexer_1_out[10]);  // AND_Gate
  and and_72 (and_72_out, multiplexer_3_out[1], multiplexer_1_out[9]);
  Adder adder_66 (.B(and_72_out), .Cin(adder_76_cout), .A(and_71_out), .Out(adder_66_out), .Cout(adder_66_cout));
  and and_73 (and_73_out, multiplexer_3_out[2], multiplexer_1_out[8]);
  Adder adder_67 (.B(and_73_out), .Cin(adder_77_cout), .A(adder_66_out), .Out(adder_67_out), .Cout(adder_67_cout));
  and and_74 (and_74_out, multiplexer_3_out[3], multiplexer_1_out[7]);
  Adder adder_68 (.B(and_74_out), .Cin(adder_78_cout), .A(adder_67_out), .Out(adder_68_out), .Cout(adder_68_cout));
  and and_75 (and_75_out, multiplexer_3_out[4], multiplexer_1_out[6]);
  Adder adder_69 (.B(and_75_out), .Cin(adder_79_cout), .A(adder_68_out), .Out(adder_69_out), .Cout(adder_69_cout));
  and and_76 (and_76_out, multiplexer_3_out[5], multiplexer_1_out[5]);
  Adder adder_70 (.B(and_76_out), .Cin(adder_80_cout), .A(adder_69_out), .Out(adder_70_out), .Cout(adder_70_cout));
  and and_77 (and_77_out, multiplexer_3_out[6], multiplexer_1_out[4]);
  Adder adder_71 (.B(and_77_out), .Cin(adder_81_cout), .A(adder_70_out), .Out(adder_71_out), .Cout(adder_71_cout));
  and and_78 (and_78_out, multiplexer_3_out[7], multiplexer_1_out[3]);
  Adder adder_72 (.B(and_78_out), .Cin(adder_82_cout), .A(adder_71_out), .Out(adder_72_out), .Cout(adder_72_cout));
  and and_79 (and_79_out, multiplexer_3_out[8], multiplexer_1_out[2]);
  Adder adder_73 (.B(and_79_out), .Cin(adder_83_cout), .A(adder_72_out), .Out(adder_73_out), .Cout(adder_73_cout));
  and and_80 (and_80_out, multiplexer_3_out[9], multiplexer_1_out[1]);
  Adder adder_74 (.B(and_80_out), .Cin(adder_84_cout), .A(adder_73_out), .Out(adder_74_out), .Cout(adder_74_cout));
  and and_81 (and_81_out, multiplexer_3_out[10], multiplexer_1_out[0]);
  Adder adder_75 (.B(and_81_out), .A(adder_74_out), .Out(and_136_out[10]), .Cout(adder_75_cout));  // open: Cin
  buf and_82 (and_82_out, multiplexer_1_out[9]);  // AND_Gate
  and and_83 (and_83_out, multiplexer_3_out[1], multiplexer_1_out[8]);
  Adder adder_76 (.B(and_83_out), .Cin(adder_85_cout), .A(and_82_out), .Out(adder_76_out), .Cout(adder_76_cout));
  and and_84 (and_84_out, multiplexer_3_out[2], multiplexer_1_out[7]);
  Adder adder_77 (.B(and_84_out), .Cin(adder_86_cout), .A(adder_76_out), .Out(adder_77_out), .Cout(adder_77_cout));
  and and_85 (and_85_out, multiplexer_3_out[3], multiplexer_1_out[6]);
  Adder adder_78 (.B(and_85_out), .Cin(adder_87_cout), .A(adder_77_out), .Out(adder_78_out), .Cout(adder_78_cout));
  and and_86 (and_86_out, multiplexer_3_out[4], multiplexer_1_out[5]);
  Adder adder_79 (.B(and_86_out), .Cin(adder_88_cout), .A(adder_78_out), .Out(adder_79_out), .Cout(adder_79_cout));
  and and_87 (and_87_out, multiplexer_3_out[5], multiplexer_1_out[4]);
  Adder adder_80 (.B(and_87_out), .Cin(adder_89_cout), .A(adder_79_out), .Out(adder_80_out), .Cout(adder_80_cout));
  and and_88 (and_88_out, multiplexer_3_out[6], multiplexer_1_out[3]);
  Adder adder_81 (.B(and_88_out), .Cin(adder_90_cout), .A(adder_80_out), .Out(adder_81_out), .Cout(adder_81_cout));
  and and_89 (and_89_out, multiplexer_3_out[7], multiplexer_1_out[2]);
  Adder adder_82 (.B(and_89_out), .Cin(adder_91_cout), .A(adder_81_out), .Out(adder_82_out), .Cout(adder_82_cout));
  and and_90 (and_90_out, multiplexer_3_out[8], multiplexer_1_out[1]);
  Adder adder_83 (.B(and_90_out), .Cin(adder_92_cout), .A(adder_82_out), .Out(adder_83_out), .Cout(adder_83_cout));
  and and_91 (and_91_out, multiplexer_3_out[9], multiplexer_1_out[0]);
  Adder adder_84 (.B(and_91_out), .A(adder_83_out), .Out(and_136_out[9]), .Cout(adder_84_cout));  // open: Cin
  and and_92 (and_92_out, multiplexer_3_out[1], multiplexer_1_out[7]);
  and and_93 (and_93_out, multiplexer_3_out[2], multiplexer_1_out[6]);
  and and_94 (and_94_out, multiplexer_3_out[3], multiplexer_1_out[5]);
  and and_95 (and_95_out, multiplexer_3_out[4], multiplexer_1_out[4]);
  and and_96 (and_96_out, multiplexer_3_out[5], multiplexer_1_out[3]);
  and and_97 (and_97_out, multiplexer_3_out[6], multiplexer_1_out[2]);
  and and_98 (and_98_out, multiplexer_3_out[7], multiplexer_1_out[1]);
  and and_99 (and_99_out, multiplexer_3_out[8], multiplexer_1_out[0]);
  and and_100 (and_100_out, multiplexer_3_out[0], multiplexer_1_out[8]);
  Adder adder_85 (.B(and_92_out), .Cin(adder_93_cout), .A(and_100_out), .Out(adder_85_out), .Cout(adder_85_cout));
  Adder adder_86 (.B(and_93_out), .Cin(adder_94_cout), .A(adder_85_out), .Out(adder_86_out), .Cout(adder_86_cout));
  Adder adder_87 (.B(and_94_out), .Cin(adder_95_cout), .A(adder_86_out), .Out(adder_87_out), .Cout(adder_87_cout));
  Adder adder_88 (.B(and_95_out), .Cin(adder_96_cout), .A(adder_87_out), .Out(adder_88_out), .Cout(adder_88_cout));
  Adder adder_89 (.B(and_96_out), .Cin(adder_97_cout), .A(adder_88_out), .Out(adder_89_out), .Cout(adder_89_cout));
  Adder adder_90 (.B(and_97_out), .Cin(adder_98_cout), .A(adder_89_out), .Out(adder_90_out), .Cout(adder_90_cout));
  Adder adder_91 (.B(and_98_out), .Cin(adder_99_cout), .A(adder_90_out), .Out(adder_91_out), .Cout(adder_91_cout));
  Adder adder_92 (.B(and_99_out), .A(adder_91_out), .Out(and_136_out[8]), .Cout(adder_92_cout));  // open: Cin
  and and_101 (and_101_out, multiplexer_3_out[0], multiplexer_1_out[7]);
  and and_102 (and_102_out, multiplexer_3_out[1], multiplexer_1_out[6]);
  Adder adder_93 (.B(and_102_out), .Cin(adder_100_cout), .A(and_101_out), .Out(adder_93_out), .Cout(adder_93_cout));
  and and_103 (and_103_out, multiplexer_3_out[2], multiplexer_1_out[5]);
  Adder adder_94 (.B(and_103_out), .Cin(adder_101_cout), .A(adder_93_out), .Out(adder_94_out), .Cout(adder_94_cout));
  and and_104 (and_104_out, multiplexer_3_out[3], multiplexer_1_out[4]);
  Adder adder_95 (.B(and_104_out), .Cin(adder_102_cout), .A(adder_94_out), .Out(adder_95_out), .Cout(adder_95_cout));
  and and_105 (and_105_out, multiplexer_3_out[4], multiplexer_1_out[3]);
  Adder adder_96 (.B(and_105_out), .Cin(adder_103_cout), .A(adder_95_out), .Out(adder_96_out), .Cout(adder_96_cout));
  and and_106 (and_106_out, multiplexer_3_out[5], multiplexer_1_out[2]);
  Adder adder_97 (.B(and_106_out), .Cin(adder_104_cout), .A(adder_96_out), .Out(adder_97_out), .Cout(adder_97_cout));
  and and_107 (and_107_out, multiplexer_3_out[6], multiplexer_1_out[1]);
  Adder adder_98 (.B(and_107_out), .Cin(adder_105_cout), .A(adder_97_out), .Out(adder_98_out), .Cout(adder_98_cout));
  and and_108 (and_108_out, multiplexer_3_out[7], multiplexer_1_out[0]);
  Adder adder_99 (.B(and_108_out), .A(adder_98_out), .Out(and_136_out[7]), .Cout(adder_99_cout));  // open: Cin
  and and_109 (and_109_out, multiplexer_3_out[0], multiplexer_1_out[6]);
  and and_110 (and_110_out, multiplexer_3_out[1], multiplexer_1_out[5]);
  Adder adder_100 (.B(and_110_out), .Cin(adder_106_cout), .A(and_109_out), .Out(adder_100_out), .Cout(adder_100_cout));
  and and_111 (and_111_out, multiplexer_3_out[2], multiplexer_1_out[4]);
  Adder adder_101 (
    .B(and_111_out), .Cin(adder_107_cout), .A(adder_100_out), .Out(adder_101_out), .Cout(adder_101_cout));
  and and_112 (and_112_out, multiplexer_3_out[3], multiplexer_1_out[3]);
  Adder adder_102 (
    .B(and_112_out), .Cin(adder_108_cout), .A(adder_101_out), .Out(adder_102_out), .Cout(adder_102_cout));
  and and_113 (and_113_out, multiplexer_3_out[4], multiplexer_1_out[2]);
  Adder adder_103 (
    .B(and_113_out), .Cin(adder_109_cout), .A(adder_102_out), .Out(adder_103_out), .Cout(adder_103_cout));
  and and_114 (and_114_out, multiplexer_3_out[5], multiplexer_1_out[1]);
  Adder adder_104 (
    .B(and_114_out), .Cin(adder_110_cout), .A(adder_103_out), .Out(adder_104_out), .Cout(adder_104_cout));
  and and_115 (and_115_out, multiplexer_3_out[6], multiplexer_1_out[0]);
  Adder adder_105 (.B(and_115_out), .A(adder_104_out), .Out(and_136_out[6]), .Cout(adder_105_cout));  // open: Cin
  and and_116 (and_116_out, multiplexer_3_out[0], multiplexer_1_out[5]);
  and and_117 (and_117_out, multiplexer_3_out[1], multiplexer_1_out[4]);
  Adder adder_106 (.B(and_117_out), .Cin(adder_111_cout), .A(and_116_out), .Out(adder_106_out), .Cout(adder_106_cout));
  and and_118 (and_118_out, multiplexer_3_out[2], multiplexer_1_out[3]);
  Adder adder_107 (
    .B(and_118_out), .Cin(adder_112_cout), .A(adder_106_out), .Out(adder_107_out), .Cout(adder_107_cout));
  and and_119 (and_119_out, multiplexer_3_out[3], multiplexer_1_out[2]);
  Adder adder_108 (
    .B(and_119_out), .Cin(adder_113_cout), .A(adder_107_out), .Out(adder_108_out), .Cout(adder_108_cout));
  and and_120 (and_120_out, multiplexer_3_out[4], multiplexer_1_out[1]);
  Adder adder_109 (
    .B(and_120_out), .Cin(adder_114_cout), .A(adder_108_out), .Out(adder_109_out), .Cout(adder_109_cout));
  and and_121 (and_121_out, multiplexer_3_out[5], multiplexer_1_out[0]);
  Adder adder_110 (.B(and_121_out), .A(adder_109_out), .Out(and_136_out[5]), .Cout(adder_110_cout));  // open: Cin
  and and_122 (and_122_out, multiplexer_3_out[0], multiplexer_1_out[4]);
  and and_123 (and_123_out, multiplexer_3_out[1], multiplexer_1_out[3]);
  Adder adder_111 (.B(and_123_out), .Cin(adder_115_cout), .A(and_122_out), .Out(adder_111_out), .Cout(adder_111_cout));
  and and_124 (and_124_out, multiplexer_3_out[2], multiplexer_1_out[2]);
  Adder adder_112 (
    .B(and_124_out), .Cin(adder_116_cout), .A(adder_111_out), .Out(adder_112_out), .Cout(adder_112_cout));
  and and_125 (and_125_out, multiplexer_3_out[3], multiplexer_1_out[1]);
  Adder adder_113 (
    .B(and_125_out), .Cin(adder_117_cout), .A(adder_112_out), .Out(adder_113_out), .Cout(adder_113_cout));
  and and_126 (and_126_out, multiplexer_3_out[4], multiplexer_1_out[0]);
  Adder adder_114 (.B(and_126_out), .A(adder_113_out), .Out(and_136_out[4]), .Cout(adder_114_cout));  // open: Cin
  and and_127 (and_127_out, multiplexer_3_out[0], multiplexer_1_out[3]);
  and and_128 (and_128_out, multiplexer_3_out[1], multiplexer_1_out[2]);
  Adder adder_115 (.B(and_128_out), .Cin(adder_118_cout), .A(and_127_out), .Out(adder_115_out), .Cout(adder_115_cout));
  and and_129 (and_129_out, multiplexer_3_out[2], multiplexer_1_out[1]);
  Adder adder_116 (
    .B(and_129_out), .Cin(adder_119_cout), .A(adder_115_out), .Out(adder_116_out), .Cout(adder_116_cout));
  and and_130 (and_130_out, multiplexer_3_out[3], multiplexer_1_out[0]);
  Adder adder_117 (.B(and_130_out), .A(adder_116_out), .Out(and_136_out[3]), .Cout(adder_117_cout));  // open: Cin
  and and_131 (and_131_out, multiplexer_3_out[0], multiplexer_1_out[2]);
  and and_132 (and_132_out, multiplexer_3_out[1], multiplexer_1_out[1]);
  Adder adder_118 (.B(and_132_out), .Cin(adder_120_cout), .A(and_131_out), .Out(adder_118_out), .Cout(adder_118_cout));
  and and_133 (and_133_out, multiplexer_3_out[2], multiplexer_1_out[0]);
  Adder adder_119 (.B(and_133_out), .A(adder_118_out), .Out(and_136_out[2]), .Cout(adder_119_cout));  // open: Cin
  and and_134 (and_134_out, multiplexer_3_out[0], multiplexer_1_out[1]);
  and and_135 (and_135_out, multiplexer_3_out[1], multiplexer_1_out[0]);
  Adder adder_120 (.B(and_135_out), .A(and_134_out), .Out(and_136_out[1]), .Cout(adder_120_cout));  // open: Cin
  TWOS_COMP_16_BIT twos_comp_16_bit_1 (.DATA_IN(A), .DATA_OUT(twos_comp_16_bit_1_data_out));
  Multiplexer #(.width(16)) multiplexer_1 (
    .in0(A), .in1(twos_comp_16_bit_1_data_out), .out(multiplexer_1_out), .sel(A[15]));
  and and_136 (and_136_out[0], multiplexer_3_out[0], multiplexer_1_out[0]);
  Multiplexer #(.width(16)) multiplexer_2 (
    .in0(and_136_out), .in1(twos_comp_16_bit_2_data_out), .out(MUL), .sel(xor_1_out));
  TWOS_COMP_16_BIT twos_comp_16_bit_2 (.DATA_IN(and_136_out), .DATA_OUT(twos_comp_16_bit_2_data_out));
  Multiplexer #(.width(16)) multiplexer_3 (
    .in0(B), .in1(twos_comp_16_bit_3_data_out), .out(multiplexer_3_out), .sel(B[15]));
  TWOS_COMP_16_BIT twos_comp_16_bit_3 (.DATA_IN(B), .DATA_OUT(twos_comp_16_bit_3_data_out));
  xor xor_1 (xor_1_out, B[15], A[15]);
endmodule

module SUBTRACTOR_1 (
  input  A,
  input  B,
  input  BORROW_IN,
  output SUB,
  output BORROW_OUT
);

  wire and_1_out, and_2_out, not_1_out, or_1_out, xor_1_out;

  xor xor_1 (xor_1_out, A, B);
  not not_1 (not_1_out, A);
  and and_1 (and_1_out, not_1_out, or_1_out);
  or or_1 (or_1_out, B, BORROW_IN);
  xor xor_2 (SUB, xor_1_out, BORROW_IN);
  and and_2 (and_2_out, A, B, BORROW_IN);
  or or_2 (BORROW_OUT, and_1_out, and_2_out);
endmodule

module ADDER_16_BIT (
  input  [15:0] A,
  input  [15:0] B,
  input  CARRY_IN,
  output CARRY_OUT,
  output [15:0] SUM
);

  wire adder_2_cout, adder_3_cout, adder_4_cout, adder_5_cout, adder_6_cout, adder_7_cout, adder_8_cout,
       adder_9_cout, adder_10_cout, adder_11_cout, adder_12_cout, adder_13_cout, adder_14_cout,
       adder_15_cout, adder_16_cout;

  Adder adder_1 (.B(B[15]), .Cin(adder_2_cout), .A(A[15]), .Out(SUM[15]), .Cout(CARRY_OUT));
  Adder adder_2 (.B(B[14]), .Cin(adder_3_cout), .A(A[14]), .Out(SUM[14]), .Cout(adder_2_cout));
  Adder adder_3 (.B(B[13]), .Cin(adder_4_cout), .A(A[13]), .Out(SUM[13]), .Cout(adder_3_cout));
  Adder adder_4 (.B(B[12]), .Cin(adder_5_cout), .A(A[12]), .Out(SUM[12]), .Cout(adder_4_cout));
  Adder adder_5 (.B(B[11]), .Cin(adder_6_cout), .A(A[11]), .Out(SUM[11]), .Cout(adder_5_cout));
  Adder adder_6 (.B(B[10]), .Cin(adder_7_cout), .A(A[10]), .Out(SUM[10]), .Cout(adder_6_cout));
  Adder adder_7 (.B(B[9]), .Cin(adder_8_cout), .A(A[9]), .Out(SUM[9]), .Cout(adder_7_cout));
  Adder adder_8 (.B(B[8]), .Cin(adder_9_cout), .A(A[8]), .Out(SUM[8]), .Cout(adder_8_cout));
  Adder adder_9 (.B(B[7]), .Cin(adder_10_cout), .A(A[7]), .Out(SUM[7]), .Cout(adder_9_cout));
  Adder adder_10 (.B(B[6]), .Cin(adder_11_cout), .A(A[6]), .Out(SUM[6]), .Cout(adder_10_cout));
  Adder adder_11 (.B(B[5]), .Cin(adder_12_cout), .A(A[5]), .Out(SUM[5]), .Cout(adder_11_cout));
  Adder adder_12 (.B(B[4]), .Cin(adder_13_cout), .A(A[4]), .Out(SUM[4]), .Cout(adder_12_cout));
  Adder adder_13 (.B(B[3]), .Cin(adder_14_cout), .A(A[3]), .Out(SUM[3]), .Cout(adder_13_cout));
  Adder adder_14 (.B(B[2]), .Cin(adder_15_cout), .A(A[2]), .Out(SUM[2]), .Cout(adder_14_cout));
  Adder adder_15 (.B(B[1]), .Cin(adder_16_cout), .A(A[1]), .Out(SUM[1]), .Cout(adder_15_cout));
  Adder adder_16 (.B(B[0]), .Cin(CARRY_IN), .A(A[0]), .Out(SUM[0]), .Cout(adder_16_cout));
endmodule

module SUBTRACTOR_16_BIT (
  input  [15:0] A,
  input  [15:0] B,
  input  BORROW_IN,
  output BORROW_OUT,
  output [15:0] SUB
);

  wire subtractor_1_2_borrow_out, subtractor_1_3_borrow_out, subtractor_1_4_borrow_out,
       subtractor_1_5_borrow_out, subtractor_1_6_borrow_out, subtractor_1_7_borrow_out,
       subtractor_1_8_borrow_out, subtractor_1_9_borrow_out, subtractor_1_10_borrow_out,
       subtractor_1_11_borrow_out, subtractor_1_12_borrow_out, subtractor_1_13_borrow_out,
       subtractor_1_14_borrow_out, subtractor_1_15_borrow_out, subtractor_1_16_borrow_out;

  SUBTRACTOR_1 subtractor_1_1 (
    .B(B[15]), .BORROW_IN(subtractor_1_2_borrow_out), .A(A[15]), .SUB(SUB[15]), .BORROW_OUT(BORROW_OUT));
  SUBTRACTOR_1 subtractor_1_2 (
    .B(B[14]), .BORROW_IN(subtractor_1_3_borrow_out), .A(A[14]), .SUB(SUB[14]),
    .BORROW_OUT(subtractor_1_2_borrow_out));
  SUBTRACTOR_1 subtractor_1_3 (
    .B(B[13]), .BORROW_IN(subtractor_1_4_borrow_out), .A(A[13]), .SUB(SUB[13]),
    .BORROW_OUT(subtractor_1_3_borrow_out));
  SUBTRACTOR_1 subtractor_1_4 (
    .B(B[12]), .BORROW_IN(subtractor_1_5_borrow_out), .A(A[12]), .SUB(SUB[12]),
    .BORROW_OUT(subtractor_1_4_borrow_out));
  SUBTRACTOR_1 subtractor_1_5 (
    .B(B[11]), .BORROW_IN(subtractor_1_6_borrow_out), .A(A[11]), .SUB(SUB[11]),
    .BORROW_OUT(subtractor_1_5_borrow_out));
  SUBTRACTOR_1 subtractor_1_6 (
    .B(B[10]), .BORROW_IN(subtractor_1_7_borrow_out), .A(A[10]), .SUB(SUB[10]),
    .BORROW_OUT(subtractor_1_6_borrow_out));
  SUBTRACTOR_1 subtractor_1_7 (
    .B(B[9]), .BORROW_IN(subtractor_1_8_borrow_out), .A(A[9]), .SUB(SUB[9]),
    .BORROW_OUT(subtractor_1_7_borrow_out));
  SUBTRACTOR_1 subtractor_1_8 (
    .B(B[8]), .BORROW_IN(subtractor_1_9_borrow_out), .A(A[8]), .SUB(SUB[8]),
    .BORROW_OUT(subtractor_1_8_borrow_out));
  SUBTRACTOR_1 subtractor_1_9 (
    .B(B[7]), .BORROW_IN(subtractor_1_10_borrow_out), .A(A[7]), .SUB(SUB[7]),
    .BORROW_OUT(subtractor_1_9_borrow_out));
  SUBTRACTOR_1 subtractor_1_10 (
    .B(B[6]), .BORROW_IN(subtractor_1_11_borrow_out), .A(A[6]), .SUB(SUB[6]),
    .BORROW_OUT(subtractor_1_10_borrow_out));
  SUBTRACTOR_1 subtractor_1_11 (
    .B(B[5]), .BORROW_IN(subtractor_1_12_borrow_out), .A(A[5]), .SUB(SUB[5]),
    .BORROW_OUT(subtractor_1_11_borrow_out));
  SUBTRACTOR_1 subtractor_1_12 (
    .B(B[4]), .BORROW_IN(subtractor_1_13_borrow_out), .A(A[4]), .SUB(SUB[4]),
    .BORROW_OUT(subtractor_1_12_borrow_out));
  SUBTRACTOR_1 subtractor_1_13 (
    .B(B[3]), .BORROW_IN(subtractor_1_14_borrow_out), .A(A[3]), .SUB(SUB[3]),
    .BORROW_OUT(subtractor_1_13_borrow_out));
  SUBTRACTOR_1 subtractor_1_14 (
    .B(B[2]), .BORROW_IN(subtractor_1_15_borrow_out), .A(A[2]), .SUB(SUB[2]),
    .BORROW_OUT(subtractor_1_14_borrow_out));
  SUBTRACTOR_1 subtractor_1_15 (
    .B(B[1]), .BORROW_IN(subtractor_1_16_borrow_out), .A(A[1]), .SUB(SUB[1]),
    .BORROW_OUT(subtractor_1_15_borrow_out));
  SUBTRACTOR_1 subtractor_1_16 (
    .B(B[0]), .BORROW_IN(BORROW_IN), .A(A[0]), .SUB(SUB[0]), .BORROW_OUT(subtractor_1_16_borrow_out));
endmodule

module TWOS_COMP_16_BIT (
  input  [15:0] DATA_IN,
  output [15:0] DATA_OUT
);

  wire [15:0] subtractor_16_bit_1_sub;

  SUBTRACTOR_16_BIT subtractor_16_bit_1 (
    .A({16{1'b1}}), .B(DATA_IN), .SUB(subtractor_16_bit_1_sub));  // open: BORROW_IN, BORROW_OUT
  ADDER_16_BIT adder_16_bit_1 (.A(subtractor_16_bit_1_sub), .B(16'h1), .SUM(DATA_OUT));  // open: CARRY_IN, CARRY_OUT
endmodule
module DIVIDER_16_BIT (
  input  [15:0] DIVISIOR,
  input  [15:0] DIVIDEND,
  output [15:0] REMAINDER,
  output [15:0] QUOTIENT
);

  wire multiplexer_1_out, multiplexer_3_out, multiplexer_4_out, multiplexer_6_out, multiplexer_7_out,
       multiplexer_8_out, multiplexer_10_out, multiplexer_11_out, multiplexer_12_out, multiplexer_13_out,
       multiplexer_16_out, multiplexer_17_out, multiplexer_18_out, multiplexer_19_out, multiplexer_20_out,
       multiplexer_22_out, multiplexer_23_out, multiplexer_24_out, multiplexer_25_out, multiplexer_26_out,
       multiplexer_27_out, multiplexer_29_out, multiplexer_30_out, multiplexer_31_out, multiplexer_32_out,
       multiplexer_33_out, multiplexer_34_out, multiplexer_35_out, multiplexer_37_out, multiplexer_38_out,
       multiplexer_39_out, multiplexer_40_out, multiplexer_41_out, multiplexer_42_out, multiplexer_43_out,
       multiplexer_44_out, multiplexer_47_out, multiplexer_48_out, multiplexer_49_out, multiplexer_50_out,
       multiplexer_51_out, multiplexer_52_out, multiplexer_53_out, multiplexer_54_out, multiplexer_55_out,
       multiplexer_56_out, multiplexer_57_out, multiplexer_58_out, multiplexer_59_out, multiplexer_60_out,
       multiplexer_61_out, multiplexer_62_out, multiplexer_63_out, multiplexer_64_out, multiplexer_65_out,
       multiplexer_67_out, multiplexer_68_out, multiplexer_69_out, multiplexer_70_out, multiplexer_71_out,
       multiplexer_72_out, multiplexer_73_out, multiplexer_74_out, multiplexer_75_out, multiplexer_76_out,
       multiplexer_77_out, multiplexer_79_out, multiplexer_80_out, multiplexer_81_out, multiplexer_82_out,
       multiplexer_83_out, multiplexer_84_out, multiplexer_85_out, multiplexer_86_out, multiplexer_87_out,
       multiplexer_88_out, multiplexer_89_out, multiplexer_90_out, multiplexer_92_out, multiplexer_93_out,
       multiplexer_94_out, multiplexer_95_out, multiplexer_96_out, multiplexer_97_out, multiplexer_98_out,
       multiplexer_99_out, multiplexer_100_out, multiplexer_101_out, multiplexer_102_out,
       multiplexer_103_out, multiplexer_104_out, multiplexer_106_out, multiplexer_107_out,
       multiplexer_108_out, multiplexer_109_out, multiplexer_110_out, multiplexer_111_out,
       multiplexer_112_out, multiplexer_113_out, multiplexer_114_out, multiplexer_115_out,
       multiplexer_116_out, multiplexer_117_out, multiplexer_118_out, multiplexer_119_out,
       multiplexer_121_out, multiplexer_122_out, multiplexer_123_out, multiplexer_124_out,
       multiplexer_125_out, multiplexer_126_out, multiplexer_127_out, multiplexer_128_out,
       multiplexer_129_out, multiplexer_130_out, multiplexer_131_out, multiplexer_132_out,
       multiplexer_133_out, multiplexer_134_out, multiplexer_135_out, subtractor_1_16_sub,
       subtractor_1_17_borrow_out, subtractor_1_18_borrow_out, subtractor_1_19_borrow_out,
       subtractor_1_20_borrow_out, subtractor_1_21_borrow_out, subtractor_1_22_borrow_out,
       subtractor_1_23_borrow_out, subtractor_1_24_borrow_out, subtractor_1_25_borrow_out,
       subtractor_1_26_borrow_out, subtractor_1_27_borrow_out, subtractor_1_28_borrow_out,
       subtractor_1_29_borrow_out, subtractor_1_30_borrow_out, subtractor_1_31_borrow_out,
       subtractor_1_31_sub, subtractor_1_32_borrow_out, subtractor_1_32_sub, subtractor_1_33_borrow_out,
       subtractor_1_34_borrow_out, subtractor_1_35_borrow_out, subtractor_1_36_borrow_out,
       subtractor_1_37_borrow_out, subtractor_1_38_borrow_out, subtractor_1_39_borrow_out,
       subtractor_1_40_borrow_out, subtractor_1_41_borrow_out, subtractor_1_42_borrow_out,
       subtractor_1_43_borrow_out, subtractor_1_44_borrow_out, subtractor_1_45_borrow_out,
       subtractor_1_46_borrow_out, subtractor_1_46_sub, subtractor_1_47_borrow_out, subtractor_1_47_sub,
       subtractor_1_48_borrow_out, subtractor_1_48_sub, subtractor_1_49_borrow_out,
       subtractor_1_50_borrow_out, subtractor_1_51_borrow_out, subtractor_1_52_borrow_out,
       subtractor_1_53_borrow_out, subtractor_1_54_borrow_out, subtractor_1_55_borrow_out,
       subtractor_1_56_borrow_out, subtractor_1_57_borrow_out, subtractor_1_58_borrow_out,
       subtractor_1_59_borrow_out, subtractor_1_60_borrow_out, subtractor_1_61_borrow_out,
       subtractor_1_61_sub, subtractor_1_62_borrow_out, subtractor_1_62_sub, subtractor_1_63_borrow_out,
       subtractor_1_63_sub, subtractor_1_64_borrow_out, subtractor_1_64_sub, subtractor_1_65_borrow_out,
       subtractor_1_66_borrow_out, subtractor_1_67_borrow_out, subtractor_1_68_borrow_out,
       subtractor_1_69_borrow_out, subtractor_1_70_borrow_out, subtractor_1_71_borrow_out,
       subtractor_1_72_borrow_out, subtractor_1_73_borrow_out, subtractor_1_74_borrow_out,
       subtractor_1_75_borrow_out, subtractor_1_76_borrow_out, subtractor_1_76_sub,
       subtractor_1_77_borrow_out, subtractor_1_77_sub, subtractor_1_78_borrow_out, subtractor_1_78_sub,
       subtractor_1_79_borrow_out, subtractor_1_79_sub, subtractor_1_80_borrow_out, subtractor_1_80_sub,
       subtractor_1_81_borrow_out, subtractor_1_82_borrow_out, subtractor_1_83_borrow_out,
       subtractor_1_84_borrow_out, subtractor_1_85_borrow_out, subtractor_1_86_borrow_out,
       subtractor_1_87_borrow_out, subtractor_1_88_borrow_out, subtractor_1_89_borrow_out,
       subtractor_1_90_borrow_out, subtractor_1_91_borrow_out, subtractor_1_91_sub,
       subtractor_1_92_borrow_out, subtractor_1_92_sub, subtractor_1_93_borrow_out, subtractor_1_93_sub,
       subtractor_1_94_borrow_out, subtractor_1_94_sub, subtractor_1_95_borrow_out, subtractor_1_95_sub,
       subtractor_1_96_borrow_out, subtractor_1_96_sub, subtractor_1_97_borrow_out,
       subtractor_1_98_borrow_out, subtractor_1_99_borrow_out, subtractor_1_100_borrow_out,
       subtractor_1_101_borrow_out, subtractor_1_102_borrow_out, subtractor_1_103_borrow_out,
       subtractor_1_104_borrow_out, subtractor_1_105_borrow_out, subtractor_1_106_borrow_out,
       subtractor_1_106_sub, subtractor_1_107_borrow_out, subtractor_1_107_sub, subtractor_1_108_borrow_out,
       subtractor_1_108_sub, subtractor_1_109_borrow_out, subtractor_1_109_sub, subtractor_1_110_borrow_out,
       subtractor_1_110_sub, subtractor_1_111_borrow_out, subtractor_1_111_sub, subtractor_1_112_borrow_out,
       subtractor_1_112_sub, subtractor_1_113_borrow_out, subtractor_1_114_borrow_out,
       subtractor_1_115_borrow_out, subtractor_1_116_borrow_out, subtractor_1_117_borrow_out,
       subtractor_1_118_borrow_out, subtractor_1_119_borrow_out, subtractor_1_120_borrow_out,
       subtractor_1_121_borrow_out, subtractor_1_121_sub, subtractor_1_122_borrow_out, subtractor_1_122_sub,
       subtractor_1_123_borrow_out, subtractor_1_123_sub, subtractor_1_124_borrow_out, subtractor_1_124_sub,
       subtractor_1_125_borrow_out, subtractor_1_125_sub, subtractor_1_126_borrow_out, subtractor_1_126_sub,
       subtractor_1_127_borrow_out, subtractor_1_127_sub, subtractor_1_128_borrow_out, subtractor_1_128_sub,
       subtractor_1_129_borrow_out, subtractor_1_130_borrow_out, subtractor_1_131_borrow_out,
       subtractor_1_132_borrow_out, subtractor_1_133_borrow_out, subtractor_1_134_borrow_out,
       subtractor_1_135_borrow_out, subtractor_1_136_borrow_out, subtractor_1_136_sub,
       subtractor_1_137_borrow_out, subtractor_1_137_sub, subtractor_1_138_borrow_out, subtractor_1_138_sub,
       subtractor_1_139_borrow_out, subtractor_1_139_sub, subtractor_1_140_borrow_out, subtractor_1_140_sub,
       subtractor_1_141_borrow_out, subtractor_1_141_sub, subtractor_1_142_borrow_out, subtractor_1_142_sub,
       subtractor_1_143_borrow_out, subtractor_1_143_sub, subtractor_1_144_borrow_out, subtractor_1_144_sub,
       subtractor_1_145_borrow_out, subtractor_1_146_borrow_out, subtractor_1_147_borrow_out,
       subtractor_1_148_borrow_out, subtractor_1_149_borrow_out, subtractor_1_150_borrow_out,
       subtractor_1_151_borrow_out, subtractor_1_151_sub, subtractor_1_152_borrow_out, subtractor_1_152_sub,
       subtractor_1_153_borrow_out, subtractor_1_153_sub, subtractor_1_154_borrow_out, subtractor_1_154_sub,
       subtractor_1_155_borrow_out, subtractor_1_155_sub, subtractor_1_156_borrow_out, subtractor_1_156_sub,
       subtractor_1_157_borrow_out, subtractor_1_157_sub, subtractor_1_158_borrow_out, subtractor_1_158_sub,
       subtractor_1_159_borrow_out, subtractor_1_159_sub, subtractor_1_160_borrow_out, subtractor_1_160_sub,
       subtractor_1_161_borrow_out, subtractor_1_162_borrow_out, subtractor_1_163_borrow_out,
       subtractor_1_164_borrow_out, subtractor_1_165_borrow_out, subtractor_1_166_borrow_out,
       subtractor_1_166_sub, subtractor_1_167_borrow_out, subtractor_1_167_sub, subtractor_1_168_borrow_out,
       subtractor_1_168_sub, subtractor_1_169_borrow_out, subtractor_1_169_sub, subtractor_1_170_borrow_out,
       subtractor_1_170_sub, subtractor_1_171_borrow_out, subtractor_1_171_sub, subtractor_1_172_borrow_out,
       subtractor_1_172_sub, subtractor_1_173_borrow_out, subtractor_1_173_sub, subtractor_1_174_borrow_out,
       subtractor_1_174_sub, subtractor_1_175_borrow_out, subtractor_1_175_sub, subtractor_1_176_borrow_out,
       subtractor_1_176_sub, subtractor_1_177_borrow_out, subtractor_1_178_borrow_out,
       subtractor_1_179_borrow_out, subtractor_1_180_borrow_out, subtractor_1_181_borrow_out,
       subtractor_1_181_sub, subtractor_1_182_borrow_out, subtractor_1_182_sub, subtractor_1_183_borrow_out,
       subtractor_1_183_sub, subtractor_1_184_borrow_out, subtractor_1_184_sub, subtractor_1_185_borrow_out,
       subtractor_1_185_sub, subtractor_1_186_borrow_out, subtractor_1_186_sub, subtractor_1_187_borrow_out,
       subtractor_1_187_sub, subtractor_1_188_borrow_out, subtractor_1_188_sub, subtractor_1_189_borrow_out,
       subtractor_1_189_sub, subtractor_1_190_borrow_out, subtractor_1_190_sub, subtractor_1_191_borrow_out,
       subtractor_1_191_sub, subtractor_1_192_borrow_out, subtractor_1_192_sub, subtractor_1_193_borrow_out,
       subtractor_1_194_borrow_out, subtractor_1_195_borrow_out, subtractor_1_196_borrow_out,
       subtractor_1_196_sub, subtractor_1_197_borrow_out, subtractor_1_197_sub, subtractor_1_198_borrow_out,
       subtractor_1_198_sub, subtractor_1_199_borrow_out, subtractor_1_199_sub, subtractor_1_200_borrow_out,
       subtractor_1_200_sub, subtractor_1_201_borrow_out, subtractor_1_201_sub, subtractor_1_202_borrow_out,
       subtractor_1_202_sub, subtractor_1_203_borrow_out, subtractor_1_203_sub, subtractor_1_204_borrow_out,
       subtractor_1_204_sub, subtractor_1_205_borrow_out, subtractor_1_205_sub, subtractor_1_206_borrow_out,
       subtractor_1_206_sub, subtractor_1_207_borrow_out, subtractor_1_207_sub, subtractor_1_208_borrow_out,
       subtractor_1_208_sub, subtractor_1_209_borrow_out, subtractor_1_210_borrow_out,
       subtractor_1_211_borrow_out, subtractor_1_211_sub, subtractor_1_212_borrow_out, subtractor_1_212_sub,
       subtractor_1_213_borrow_out, subtractor_1_213_sub, subtractor_1_214_borrow_out, subtractor_1_214_sub,
       subtractor_1_215_borrow_out, subtractor_1_215_sub, subtractor_1_216_borrow_out, subtractor_1_216_sub,
       subtractor_1_217_borrow_out, subtractor_1_217_sub, subtractor_1_218_borrow_out, subtractor_1_218_sub,
       subtractor_1_219_borrow_out, subtractor_1_219_sub, subtractor_1_220_borrow_out, subtractor_1_220_sub,
       subtractor_1_221_borrow_out, subtractor_1_221_sub, subtractor_1_222_borrow_out, subtractor_1_222_sub,
       subtractor_1_223_borrow_out, subtractor_1_223_sub, subtractor_1_224_borrow_out, subtractor_1_224_sub,
       subtractor_1_225_borrow_out, subtractor_1_226_borrow_out, subtractor_1_226_sub,
       subtractor_1_227_borrow_out, subtractor_1_227_sub, subtractor_1_228_borrow_out, subtractor_1_228_sub,
       subtractor_1_229_borrow_out, subtractor_1_229_sub, subtractor_1_230_borrow_out, subtractor_1_230_sub,
       subtractor_1_231_borrow_out, subtractor_1_231_sub, subtractor_1_232_borrow_out, subtractor_1_232_sub,
       subtractor_1_233_borrow_out, subtractor_1_233_sub, subtractor_1_234_borrow_out, subtractor_1_234_sub,
       subtractor_1_235_borrow_out, subtractor_1_235_sub, subtractor_1_236_borrow_out, subtractor_1_236_sub,
       subtractor_1_237_borrow_out, subtractor_1_237_sub, subtractor_1_238_borrow_out, subtractor_1_238_sub,
       subtractor_1_239_borrow_out, subtractor_1_239_sub, subtractor_1_240_borrow_out, subtractor_1_240_sub,
       subtractor_1_241_borrow_out, subtractor_1_241_sub, subtractor_1_242_borrow_out, subtractor_1_242_sub,
       subtractor_1_243_borrow_out, subtractor_1_243_sub, subtractor_1_244_borrow_out, subtractor_1_244_sub,
       subtractor_1_245_borrow_out, subtractor_1_245_sub, subtractor_1_246_borrow_out, subtractor_1_246_sub,
       subtractor_1_247_borrow_out, subtractor_1_247_sub, subtractor_1_248_borrow_out, subtractor_1_248_sub,
       subtractor_1_249_borrow_out, subtractor_1_249_sub, subtractor_1_250_borrow_out, subtractor_1_250_sub,
       subtractor_1_251_borrow_out, subtractor_1_251_sub, subtractor_1_252_borrow_out, subtractor_1_252_sub,
       subtractor_1_253_borrow_out, subtractor_1_253_sub, subtractor_1_254_borrow_out, subtractor_1_254_sub,
       subtractor_1_255_borrow_out, subtractor_1_255_sub, subtractor_1_256_borrow_out, subtractor_1_256_sub,
       xor_1_out;
  wire [15:0] multiplexer_137_out, multiplexer_139_out, not_1_out, subtractor_1_16_borrow_out,
       twos_comp_16_bit_1_data_out, twos_comp_16_bit_2_data_out, twos_comp_16_bit_3_data_out;

  SUBTRACTOR_1 subtractor_1_1 (
    .B(multiplexer_137_out[15]), .BORROW_IN(subtractor_1_17_borrow_out), .A(1'b0),
    .BORROW_OUT(subtractor_1_16_borrow_out[15]));  // open: SUB
  SUBTRACTOR_1 subtractor_1_2 (
    .B(multiplexer_137_out[15]), .BORROW_IN(subtractor_1_18_borrow_out), .A(1'b0),
    .BORROW_OUT(subtractor_1_16_borrow_out[14]));  // open: SUB
  SUBTRACTOR_1 subtractor_1_3 (
    .B(multiplexer_137_out[15]), .BORROW_IN(subtractor_1_19_borrow_out), .A(1'b0),
    .BORROW_OUT(subtractor_1_16_borrow_out[13]));  // open: SUB
  SUBTRACTOR_1 subtractor_1_4 (
    .B(multiplexer_137_out[15]), .BORROW_IN(subtractor_1_20_borrow_out), .A(1'b0),
    .BORROW_OUT(subtractor_1_16_borrow_out[12]));  // open: SUB
  SUBTRACTOR_1 subtractor_1_5 (
    .B(multiplexer_137_out[15]), .BORROW_IN(subtractor_1_21_borrow_out), .A(1'b0),
    .BORROW_OUT(subtractor_1_16_borrow_out[11]));  // open: SUB
  SUBTRACTOR_1 subtractor_1_6 (
    .B(multiplexer_137_out[15]), .BORROW_IN(subtractor_1_22_borrow_out), .A(1'b0),
    .BORROW_OUT(subtractor_1_16_borrow_out[10]));  // open: SUB
  SUBTRACTOR_1 subtractor_1_7 (
    .B(multiplexer_137_out[15]), .BORROW_IN(subtractor_1_23_borrow_out), .A(1'b0),
    .BORROW_OUT(subtractor_1_16_borrow_out[9]));  // open: SUB
  SUBTRACTOR_1 subtractor_1_8 (
    .B(multiplexer_137_out[15]), .BORROW_IN(subtractor_1_24_borrow_out), .A(1'b0),
    .BORROW_OUT(subtractor_1_16_borrow_out[8]));  // open: SUB
  SUBTRACTOR_1 subtractor_1_9 (
    .B(multiplexer_137_out[15]), .BORROW_IN(subtractor_1_25_borrow_out), .A(1'b0),
    .BORROW_OUT(subtractor_1_16_borrow_out[7]));  // open: SUB
  SUBTRACTOR_1 subtractor_1_10 (
    .B(multiplexer_137_out[15]), .BORROW_IN(subtractor_1_26_borrow_out), .A(1'b0),
    .BORROW_OUT(subtractor_1_16_borrow_out[6]));  // open: SUB
  SUBTRACTOR_1 subtractor_1_11 (
    .B(multiplexer_137_out[15]), .BORROW_IN(subtractor_1_27_borrow_out), .A(1'b0),
    .BORROW_OUT(subtractor_1_16_borrow_out[5]));  // open: SUB
  SUBTRACTOR_1 subtractor_1_12 (
    .B(multiplexer_137_out[15]), .BORROW_IN(subtractor_1_28_borrow_out), .A(1'b0),
    .BORROW_OUT(subtractor_1_16_borrow_out[4]));  // open: SUB
  SUBTRACTOR_1 subtractor_1_13 (
    .B(multiplexer_137_out[15]), .BORROW_IN(subtractor_1_29_borrow_out), .A(1'b0),
    .BORROW_OUT(subtractor_1_16_borrow_out[3]));  // open: SUB
  SUBTRACTOR_1 subtractor_1_14 (
    .B(multiplexer_137_out[15]), .BORROW_IN(subtractor_1_30_borrow_out), .A(1'b0),
    .BORROW_OUT(subtractor_1_16_borrow_out[2]));  // open: SUB
  SUBTRACTOR_1 subtractor_1_15 (
    .B(multiplexer_137_out[15]), .BORROW_IN(subtractor_1_31_borrow_out), .A(1'b0),
    .BORROW_OUT(subtractor_1_16_borrow_out[1]));  // open: SUB
  SUBTRACTOR_1 subtractor_1_16 (
    .B(multiplexer_137_out[15]), .BORROW_IN(subtractor_1_32_borrow_out), .A(multiplexer_1_out),
    .SUB(subtractor_1_16_sub), .BORROW_OUT(subtractor_1_16_borrow_out[0]));
  assign not_1_out = ~subtractor_1_16_borrow_out;  // NOT_Gate not_1, 16 bits wide
  Multiplexer multiplexer_1 (
    .in0(subtractor_1_31_sub), .in1(multiplexer_3_out), .out(multiplexer_1_out),
    .sel(subtractor_1_16_borrow_out[1]));
  Multiplexer multiplexer_2 (
    .in0(subtractor_1_16_sub), .in1(multiplexer_1_out), .out(REMAINDER[15]),
    .sel(subtractor_1_16_borrow_out[0]));
  SUBTRACTOR_1 subtractor_1_17 (
    .B(multiplexer_137_out[14]), .BORROW_IN(subtractor_1_33_borrow_out), .A(1'b0),
    .BORROW_OUT(subtractor_1_17_borrow_out));  // open: SUB
  SUBTRACTOR_1 subtractor_1_18 (
    .B(multiplexer_137_out[14]), .BORROW_IN(subtractor_1_34_borrow_out), .A(1'b0),
    .BORROW_OUT(subtractor_1_18_borrow_out));  // open: SUB
  SUBTRACTOR_1 subtractor_1_19 (
    .B(multiplexer_137_out[14]), .BORROW_IN(subtractor_1_35_borrow_out), .A(1'b0),
    .BORROW_OUT(subtractor_1_19_borrow_out));  // open: SUB
  SUBTRACTOR_1 subtractor_1_20 (
    .B(multiplexer_137_out[14]), .BORROW_IN(subtractor_1_36_borrow_out), .A(1'b0),
    .BORROW_OUT(subtractor_1_20_borrow_out));  // open: SUB
  SUBTRACTOR_1 subtractor_1_21 (
    .B(multiplexer_137_out[14]), .BORROW_IN(subtractor_1_37_borrow_out), .A(1'b0),
    .BORROW_OUT(subtractor_1_21_borrow_out));  // open: SUB
  SUBTRACTOR_1 subtractor_1_22 (
    .B(multiplexer_137_out[14]), .BORROW_IN(subtractor_1_38_borrow_out), .A(1'b0),
    .BORROW_OUT(subtractor_1_22_borrow_out));  // open: SUB
  SUBTRACTOR_1 subtractor_1_23 (
    .B(multiplexer_137_out[14]), .BORROW_IN(subtractor_1_39_borrow_out), .A(1'b0),
    .BORROW_OUT(subtractor_1_23_borrow_out));  // open: SUB
  SUBTRACTOR_1 subtractor_1_24 (
    .B(multiplexer_137_out[14]), .BORROW_IN(subtractor_1_40_borrow_out), .A(1'b0),
    .BORROW_OUT(subtractor_1_24_borrow_out));  // open: SUB
  SUBTRACTOR_1 subtractor_1_25 (
    .B(multiplexer_137_out[14]), .BORROW_IN(subtractor_1_41_borrow_out), .A(1'b0),
    .BORROW_OUT(subtractor_1_25_borrow_out));  // open: SUB
  SUBTRACTOR_1 subtractor_1_26 (
    .B(multiplexer_137_out[14]), .BORROW_IN(subtractor_1_42_borrow_out), .A(1'b0),
    .BORROW_OUT(subtractor_1_26_borrow_out));  // open: SUB
  SUBTRACTOR_1 subtractor_1_27 (
    .B(multiplexer_137_out[14]), .BORROW_IN(subtractor_1_43_borrow_out), .A(1'b0),
    .BORROW_OUT(subtractor_1_27_borrow_out));  // open: SUB
  SUBTRACTOR_1 subtractor_1_28 (
    .B(multiplexer_137_out[14]), .BORROW_IN(subtractor_1_44_borrow_out), .A(1'b0),
    .BORROW_OUT(subtractor_1_28_borrow_out));  // open: SUB
  SUBTRACTOR_1 subtractor_1_29 (
    .B(multiplexer_137_out[14]), .BORROW_IN(subtractor_1_45_borrow_out), .A(1'b0),
    .BORROW_OUT(subtractor_1_29_borrow_out));  // open: SUB
  SUBTRACTOR_1 subtractor_1_30 (
    .B(multiplexer_137_out[14]), .BORROW_IN(subtractor_1_46_borrow_out), .A(1'b0),
    .BORROW_OUT(subtractor_1_30_borrow_out));  // open: SUB
  Multiplexer multiplexer_3 (
    .in0(subtractor_1_46_sub), .in1(multiplexer_6_out), .out(multiplexer_3_out),
    .sel(subtractor_1_16_borrow_out[2]));
  SUBTRACTOR_1 subtractor_1_31 (
    .B(multiplexer_137_out[14]), .BORROW_IN(subtractor_1_47_borrow_out), .A(multiplexer_3_out),
    .SUB(subtractor_1_31_sub), .BORROW_OUT(subtractor_1_31_borrow_out));
  Multiplexer multiplexer_4 (
    .in0(subtractor_1_47_sub), .in1(multiplexer_7_out), .out(multiplexer_4_out),
    .sel(subtractor_1_16_borrow_out[1]));
  SUBTRACTOR_1 subtractor_1_32 (
    .B(multiplexer_137_out[14]), .BORROW_IN(subtractor_1_48_borrow_out), .A(multiplexer_4_out),
    .SUB(subtractor_1_32_sub), .BORROW_OUT(subtractor_1_32_borrow_out));
  Multiplexer multiplexer_5 (
    .in0(subtractor_1_32_sub), .in1(multiplexer_4_out), .out(REMAINDER[14]),
    .sel(subtractor_1_16_borrow_out[0]));
  SUBTRACTOR_1 subtractor_1_33 (
    .B(multiplexer_137_out[13]), .BORROW_IN(subtractor_1_49_borrow_out), .A(1'b0),
    .BORROW_OUT(subtractor_1_33_borrow_out));  // open: SUB
  SUBTRACTOR_1 subtractor_1_34 (
    .B(multiplexer_137_out[13]), .BORROW_IN(subtractor_1_50_borrow_out), .A(1'b0),
    .BORROW_OUT(subtractor_1_34_borrow_out));  // open: SUB
  SUBTRACTOR_1 subtractor_1_35 (
    .B(multiplexer_137_out[13]), .BORROW_IN(subtractor_1_51_borrow_out), .A(1'b0),
    .BORROW_OUT(subtractor_1_35_borrow_out));  // open: SUB
  SUBTRACTOR_1 subtractor_1_36 (
    .B(multiplexer_137_out[13]), .BORROW_IN(subtractor_1_52_borrow_out), .A(1'b0),
    .BORROW_OUT(subtractor_1_36_borrow_out));  // open: SUB
  SUBTRACTOR_1 subtractor_1_37 (
    .B(multiplexer_137_out[13]), .BORROW_IN(subtractor_1_53_borrow_out), .A(1'b0),
    .BORROW_OUT(subtractor_1_37_borrow_out));  // open: SUB
  SUBTRACTOR_1 subtractor_1_38 (
    .B(multiplexer_137_out[13]), .BORROW_IN(subtractor_1_54_borrow_out), .A(1'b0),
    .BORROW_OUT(subtractor_1_38_borrow_out));  // open: SUB
  SUBTRACTOR_1 subtractor_1_39 (
    .B(multiplexer_137_out[13]), .BORROW_IN(subtractor_1_55_borrow_out), .A(1'b0),
    .BORROW_OUT(subtractor_1_39_borrow_out));  // open: SUB
  SUBTRACTOR_1 subtractor_1_40 (
    .B(multiplexer_137_out[13]), .BORROW_IN(subtractor_1_56_borrow_out), .A(1'b0),
    .BORROW_OUT(subtractor_1_40_borrow_out));  // open: SUB
  SUBTRACTOR_1 subtractor_1_41 (
    .B(multiplexer_137_out[13]), .BORROW_IN(subtractor_1_57_borrow_out), .A(1'b0),
    .BORROW_OUT(subtractor_1_41_borrow_out));  // open: SUB
  SUBTRACTOR_1 subtractor_1_42 (
    .B(multiplexer_137_out[13]), .BORROW_IN(subtractor_1_58_borrow_out), .A(1'b0),
    .BORROW_OUT(subtractor_1_42_borrow_out));  // open: SUB
  SUBTRACTOR_1 subtractor_1_43 (
    .B(multiplexer_137_out[13]), .BORROW_IN(subtractor_1_59_borrow_out), .A(1'b0),
    .BORROW_OUT(subtractor_1_43_borrow_out));  // open: SUB
  SUBTRACTOR_1 subtractor_1_44 (
    .B(multiplexer_137_out[13]), .BORROW_IN(subtractor_1_60_borrow_out), .A(1'b0),
    .BORROW_OUT(subtractor_1_44_borrow_out));  // open: SUB
  SUBTRACTOR_1 subtractor_1_45 (
    .B(multiplexer_137_out[13]), .BORROW_IN(subtractor_1_61_borrow_out), .A(1'b0),
    .BORROW_OUT(subtractor_1_45_borrow_out));  // open: SUB
  Multiplexer multiplexer_6 (
    .in0(subtractor_1_61_sub), .in1(multiplexer_10_out), .out(multiplexer_6_out),
    .sel(subtractor_1_16_borrow_out[3]));
  SUBTRACTOR_1 subtractor_1_46 (
    .B(multiplexer_137_out[13]), .BORROW_IN(subtractor_1_62_borrow_out), .A(multiplexer_6_out),
    .SUB(subtractor_1_46_sub), .BORROW_OUT(subtractor_1_46_borrow_out));
  Multiplexer multiplexer_7 (
    .in0(subtractor_1_62_sub), .in1(multiplexer_11_out), .out(multiplexer_7_out),
    .sel(subtractor_1_16_borrow_out[2]));
  SUBTRACTOR_1 subtractor_1_47 (
    .B(multiplexer_137_out[13]), .BORROW_IN(subtractor_1_63_borrow_out), .A(multiplexer_7_out),
    .SUB(subtractor_1_47_sub), .BORROW_OUT(subtractor_1_47_borrow_out));
  Multiplexer multiplexer_8 (
    .in0(subtractor_1_63_sub), .in1(multiplexer_12_out), .out(multiplexer_8_out),
    .sel(subtractor_1_16_borrow_out[1]));
  SUBTRACTOR_1 subtractor_1_48 (
    .B(multiplexer_137_out[13]), .BORROW_IN(subtractor_1_64_borrow_out), .A(multiplexer_8_out),
    .SUB(subtractor_1_48_sub), .BORROW_OUT(subtractor_1_48_borrow_out));
  Multiplexer multiplexer_9 (
    .in0(subtractor_1_48_sub), .in1(multiplexer_8_out), .out(REMAINDER[13]),
    .sel(subtractor_1_16_borrow_out[0]));
  SUBTRACTOR_1 subtractor_1_49 (
    .B(multiplexer_137_out[12]), .BORROW_IN(subtractor_1_65_borrow_out), .A(1'b0),
    .BORROW_OUT(subtractor_1_49_borrow_out));  // open: SUB
  SUBTRACTOR_1 subtractor_1_50 (
    .B(multiplexer_137_out[12]), .BORROW_IN(subtractor_1_66_borrow_out), .A(1'b0),
    .BORROW_OUT(subtractor_1_50_borrow_out));  // open: SUB
  SUBTRACTOR_1 subtractor_1_51 (
    .B(multiplexer_137_out[12]), .BORROW_IN(subtractor_1_67_borrow_out), .A(1'b0),
    .BORROW_OUT(subtractor_1_51_borrow_out));  // open: SUB
  SUBTRACTOR_1 subtractor_1_52 (
    .B(multiplexer_137_out[12]), .BORROW_IN(subtractor_1_68_borrow_out), .A(1'b0),
    .BORROW_OUT(subtractor_1_52_borrow_out));  // open: SUB
  SUBTRACTOR_1 subtractor_1_53 (
    .B(multiplexer_137_out[12]), .BORROW_IN(subtractor_1_69_borrow_out), .A(1'b0),
    .BORROW_OUT(subtractor_1_53_borrow_out));  // open: SUB
  SUBTRACTOR_1 subtractor_1_54 (
    .B(multiplexer_137_out[12]), .BORROW_IN(subtractor_1_70_borrow_out), .A(1'b0),
    .BORROW_OUT(subtractor_1_54_borrow_out));  // open: SUB
  SUBTRACTOR_1 subtractor_1_55 (
    .B(multiplexer_137_out[12]), .BORROW_IN(subtractor_1_71_borrow_out), .A(1'b0),
    .BORROW_OUT(subtractor_1_55_borrow_out));  // open: SUB
  SUBTRACTOR_1 subtractor_1_56 (
    .B(multiplexer_137_out[12]), .BORROW_IN(subtractor_1_72_borrow_out), .A(1'b0),
    .BORROW_OUT(subtractor_1_56_borrow_out));  // open: SUB
  SUBTRACTOR_1 subtractor_1_57 (
    .B(multiplexer_137_out[12]), .BORROW_IN(subtractor_1_73_borrow_out), .A(1'b0),
    .BORROW_OUT(subtractor_1_57_borrow_out));  // open: SUB
  SUBTRACTOR_1 subtractor_1_58 (
    .B(multiplexer_137_out[12]), .BORROW_IN(subtractor_1_74_borrow_out), .A(1'b0),
    .BORROW_OUT(subtractor_1_58_borrow_out));  // open: SUB
  SUBTRACTOR_1 subtractor_1_59 (
    .B(multiplexer_137_out[12]), .BORROW_IN(subtractor_1_75_borrow_out), .A(1'b0),
    .BORROW_OUT(subtractor_1_59_borrow_out));  // open: SUB
  SUBTRACTOR_1 subtractor_1_60 (
    .B(multiplexer_137_out[12]), .BORROW_IN(subtractor_1_76_borrow_out), .A(1'b0),
    .BORROW_OUT(subtractor_1_60_borrow_out));  // open: SUB
  Multiplexer multiplexer_10 (
    .in0(subtractor_1_76_sub), .in1(multiplexer_16_out), .out(multiplexer_10_out),
    .sel(subtractor_1_16_borrow_out[4]));
  SUBTRACTOR_1 subtractor_1_61 (
    .B(multiplexer_137_out[12]), .BORROW_IN(subtractor_1_77_borrow_out), .A(multiplexer_10_out),
    .SUB(subtractor_1_61_sub), .BORROW_OUT(subtractor_1_61_borrow_out));
  Multiplexer multiplexer_11 (
    .in0(subtractor_1_77_sub), .in1(multiplexer_17_out), .out(multiplexer_11_out),
    .sel(subtractor_1_16_borrow_out[3]));
  SUBTRACTOR_1 subtractor_1_62 (
    .B(multiplexer_137_out[12]), .BORROW_IN(subtractor_1_78_borrow_out), .A(multiplexer_11_out),
    .SUB(subtractor_1_62_sub), .BORROW_OUT(subtractor_1_62_borrow_out));
  Multiplexer multiplexer_12 (
    .in0(subtractor_1_78_sub), .in1(multiplexer_18_out), .out(multiplexer_12_out),
    .sel(subtractor_1_16_borrow_out[2]));
  SUBTRACTOR_1 subtractor_1_63 (
    .B(multiplexer_137_out[12]), .BORROW_IN(subtractor_1_79_borrow_out), .A(multiplexer_12_out),
    .SUB(subtractor_1_63_sub), .BORROW_OUT(subtractor_1_63_borrow_out));
  Multiplexer multiplexer_13 (
    .in0(subtractor_1_79_sub), .in1(multiplexer_19_out), .out(multiplexer_13_out),
    .sel(subtractor_1_16_borrow_out[1]));
  SUBTRACTOR_1 subtractor_1_64 (
    .B(multiplexer_137_out[12]), .BORROW_IN(subtractor_1_80_borrow_out), .A(multiplexer_13_out),
    .SUB(subtractor_1_64_sub), .BORROW_OUT(subtractor_1_64_borrow_out));
  Multiplexer multiplexer_14 (
    .in0(subtractor_1_64_sub), .in1(multiplexer_13_out), .out(REMAINDER[12]),
    .sel(subtractor_1_16_borrow_out[0]));
  TWOS_COMP_16_BIT twos_comp_16_bit_1 (.DATA_IN(not_1_out), .DATA_OUT(twos_comp_16_bit_1_data_out));
  xor xor_1 (xor_1_out, DIVISIOR[15], DIVIDEND[15]);
  Multiplexer #(.width(16)) multiplexer_15 (
    .in0(not_1_out), .in1(twos_comp_16_bit_1_data_out), .out(QUOTIENT), .sel(xor_1_out));
  SUBTRACTOR_1 subtractor_1_65 (
    .B(multiplexer_137_out[11]), .BORROW_IN(subtractor_1_81_borrow_out), .A(1'b0),
    .BORROW_OUT(subtractor_1_65_borrow_out));  // open: SUB
  SUBTRACTOR_1 subtractor_1_66 (
    .B(multiplexer_137_out[11]), .BORROW_IN(subtractor_1_82_borrow_out), .A(1'b0),
    .BORROW_OUT(subtractor_1_66_borrow_out));  // open: SUB
  SUBTRACTOR_1 subtractor_1_67 (
    .B(multiplexer_137_out[11]), .BORROW_IN(subtractor_1_83_borrow_out), .A(1'b0),
    .BORROW_OUT(subtractor_1_67_borrow_out));  // open: SUB
  SUBTRACTOR_1 subtractor_1_68 (
    .B(multiplexer_137_out[11]), .BORROW_IN(subtractor_1_84_borrow_out), .A(1'b0),
    .BORROW_OUT(subtractor_1_68_borrow_out));  // open: SUB
  SUBTRACTOR_1 subtractor_1_69 (
    .B(multiplexer_137_out[11]), .BORROW_IN(subtractor_1_85_borrow_out), .A(1'b0),
    .BORROW_OUT(subtractor_1_69_borrow_out));  // open: SUB
  SUBTRACTOR_1 subtractor_1_70 (
    .B(multiplexer_137_out[11]), .BORROW_IN(subtractor_1_86_borrow_out), .A(1'b0),
    .BORROW_OUT(subtractor_1_70_borrow_out));  // open: SUB
  SUBTRACTOR_1 subtractor_1_71 (
    .B(multiplexer_137_out[11]), .BORROW_IN(subtractor_1_87_borrow_out), .A(1'b0),
    .BORROW_OUT(subtractor_1_71_borrow_out));  // open: SUB
  SUBTRACTOR_1 subtractor_1_72 (
    .B(multiplexer_137_out[11]), .BORROW_IN(subtractor_1_88_borrow_out), .A(1'b0),
    .BORROW_OUT(subtractor_1_72_borrow_out));  // open: SUB
  SUBTRACTOR_1 subtractor_1_73 (
    .B(multiplexer_137_out[11]), .BORROW_IN(subtractor_1_89_borrow_out), .A(1'b0),
    .BORROW_OUT(subtractor_1_73_borrow_out));  // open: SUB
  SUBTRACTOR_1 subtractor_1_74 (
    .B(multiplexer_137_out[11]), .BORROW_IN(subtractor_1_90_borrow_out), .A(1'b0),
    .BORROW_OUT(subtractor_1_74_borrow_out));  // open: SUB
  SUBTRACTOR_1 subtractor_1_75 (
    .B(multiplexer_137_out[11]), .BORROW_IN(subtractor_1_91_borrow_out), .A(1'b0),
    .BORROW_OUT(subtractor_1_75_borrow_out));  // open: SUB
  Multiplexer multiplexer_16 (
    .in0(subtractor_1_91_sub), .in1(multiplexer_22_out), .out(multiplexer_16_out),
    .sel(subtractor_1_16_borrow_out[5]));
  SUBTRACTOR_1 subtractor_1_76 (
    .B(multiplexer_137_out[11]), .BORROW_IN(subtractor_1_92_borrow_out), .A(multiplexer_16_out),
    .SUB(subtractor_1_76_sub), .BORROW_OUT(subtractor_1_76_borrow_out));
  Multiplexer multiplexer_17 (
    .in0(subtractor_1_92_sub), .in1(multiplexer_23_out), .out(multiplexer_17_out),
    .sel(subtractor_1_16_borrow_out[4]));
  SUBTRACTOR_1 subtractor_1_77 (
    .B(multiplexer_137_out[11]), .BORROW_IN(subtractor_1_93_borrow_out), .A(multiplexer_17_out),
    .SUB(subtractor_1_77_sub), .BORROW_OUT(subtractor_1_77_borrow_out));
  Multiplexer multiplexer_18 (
    .in0(subtractor_1_93_sub), .in1(multiplexer_24_out), .out(multiplexer_18_out),
    .sel(subtractor_1_16_borrow_out[3]));
  SUBTRACTOR_1 subtractor_1_78 (
    .B(multiplexer_137_out[11]), .BORROW_IN(subtractor_1_94_borrow_out), .A(multiplexer_18_out),
    .SUB(subtractor_1_78_sub), .BORROW_OUT(subtractor_1_78_borrow_out));
  Multiplexer multiplexer_19 (
    .in0(subtractor_1_94_sub), .in1(multiplexer_25_out), .out(multiplexer_19_out),
    .sel(subtractor_1_16_borrow_out[2]));
  SUBTRACTOR_1 subtractor_1_79 (
    .B(multiplexer_137_out[11]), .BORROW_IN(subtractor_1_95_borrow_out), .A(multiplexer_19_out),
    .SUB(subtractor_1_79_sub), .BORROW_OUT(subtractor_1_79_borrow_out));
  Multiplexer multiplexer_20 (
    .in0(subtractor_1_95_sub), .in1(multiplexer_26_out), .out(multiplexer_20_out),
    .sel(subtractor_1_16_borrow_out[1]));
  SUBTRACTOR_1 subtractor_1_80 (
    .B(multiplexer_137_out[11]), .BORROW_IN(subtractor_1_96_borrow_out), .A(multiplexer_20_out),
    .SUB(subtractor_1_80_sub), .BORROW_OUT(subtractor_1_80_borrow_out));
  Multiplexer multiplexer_21 (
    .in0(subtractor_1_80_sub), .in1(multiplexer_20_out), .out(REMAINDER[11]),
    .sel(subtractor_1_16_borrow_out[0]));
  SUBTRACTOR_1 subtractor_1_81 (
    .B(multiplexer_137_out[10]), .BORROW_IN(subtractor_1_97_borrow_out), .A(1'b0),
    .BORROW_OUT(subtractor_1_81_borrow_out));  // open: SUB
  SUBTRACTOR_1 subtractor_1_82 (
    .B(multiplexer_137_out[10]), .BORROW_IN(subtractor_1_98_borrow_out), .A(1'b0),
    .BORROW_OUT(subtractor_1_82_borrow_out));  // open: SUB
  SUBTRACTOR_1 subtractor_1_83 (
    .B(multiplexer_137_out[10]), .BORROW_IN(subtractor_1_99_borrow_out), .A(1'b0),
    .BORROW_OUT(subtractor_1_83_borrow_out));  // open: SUB
  SUBTRACTOR_1 subtractor_1_84 (
    .B(multiplexer_137_out[10]), .BORROW_IN(subtractor_1_100_borrow_out), .A(1'b0),
    .BORROW_OUT(subtractor_1_84_borrow_out));  // open: SUB
  SUBTRACTOR_1 subtractor_1_85 (
    .B(multiplexer_137_out[10]), .BORROW_IN(subtractor_1_101_borrow_out), .A(1'b0),
    .BORROW_OUT(subtractor_1_85_borrow_out));  // open: SUB
  SUBTRACTOR_1 subtractor_1_86 (
    .B(multiplexer_137_out[10]), .BORROW_IN(subtractor_1_102_borrow_out), .A(1'b0),
    .BORROW_OUT(subtractor_1_86_borrow_out));  // open: SUB
  SUBTRACTOR_1 subtractor_1_87 (
    .B(multiplexer_137_out[10]), .BORROW_IN(subtractor_1_103_borrow_out), .A(1'b0),
    .BORROW_OUT(subtractor_1_87_borrow_out));  // open: SUB
  SUBTRACTOR_1 subtractor_1_88 (
    .B(multiplexer_137_out[10]), .BORROW_IN(subtractor_1_104_borrow_out), .A(1'b0),
    .BORROW_OUT(subtractor_1_88_borrow_out));  // open: SUB
  SUBTRACTOR_1 subtractor_1_89 (
    .B(multiplexer_137_out[10]), .BORROW_IN(subtractor_1_105_borrow_out), .A(1'b0),
    .BORROW_OUT(subtractor_1_89_borrow_out));  // open: SUB
  SUBTRACTOR_1 subtractor_1_90 (
    .B(multiplexer_137_out[10]), .BORROW_IN(subtractor_1_106_borrow_out), .A(1'b0),
    .BORROW_OUT(subtractor_1_90_borrow_out));  // open: SUB
  Multiplexer multiplexer_22 (
    .in0(subtractor_1_106_sub), .in1(multiplexer_29_out), .out(multiplexer_22_out),
    .sel(subtractor_1_16_borrow_out[6]));
  SUBTRACTOR_1 subtractor_1_91 (
    .B(multiplexer_137_out[10]), .BORROW_IN(subtractor_1_107_borrow_out), .A(multiplexer_22_out),
    .SUB(subtractor_1_91_sub), .BORROW_OUT(subtractor_1_91_borrow_out));
  Multiplexer multiplexer_23 (
    .in0(subtractor_1_107_sub), .in1(multiplexer_30_out), .out(multiplexer_23_out),
    .sel(subtractor_1_16_borrow_out[5]));
  SUBTRACTOR_1 subtractor_1_92 (
    .B(multiplexer_137_out[10]), .BORROW_IN(subtractor_1_108_borrow_out), .A(multiplexer_23_out),
    .SUB(subtractor_1_92_sub), .BORROW_OUT(subtractor_1_92_borrow_out));
  Multiplexer multiplexer_24 (
    .in0(subtractor_1_108_sub), .in1(multiplexer_31_out), .out(multiplexer_24_out),
    .sel(subtractor_1_16_borrow_out[4]));
  SUBTRACTOR_1 subtractor_1_93 (
    .B(multiplexer_137_out[10]), .BORROW_IN(subtractor_1_109_borrow_out), .A(multiplexer_24_out),
    .SUB(subtractor_1_93_sub), .BORROW_OUT(subtractor_1_93_borrow_out));
  Multiplexer multiplexer_25 (
    .in0(subtractor_1_109_sub), .in1(multiplexer_32_out), .out(multiplexer_25_out),
    .sel(subtractor_1_16_borrow_out[3]));
  SUBTRACTOR_1 subtractor_1_94 (
    .B(multiplexer_137_out[10]), .BORROW_IN(subtractor_1_110_borrow_out), .A(multiplexer_25_out),
    .SUB(subtractor_1_94_sub), .BORROW_OUT(subtractor_1_94_borrow_out));
  Multiplexer multiplexer_26 (
    .in0(subtractor_1_110_sub), .in1(multiplexer_33_out), .out(multiplexer_26_out),
    .sel(subtractor_1_16_borrow_out[2]));
  SUBTRACTOR_1 subtractor_1_95 (
    .B(multiplexer_137_out[10]), .BORROW_IN(subtractor_1_111_borrow_out), .A(multiplexer_26_out),
    .SUB(subtractor_1_95_sub), .BORROW_OUT(subtractor_1_95_borrow_out));
  Multiplexer multiplexer_27 (
    .in0(subtractor_1_111_sub), .in1(multiplexer_34_out), .out(multiplexer_27_out),
    .sel(subtractor_1_16_borrow_out[1]));
  SUBTRACTOR_1 subtractor_1_96 (
    .B(multiplexer_137_out[10]), .BORROW_IN(subtractor_1_112_borrow_out), .A(multiplexer_27_out),
    .SUB(subtractor_1_96_sub), .BORROW_OUT(subtractor_1_96_borrow_out));
  Multiplexer multiplexer_28 (
    .in0(subtractor_1_96_sub), .in1(multiplexer_27_out), .out(REMAINDER[10]),
    .sel(subtractor_1_16_borrow_out[0]));
  SUBTRACTOR_1 subtractor_1_97 (
    .B(multiplexer_137_out[9]), .BORROW_IN(subtractor_1_113_borrow_out), .A(1'b0),
    .BORROW_OUT(subtractor_1_97_borrow_out));  // open: SUB
  SUBTRACTOR_1 subtractor_1_98 (
    .B(multiplexer_137_out[9]), .BORROW_IN(subtractor_1_114_borrow_out), .A(1'b0),
    .BORROW_OUT(subtractor_1_98_borrow_out));  // open: SUB
  SUBTRACTOR_1 subtractor_1_99 (
    .B(multiplexer_137_out[9]), .BORROW_IN(subtractor_1_115_borrow_out), .A(1'b0),
    .BORROW_OUT(subtractor_1_99_borrow_out));  // open: SUB
  SUBTRACTOR_1 subtractor_1_100 (
    .B(multiplexer_137_out[9]), .BORROW_IN(subtractor_1_116_borrow_out), .A(1'b0),
    .BORROW_OUT(subtractor_1_100_borrow_out));  // open: SUB
  SUBTRACTOR_1 subtractor_1_101 (
    .B(multiplexer_137_out[9]), .BORROW_IN(subtractor_1_117_borrow_out), .A(1'b0),
    .BORROW_OUT(subtractor_1_101_borrow_out));  // open: SUB
  SUBTRACTOR_1 subtractor_1_102 (
    .B(multiplexer_137_out[9]), .BORROW_IN(subtractor_1_118_borrow_out), .A(1'b0),
    .BORROW_OUT(subtractor_1_102_borrow_out));  // open: SUB
  SUBTRACTOR_1 subtractor_1_103 (
    .B(multiplexer_137_out[9]), .BORROW_IN(subtractor_1_119_borrow_out), .A(1'b0),
    .BORROW_OUT(subtractor_1_103_borrow_out));  // open: SUB
  SUBTRACTOR_1 subtractor_1_104 (
    .B(multiplexer_137_out[9]), .BORROW_IN(subtractor_1_120_borrow_out), .A(1'b0),
    .BORROW_OUT(subtractor_1_104_borrow_out));  // open: SUB
  SUBTRACTOR_1 subtractor_1_105 (
    .B(multiplexer_137_out[9]), .BORROW_IN(subtractor_1_121_borrow_out), .A(1'b0),
    .BORROW_OUT(subtractor_1_105_borrow_out));  // open: SUB
  Multiplexer multiplexer_29 (
    .in0(subtractor_1_121_sub), .in1(multiplexer_37_out), .out(multiplexer_29_out),
    .sel(subtractor_1_16_borrow_out[7]));
  SUBTRACTOR_1 subtractor_1_106 (
    .B(multiplexer_137_out[9]), .BORROW_IN(subtractor_1_122_borrow_out), .A(multiplexer_29_out),
    .SUB(subtractor_1_106_sub), .BORROW_OUT(subtractor_1_106_borrow_out));
  Multiplexer multiplexer_30 (
    .in0(subtractor_1_122_sub), .in1(multiplexer_38_out), .out(multiplexer_30_out),
    .sel(subtractor_1_16_borrow_out[6]));
  SUBTRACTOR_1 subtractor_1_107 (
    .B(multiplexer_137_out[9]), .BORROW_IN(subtractor_1_123_borrow_out), .A(multiplexer_30_out),
    .SUB(subtractor_1_107_sub), .BORROW_OUT(subtractor_1_107_borrow_out));
  Multiplexer multiplexer_31 (
    .in0(subtractor_1_123_sub), .in1(multiplexer_39_out), .out(multiplexer_31_out),
    .sel(subtractor_1_16_borrow_out[5]));
  SUBTRACTOR_1 subtractor_1_108 (
    .B(multiplexer_137_out[9]), .BORROW_IN(subtractor_1_124_borrow_out), .A(multiplexer_31_out),
    .SUB(subtractor_1_108_sub), .BORROW_OUT(subtractor_1_108_borrow_out));
  Multiplexer multiplexer_32 (
    .in0(subtractor_1_124_sub), .in1(multiplexer_40_out), .out(multiplexer_32_out),
    .sel(subtractor_1_16_borrow_out[4]));
  SUBTRACTOR_1 subtractor_1_109 (
    .B(multiplexer_137_out[9]), .BORROW_IN(subtractor_1_125_borrow_out), .A(multiplexer_32_out),
    .SUB(subtractor_1_109_sub), .BORROW_OUT(subtractor_1_109_borrow_out));
  Multiplexer multiplexer_33 (
    .in0(subtractor_1_125_sub), .in1(multiplexer_41_out), .out(multiplexer_33_out),
    .sel(subtractor_1_16_borrow_out[3]));
  SUBTRACTOR_1 subtractor_1_110 (
    .B(multiplexer_137_out[9]), .BORROW_IN(subtractor_1_126_borrow_out), .A(multiplexer_33_out),
    .SUB(subtractor_1_110_sub), .BORROW_OUT(subtractor_1_110_borrow_out));
  Multiplexer multiplexer_34 (
    .in0(subtractor_1_126_sub), .in1(multiplexer_42_out), .out(multiplexer_34_out),
    .sel(subtractor_1_16_borrow_out[2]));
  SUBTRACTOR_1 subtractor_1_111 (
    .B(multiplexer_137_out[9]), .BORROW_IN(subtractor_1_127_borrow_out), .A(multiplexer_34_out),
    .SUB(subtractor_1_111_sub), .BORROW_OUT(subtractor_1_111_borrow_out));
  Multiplexer multiplexer_35 (
    .in0(subtractor_1_127_sub), .in1(multiplexer_43_out), .out(multiplexer_35_out),
    .sel(subtractor_1_16_borrow_out[1]));
  SUBTRACTOR_1 subtractor_1_112 (
    .B(multiplexer_137_out[9]), .BORROW_IN(subtractor_1_128_borrow_out), .A(multiplexer_35_out),
    .SUB(subtractor_1_112_sub), .BORROW_OUT(subtractor_1_112_borrow_out));
  Multiplexer multiplexer_36 (
    .in0(subtractor_1_112_sub), .in1(multiplexer_35_out), .out(REMAINDER[9]),
    .sel(subtractor_1_16_borrow_out[0]));
  SUBTRACTOR_1 subtractor_1_113 (
    .B(multiplexer_137_out[8]), .BORROW_IN(subtractor_1_129_borrow_out), .A(1'b0),
    .BORROW_OUT(subtractor_1_113_borrow_out));  // open: SUB
  SUBTRACTOR_1 subtractor_1_114 (
    .B(multiplexer_137_out[8]), .BORROW_IN(subtractor_1_130_borrow_out), .A(1'b0),
    .BORROW_OUT(subtractor_1_114_borrow_out));  // open: SUB
  SUBTRACTOR_1 subtractor_1_115 (
    .B(multiplexer_137_out[8]), .BORROW_IN(subtractor_1_131_borrow_out), .A(1'b0),
    .BORROW_OUT(subtractor_1_115_borrow_out));  // open: SUB
  SUBTRACTOR_1 subtractor_1_116 (
    .B(multiplexer_137_out[8]), .BORROW_IN(subtractor_1_132_borrow_out), .A(1'b0),
    .BORROW_OUT(subtractor_1_116_borrow_out));  // open: SUB
  SUBTRACTOR_1 subtractor_1_117 (
    .B(multiplexer_137_out[8]), .BORROW_IN(subtractor_1_133_borrow_out), .A(1'b0),
    .BORROW_OUT(subtractor_1_117_borrow_out));  // open: SUB
  SUBTRACTOR_1 subtractor_1_118 (
    .B(multiplexer_137_out[8]), .BORROW_IN(subtractor_1_134_borrow_out), .A(1'b0),
    .BORROW_OUT(subtractor_1_118_borrow_out));  // open: SUB
  SUBTRACTOR_1 subtractor_1_119 (
    .B(multiplexer_137_out[8]), .BORROW_IN(subtractor_1_135_borrow_out), .A(1'b0),
    .BORROW_OUT(subtractor_1_119_borrow_out));  // open: SUB
  SUBTRACTOR_1 subtractor_1_120 (
    .B(multiplexer_137_out[8]), .BORROW_IN(subtractor_1_136_borrow_out), .A(1'b0),
    .BORROW_OUT(subtractor_1_120_borrow_out));  // open: SUB
  Multiplexer multiplexer_37 (
    .in0(subtractor_1_136_sub), .in1(multiplexer_47_out), .out(multiplexer_37_out),
    .sel(subtractor_1_16_borrow_out[8]));
  SUBTRACTOR_1 subtractor_1_121 (
    .B(multiplexer_137_out[8]), .BORROW_IN(subtractor_1_137_borrow_out), .A(multiplexer_37_out),
    .SUB(subtractor_1_121_sub), .BORROW_OUT(subtractor_1_121_borrow_out));
  Multiplexer multiplexer_38 (
    .in0(subtractor_1_137_sub), .in1(multiplexer_48_out), .out(multiplexer_38_out),
    .sel(subtractor_1_16_borrow_out[7]));
  SUBTRACTOR_1 subtractor_1_122 (
    .B(multiplexer_137_out[8]), .BORROW_IN(subtractor_1_138_borrow_out), .A(multiplexer_38_out),
    .SUB(subtractor_1_122_sub), .BORROW_OUT(subtractor_1_122_borrow_out));
  Multiplexer multiplexer_39 (
    .in0(subtractor_1_138_sub), .in1(multiplexer_49_out), .out(multiplexer_39_out),
    .sel(subtractor_1_16_borrow_out[6]));
  SUBTRACTOR_1 subtractor_1_123 (
    .B(multiplexer_137_out[8]), .BORROW_IN(subtractor_1_139_borrow_out), .A(multiplexer_39_out),
    .SUB(subtractor_1_123_sub), .BORROW_OUT(subtractor_1_123_borrow_out));
  Multiplexer multiplexer_40 (
    .in0(subtractor_1_139_sub), .in1(multiplexer_50_out), .out(multiplexer_40_out),
    .sel(subtractor_1_16_borrow_out[5]));
  SUBTRACTOR_1 subtractor_1_124 (
    .B(multiplexer_137_out[8]), .BORROW_IN(subtractor_1_140_borrow_out), .A(multiplexer_40_out),
    .SUB(subtractor_1_124_sub), .BORROW_OUT(subtractor_1_124_borrow_out));
  Multiplexer multiplexer_41 (
    .in0(subtractor_1_140_sub), .in1(multiplexer_51_out), .out(multiplexer_41_out),
    .sel(subtractor_1_16_borrow_out[4]));
  SUBTRACTOR_1 subtractor_1_125 (
    .B(multiplexer_137_out[8]), .BORROW_IN(subtractor_1_141_borrow_out), .A(multiplexer_41_out),
    .SUB(subtractor_1_125_sub), .BORROW_OUT(subtractor_1_125_borrow_out));
  Multiplexer multiplexer_42 (
    .in0(subtractor_1_141_sub), .in1(multiplexer_52_out), .out(multiplexer_42_out),
    .sel(subtractor_1_16_borrow_out[3]));
  SUBTRACTOR_1 subtractor_1_126 (
    .B(multiplexer_137_out[8]), .BORROW_IN(subtractor_1_142_borrow_out), .A(multiplexer_42_out),
    .SUB(subtractor_1_126_sub), .BORROW_OUT(subtractor_1_126_borrow_out));
  Multiplexer multiplexer_43 (
    .in0(subtractor_1_142_sub), .in1(multiplexer_53_out), .out(multiplexer_43_out),
    .sel(subtractor_1_16_borrow_out[2]));
  SUBTRACTOR_1 subtractor_1_127 (
    .B(multiplexer_137_out[8]), .BORROW_IN(subtractor_1_143_borrow_out), .A(multiplexer_43_out),
    .SUB(subtractor_1_127_sub), .BORROW_OUT(subtractor_1_127_borrow_out));
  Multiplexer multiplexer_44 (
    .in0(subtractor_1_143_sub), .in1(multiplexer_54_out), .out(multiplexer_44_out),
    .sel(subtractor_1_16_borrow_out[1]));
  SUBTRACTOR_1 subtractor_1_128 (
    .B(multiplexer_137_out[8]), .BORROW_IN(subtractor_1_144_borrow_out), .A(multiplexer_44_out),
    .SUB(subtractor_1_128_sub), .BORROW_OUT(subtractor_1_128_borrow_out));
  Multiplexer multiplexer_45 (
    .in0(subtractor_1_128_sub), .in1(multiplexer_44_out), .out(REMAINDER[8]),
    .sel(subtractor_1_16_borrow_out[0]));
  SUBTRACTOR_1 subtractor_1_129 (
    .B(multiplexer_137_out[7]), .BORROW_IN(subtractor_1_145_borrow_out), .A(1'b0),
    .BORROW_OUT(subtractor_1_129_borrow_out));  // open: SUB
  SUBTRACTOR_1 subtractor_1_130 (
    .B(multiplexer_137_out[7]), .BORROW_IN(subtractor_1_146_borrow_out), .A(1'b0),
    .BORROW_OUT(subtractor_1_130_borrow_out));  // open: SUB
  SUBTRACTOR_1 subtractor_1_131 (
    .B(multiplexer_137_out[7]), .BORROW_IN(subtractor_1_147_borrow_out), .A(1'b0),
    .BORROW_OUT(subtractor_1_131_borrow_out));  // open: SUB
  SUBTRACTOR_1 subtractor_1_132 (
    .B(multiplexer_137_out[7]), .BORROW_IN(subtractor_1_148_borrow_out), .A(1'b0),
    .BORROW_OUT(subtractor_1_132_borrow_out));  // open: SUB
  SUBTRACTOR_1 subtractor_1_133 (
    .B(multiplexer_137_out[7]), .BORROW_IN(subtractor_1_149_borrow_out), .A(1'b0),
    .BORROW_OUT(subtractor_1_133_borrow_out));  // open: SUB
  SUBTRACTOR_1 subtractor_1_134 (
    .B(multiplexer_137_out[7]), .BORROW_IN(subtractor_1_150_borrow_out), .A(1'b0),
    .BORROW_OUT(subtractor_1_134_borrow_out));  // open: SUB
  SUBTRACTOR_1 subtractor_1_135 (
    .B(multiplexer_137_out[7]), .BORROW_IN(subtractor_1_151_borrow_out), .A(1'b0),
    .BORROW_OUT(subtractor_1_135_borrow_out));  // open: SUB
  SUBTRACTOR_1 subtractor_1_136 (
    .B(multiplexer_137_out[7]), .BORROW_IN(subtractor_1_152_borrow_out), .A(multiplexer_47_out),
    .SUB(subtractor_1_136_sub), .BORROW_OUT(subtractor_1_136_borrow_out));
  SUBTRACTOR_1 subtractor_1_137 (
    .B(multiplexer_137_out[7]), .BORROW_IN(subtractor_1_153_borrow_out), .A(multiplexer_48_out),
    .SUB(subtractor_1_137_sub), .BORROW_OUT(subtractor_1_137_borrow_out));
  SUBTRACTOR_1 subtractor_1_138 (
    .B(multiplexer_137_out[7]), .BORROW_IN(subtractor_1_154_borrow_out), .A(multiplexer_49_out),
    .SUB(subtractor_1_138_sub), .BORROW_OUT(subtractor_1_138_borrow_out));
  SUBTRACTOR_1 subtractor_1_139 (
    .B(multiplexer_137_out[7]), .BORROW_IN(subtractor_1_155_borrow_out), .A(multiplexer_50_out),
    .SUB(subtractor_1_139_sub), .BORROW_OUT(subtractor_1_139_borrow_out));
  SUBTRACTOR_1 subtractor_1_140 (
    .B(multiplexer_137_out[7]), .BORROW_IN(subtractor_1_156_borrow_out), .A(multiplexer_51_out),
    .SUB(subtractor_1_140_sub), .BORROW_OUT(subtractor_1_140_borrow_out));
  SUBTRACTOR_1 subtractor_1_141 (
    .B(multiplexer_137_out[7]), .BORROW_IN(subtractor_1_157_borrow_out), .A(multiplexer_52_out),
    .SUB(subtractor_1_141_sub), .BORROW_OUT(subtractor_1_141_borrow_out));
  SUBTRACTOR_1 subtractor_1_142 (
    .B(multiplexer_137_out[7]), .BORROW_IN(subtractor_1_158_borrow_out), .A(multiplexer_53_out),
    .SUB(subtractor_1_142_sub), .BORROW_OUT(subtractor_1_142_borrow_out));
  SUBTRACTOR_1 subtractor_1_143 (
    .B(multiplexer_137_out[7]), .BORROW_IN(subtractor_1_159_borrow_out), .A(multiplexer_54_out),
    .SUB(subtractor_1_143_sub), .BORROW_OUT(subtractor_1_143_borrow_out));
  SUBTRACTOR_1 subtractor_1_144 (
    .B(multiplexer_137_out[7]), .BORROW_IN(subtractor_1_160_borrow_out), .A(multiplexer_55_out),
    .SUB(subtractor_1_144_sub), .BORROW_OUT(subtractor_1_144_borrow_out));
  Multiplexer multiplexer_46 (
    .in0(subtractor_1_144_sub), .in1(multiplexer_55_out), .out(REMAINDER[7]),
    .sel(subtractor_1_16_borrow_out[0]));
  Multiplexer multiplexer_47 (
    .in0(subtractor_1_151_sub), .in1(multiplexer_56_out), .out(multiplexer_47_out),
    .sel(subtractor_1_16_borrow_out[9]));
  Multiplexer multiplexer_48 (
    .in0(subtractor_1_152_sub), .in1(multiplexer_57_out), .out(multiplexer_48_out),
    .sel(subtractor_1_16_borrow_out[8]));
  Multiplexer multiplexer_49 (
    .in0(subtractor_1_153_sub), .in1(multiplexer_58_out), .out(multiplexer_49_out),
    .sel(subtractor_1_16_borrow_out[7]));
  Multiplexer multiplexer_50 (
    .in0(subtractor_1_154_sub), .in1(multiplexer_59_out), .out(multiplexer_50_out),
    .sel(subtractor_1_16_borrow_out[6]));
  Multiplexer multiplexer_51 (
    .in0(subtractor_1_155_sub), .in1(multiplexer_60_out), .out(multiplexer_51_out),
    .sel(subtractor_1_16_borrow_out[5]));
  Multiplexer multiplexer_52 (
    .in0(subtractor_1_156_sub), .in1(multiplexer_61_out), .out(multiplexer_52_out),
    .sel(subtractor_1_16_borrow_out[4]));
  Multiplexer multiplexer_53 (
    .in0(subtractor_1_157_sub), .in1(multiplexer_62_out), .out(multiplexer_53_out),
    .sel(subtractor_1_16_borrow_out[3]));
  Multiplexer multiplexer_54 (
    .in0(subtractor_1_158_sub), .in1(multiplexer_63_out), .out(multiplexer_54_out),
    .sel(subtractor_1_16_borrow_out[2]));
  Multiplexer multiplexer_55 (
    .in0(subtractor_1_159_sub), .in1(multiplexer_64_out), .out(multiplexer_55_out),
    .sel(subtractor_1_16_borrow_out[1]));
  SUBTRACTOR_1 subtractor_1_145 (
    .B(multiplexer_137_out[6]), .BORROW_IN(subtractor_1_161_borrow_out), .A(1'b0),
    .BORROW_OUT(subtractor_1_145_borrow_out));  // open: SUB
  SUBTRACTOR_1 subtractor_1_146 (
    .B(multiplexer_137_out[6]), .BORROW_IN(subtractor_1_162_borrow_out), .A(1'b0),
    .BORROW_OUT(subtractor_1_146_borrow_out));  // open: SUB
  SUBTRACTOR_1 subtractor_1_147 (
    .B(multiplexer_137_out[6]), .BORROW_IN(subtractor_1_163_borrow_out), .A(1'b0),
    .BORROW_OUT(subtractor_1_147_borrow_out));  // open: SUB
  SUBTRACTOR_1 subtractor_1_148 (
    .B(multiplexer_137_out[6]), .BORROW_IN(subtractor_1_164_borrow_out), .A(1'b0),
    .BORROW_OUT(subtractor_1_148_borrow_out));  // open: SUB
  SUBTRACTOR_1 subtractor_1_149 (
    .B(multiplexer_137_out[6]), .BORROW_IN(subtractor_1_165_borrow_out), .A(1'b0),
    .BORROW_OUT(subtractor_1_149_borrow_out));  // open: SUB
  SUBTRACTOR_1 subtractor_1_150 (
    .B(multiplexer_137_out[6]), .BORROW_IN(subtractor_1_166_borrow_out), .A(1'b0),
    .BORROW_OUT(subtractor_1_150_borrow_out));  // open: SUB
  Multiplexer multiplexer_56 (
    .in0(subtractor_1_166_sub), .in1(multiplexer_67_out), .out(multiplexer_56_out),
    .sel(subtractor_1_16_borrow_out[10]));
  SUBTRACTOR_1 subtractor_1_151 (
    .B(multiplexer_137_out[6]), .BORROW_IN(subtractor_1_167_borrow_out), .A(multiplexer_56_out),
    .SUB(subtractor_1_151_sub), .BORROW_OUT(subtractor_1_151_borrow_out));
  Multiplexer multiplexer_57 (
    .in0(subtractor_1_167_sub), .in1(multiplexer_68_out), .out(multiplexer_57_out),
    .sel(subtractor_1_16_borrow_out[9]));
  SUBTRACTOR_1 subtractor_1_152 (
    .B(multiplexer_137_out[6]), .BORROW_IN(subtractor_1_168_borrow_out), .A(multiplexer_57_out),
    .SUB(subtractor_1_152_sub), .BORROW_OUT(subtractor_1_152_borrow_out));
  Multiplexer multiplexer_58 (
    .in0(subtractor_1_168_sub), .in1(multiplexer_69_out), .out(multiplexer_58_out),
    .sel(subtractor_1_16_borrow_out[8]));
  SUBTRACTOR_1 subtractor_1_153 (
    .B(multiplexer_137_out[6]), .BORROW_IN(subtractor_1_169_borrow_out), .A(multiplexer_58_out),
    .SUB(subtractor_1_153_sub), .BORROW_OUT(subtractor_1_153_borrow_out));
  Multiplexer multiplexer_59 (
    .in0(subtractor_1_169_sub), .in1(multiplexer_70_out), .out(multiplexer_59_out),
    .sel(subtractor_1_16_borrow_out[7]));
  SUBTRACTOR_1 subtractor_1_154 (
    .B(multiplexer_137_out[6]), .BORROW_IN(subtractor_1_170_borrow_out), .A(multiplexer_59_out),
    .SUB(subtractor_1_154_sub), .BORROW_OUT(subtractor_1_154_borrow_out));
  Multiplexer multiplexer_60 (
    .in0(subtractor_1_170_sub), .in1(multiplexer_71_out), .out(multiplexer_60_out),
    .sel(subtractor_1_16_borrow_out[6]));
  SUBTRACTOR_1 subtractor_1_155 (
    .B(multiplexer_137_out[6]), .BORROW_IN(subtractor_1_171_borrow_out), .A(multiplexer_60_out),
    .SUB(subtractor_1_155_sub), .BORROW_OUT(subtractor_1_155_borrow_out));
  Multiplexer multiplexer_61 (
    .in0(subtractor_1_171_sub), .in1(multiplexer_72_out), .out(multiplexer_61_out),
    .sel(subtractor_1_16_borrow_out[5]));
  SUBTRACTOR_1 subtractor_1_156 (
    .B(multiplexer_137_out[6]), .BORROW_IN(subtractor_1_172_borrow_out), .A(multiplexer_61_out),
    .SUB(subtractor_1_156_sub), .BORROW_OUT(subtractor_1_156_borrow_out));
  Multiplexer multiplexer_62 (
    .in0(subtractor_1_172_sub), .in1(multiplexer_73_out), .out(multiplexer_62_out),
    .sel(subtractor_1_16_borrow_out[4]));
  SUBTRACTOR_1 subtractor_1_157 (
    .B(multiplexer_137_out[6]), .BORROW_IN(subtractor_1_173_borrow_out), .A(multiplexer_62_out),
    .SUB(subtractor_1_157_sub), .BORROW_OUT(subtractor_1_157_borrow_out));
  Multiplexer multiplexer_63 (
    .in0(subtractor_1_173_sub), .in1(multiplexer_74_out), .out(multiplexer_63_out),
    .sel(subtractor_1_16_borrow_out[3]));
  SUBTRACTOR_1 subtractor_1_158 (
    .B(multiplexer_137_out[6]), .BORROW_IN(subtractor_1_174_borrow_out), .A(multiplexer_63_out),
    .SUB(subtractor_1_158_sub), .BORROW_OUT(subtractor_1_158_borrow_out));
  Multiplexer multiplexer_64 (
    .in0(subtractor_1_174_sub), .in1(multiplexer_75_out), .out(multiplexer_64_out),
    .sel(subtractor_1_16_borrow_out[2]));
  SUBTRACTOR_1 subtractor_1_159 (
    .B(multiplexer_137_out[6]), .BORROW_IN(subtractor_1_175_borrow_out), .A(multiplexer_64_out),
    .SUB(subtractor_1_159_sub), .BORROW_OUT(subtractor_1_159_borrow_out));
  Multiplexer multiplexer_65 (
    .in0(subtractor_1_175_sub), .in1(multiplexer_76_out), .out(multiplexer_65_out),
    .sel(subtractor_1_16_borrow_out[1]));
  SUBTRACTOR_1 subtractor_1_160 (
    .B(multiplexer_137_out[6]), .BORROW_IN(subtractor_1_176_borrow_out), .A(multiplexer_65_out),
    .SUB(subtractor_1_160_sub), .BORROW_OUT(subtractor_1_160_borrow_out));
  Multiplexer multiplexer_66 (
    .in0(subtractor_1_160_sub), .in1(multiplexer_65_out), .out(REMAINDER[6]),
    .sel(subtractor_1_16_borrow_out[0]));
  SUBTRACTOR_1 subtractor_1_161 (
    .B(multiplexer_137_out[5]), .BORROW_IN(subtractor_1_177_borrow_out), .A(1'b0),
    .BORROW_OUT(subtractor_1_161_borrow_out));  // open: SUB
  SUBTRACTOR_1 subtractor_1_162 (
    .B(multiplexer_137_out[5]), .BORROW_IN(subtractor_1_178_borrow_out), .A(1'b0),
    .BORROW_OUT(subtractor_1_162_borrow_out));  // open: SUB
  SUBTRACTOR_1 subtractor_1_163 (
    .B(multiplexer_137_out[5]), .BORROW_IN(subtractor_1_179_borrow_out), .A(1'b0),
    .BORROW_OUT(subtractor_1_163_borrow_out));  // open: SUB
  SUBTRACTOR_1 subtractor_1_164 (
    .B(multiplexer_137_out[5]), .BORROW_IN(subtractor_1_180_borrow_out), .A(1'b0),
    .BORROW_OUT(subtractor_1_164_borrow_out));  // open: SUB
  SUBTRACTOR_1 subtractor_1_165 (
    .B(multiplexer_137_out[5]), .BORROW_IN(subtractor_1_181_borrow_out), .A(1'b0),
    .BORROW_OUT(subtractor_1_165_borrow_out));  // open: SUB
  Multiplexer multiplexer_67 (
    .in0(subtractor_1_181_sub), .in1(multiplexer_79_out), .out(multiplexer_67_out),
    .sel(subtractor_1_16_borrow_out[11]));
  SUBTRACTOR_1 subtractor_1_166 (
    .B(multiplexer_137_out[5]), .BORROW_IN(subtractor_1_182_borrow_out), .A(multiplexer_67_out),
    .SUB(subtractor_1_166_sub), .BORROW_OUT(subtractor_1_166_borrow_out));
  Multiplexer multiplexer_68 (
    .in0(subtractor_1_182_sub), .in1(multiplexer_80_out), .out(multiplexer_68_out),
    .sel(subtractor_1_16_borrow_out[10]));
  SUBTRACTOR_1 subtractor_1_167 (
    .B(multiplexer_137_out[5]), .BORROW_IN(subtractor_1_183_borrow_out), .A(multiplexer_68_out),
    .SUB(subtractor_1_167_sub), .BORROW_OUT(subtractor_1_167_borrow_out));
  Multiplexer multiplexer_69 (
    .in0(subtractor_1_183_sub), .in1(multiplexer_81_out), .out(multiplexer_69_out),
    .sel(subtractor_1_16_borrow_out[9]));
  SUBTRACTOR_1 subtractor_1_168 (
    .B(multiplexer_137_out[5]), .BORROW_IN(subtractor_1_184_borrow_out), .A(multiplexer_69_out),
    .SUB(subtractor_1_168_sub), .BORROW_OUT(subtractor_1_168_borrow_out));
  Multiplexer multiplexer_70 (
    .in0(subtractor_1_184_sub), .in1(multiplexer_82_out), .out(multiplexer_70_out),
    .sel(subtractor_1_16_borrow_out[8]));
  SUBTRACTOR_1 subtractor_1_169 (
    .B(multiplexer_137_out[5]), .BORROW_IN(subtractor_1_185_borrow_out), .A(multiplexer_70_out),
    .SUB(subtractor_1_169_sub), .BORROW_OUT(subtractor_1_169_borrow_out));
  Multiplexer multiplexer_71 (
    .in0(subtractor_1_185_sub), .in1(multiplexer_83_out), .out(multiplexer_71_out),
    .sel(subtractor_1_16_borrow_out[7]));
  SUBTRACTOR_1 subtractor_1_170 (
    .B(multiplexer_137_out[5]), .BORROW_IN(subtractor_1_186_borrow_out), .A(multiplexer_71_out),
    .SUB(subtractor_1_170_sub), .BORROW_OUT(subtractor_1_170_borrow_out));
  Multiplexer multiplexer_72 (
    .in0(subtractor_1_186_sub), .in1(multiplexer_84_out), .out(multiplexer_72_out),
    .sel(subtractor_1_16_borrow_out[6]));
  SUBTRACTOR_1 subtractor_1_171 (
    .B(multiplexer_137_out[5]), .BORROW_IN(subtractor_1_187_borrow_out), .A(multiplexer_72_out),
    .SUB(subtractor_1_171_sub), .BORROW_OUT(subtractor_1_171_borrow_out));
  Multiplexer multiplexer_73 (
    .in0(subtractor_1_187_sub), .in1(multiplexer_85_out), .out(multiplexer_73_out),
    .sel(subtractor_1_16_borrow_out[5]));
  SUBTRACTOR_1 subtractor_1_172 (
    .B(multiplexer_137_out[5]), .BORROW_IN(subtractor_1_188_borrow_out), .A(multiplexer_73_out),
    .SUB(subtractor_1_172_sub), .BORROW_OUT(subtractor_1_172_borrow_out));
  Multiplexer multiplexer_74 (
    .in0(subtractor_1_188_sub), .in1(multiplexer_86_out), .out(multiplexer_74_out),
    .sel(subtractor_1_16_borrow_out[4]));
  SUBTRACTOR_1 subtractor_1_173 (
    .B(multiplexer_137_out[5]), .BORROW_IN(subtractor_1_189_borrow_out), .A(multiplexer_74_out),
    .SUB(subtractor_1_173_sub), .BORROW_OUT(subtractor_1_173_borrow_out));
  Multiplexer multiplexer_75 (
    .in0(subtractor_1_189_sub), .in1(multiplexer_87_out), .out(multiplexer_75_out),
    .sel(subtractor_1_16_borrow_out[3]));
  SUBTRACTOR_1 subtractor_1_174 (
    .B(multiplexer_137_out[5]), .BORROW_IN(subtractor_1_190_borrow_out), .A(multiplexer_75_out),
    .SUB(subtractor_1_174_sub), .BORROW_OUT(subtractor_1_174_borrow_out));
  Multiplexer multiplexer_76 (
    .in0(subtractor_1_190_sub), .in1(multiplexer_88_out), .out(multiplexer_76_out),
    .sel(subtractor_1_16_borrow_out[2]));
  SUBTRACTOR_1 subtractor_1_175 (
    .B(multiplexer_137_out[5]), .BORROW_IN(subtractor_1_191_borrow_out), .A(multiplexer_76_out),
    .SUB(subtractor_1_175_sub), .BORROW_OUT(subtractor_1_175_borrow_out));
  Multiplexer multiplexer_77 (
    .in0(subtractor_1_191_sub), .in1(multiplexer_89_out), .out(multiplexer_77_out),
    .sel(subtractor_1_16_borrow_out[1]));
  SUBTRACTOR_1 subtractor_1_176 (
    .B(multiplexer_137_out[5]), .BORROW_IN(subtractor_1_192_borrow_out), .A(multiplexer_77_out),
    .SUB(subtractor_1_176_sub), .BORROW_OUT(subtractor_1_176_borrow_out));
  Multiplexer multiplexer_78 (
    .in0(subtractor_1_176_sub), .in1(multiplexer_77_out), .out(REMAINDER[5]),
    .sel(subtractor_1_16_borrow_out[0]));
  SUBTRACTOR_1 subtractor_1_177 (
    .B(multiplexer_137_out[4]), .BORROW_IN(subtractor_1_193_borrow_out), .A(1'b0),
    .BORROW_OUT(subtractor_1_177_borrow_out));  // open: SUB
  SUBTRACTOR_1 subtractor_1_178 (
    .B(multiplexer_137_out[4]), .BORROW_IN(subtractor_1_194_borrow_out), .A(1'b0),
    .BORROW_OUT(subtractor_1_178_borrow_out));  // open: SUB
  SUBTRACTOR_1 subtractor_1_179 (
    .B(multiplexer_137_out[4]), .BORROW_IN(subtractor_1_195_borrow_out), .A(1'b0),
    .BORROW_OUT(subtractor_1_179_borrow_out));  // open: SUB
  SUBTRACTOR_1 subtractor_1_180 (
    .B(multiplexer_137_out[4]), .BORROW_IN(subtractor_1_196_borrow_out), .A(1'b0),
    .BORROW_OUT(subtractor_1_180_borrow_out));  // open: SUB
  Multiplexer multiplexer_79 (
    .in0(subtractor_1_196_sub), .in1(multiplexer_92_out), .out(multiplexer_79_out),
    .sel(subtractor_1_16_borrow_out[12]));
  SUBTRACTOR_1 subtractor_1_181 (
    .B(multiplexer_137_out[4]), .BORROW_IN(subtractor_1_197_borrow_out), .A(multiplexer_79_out),
    .SUB(subtractor_1_181_sub), .BORROW_OUT(subtractor_1_181_borrow_out));
  Multiplexer multiplexer_80 (
    .in0(subtractor_1_197_sub), .in1(multiplexer_93_out), .out(multiplexer_80_out),
    .sel(subtractor_1_16_borrow_out[11]));
  SUBTRACTOR_1 subtractor_1_182 (
    .B(multiplexer_137_out[4]), .BORROW_IN(subtractor_1_198_borrow_out), .A(multiplexer_80_out),
    .SUB(subtractor_1_182_sub), .BORROW_OUT(subtractor_1_182_borrow_out));
  Multiplexer multiplexer_81 (
    .in0(subtractor_1_198_sub), .in1(multiplexer_94_out), .out(multiplexer_81_out),
    .sel(subtractor_1_16_borrow_out[10]));
  SUBTRACTOR_1 subtractor_1_183 (
    .B(multiplexer_137_out[4]), .BORROW_IN(subtractor_1_199_borrow_out), .A(multiplexer_81_out),
    .SUB(subtractor_1_183_sub), .BORROW_OUT(subtractor_1_183_borrow_out));
  Multiplexer multiplexer_82 (
    .in0(subtractor_1_199_sub), .in1(multiplexer_95_out), .out(multiplexer_82_out),
    .sel(subtractor_1_16_borrow_out[9]));
  SUBTRACTOR_1 subtractor_1_184 (
    .B(multiplexer_137_out[4]), .BORROW_IN(subtractor_1_200_borrow_out), .A(multiplexer_82_out),
    .SUB(subtractor_1_184_sub), .BORROW_OUT(subtractor_1_184_borrow_out));
  Multiplexer multiplexer_83 (
    .in0(subtractor_1_200_sub), .in1(multiplexer_96_out), .out(multiplexer_83_out),
    .sel(subtractor_1_16_borrow_out[8]));
  SUBTRACTOR_1 subtractor_1_185 (
    .B(multiplexer_137_out[4]), .BORROW_IN(subtractor_1_201_borrow_out), .A(multiplexer_83_out),
    .SUB(subtractor_1_185_sub), .BORROW_OUT(subtractor_1_185_borrow_out));
  Multiplexer multiplexer_84 (
    .in0(subtractor_1_201_sub), .in1(multiplexer_97_out), .out(multiplexer_84_out),
    .sel(subtractor_1_16_borrow_out[7]));
  SUBTRACTOR_1 subtractor_1_186 (
    .B(multiplexer_137_out[4]), .BORROW_IN(subtractor_1_202_borrow_out), .A(multiplexer_84_out),
    .SUB(subtractor_1_186_sub), .BORROW_OUT(subtractor_1_186_borrow_out));
  Multiplexer multiplexer_85 (
    .in0(subtractor_1_202_sub), .in1(multiplexer_98_out), .out(multiplexer_85_out),
    .sel(subtractor_1_16_borrow_out[6]));
  SUBTRACTOR_1 subtractor_1_187 (
    .B(multiplexer_137_out[4]), .BORROW_IN(subtractor_1_203_borrow_out), .A(multiplexer_85_out),
    .SUB(subtractor_1_187_sub), .BORROW_OUT(subtractor_1_187_borrow_out));
  Multiplexer multiplexer_86 (
    .in0(subtractor_1_203_sub), .in1(multiplexer_99_out), .out(multiplexer_86_out),
    .sel(subtractor_1_16_borrow_out[5]));
  SUBTRACTOR_1 subtractor_1_188 (
    .B(multiplexer_137_out[4]), .BORROW_IN(subtractor_1_204_borrow_out), .A(multiplexer_86_out),
    .SUB(subtractor_1_188_sub), .BORROW_OUT(subtractor_1_188_borrow_out));
  Multiplexer multiplexer_87 (
    .in0(subtractor_1_204_sub), .in1(multiplexer_100_out), .out(multiplexer_87_out),
    .sel(subtractor_1_16_borrow_out[4]));
  SUBTRACTOR_1 subtractor_1_189 (
    .B(multiplexer_137_out[4]), .BORROW_IN(subtractor_1_205_borrow_out), .A(multiplexer_87_out),
    .SUB(subtractor_1_189_sub), .BORROW_OUT(subtractor_1_189_borrow_out));
  Multiplexer multiplexer_88 (
    .in0(subtractor_1_205_sub), .in1(multiplexer_101_out), .out(multiplexer_88_out),
    .sel(subtractor_1_16_borrow_out[3]));
  SUBTRACTOR_1 subtractor_1_190 (
    .B(multiplexer_137_out[4]), .BORROW_IN(subtractor_1_206_borrow_out), .A(multiplexer_88_out),
    .SUB(subtractor_1_190_sub), .BORROW_OUT(subtractor_1_190_borrow_out));
  Multiplexer multiplexer_89 (
    .in0(subtractor_1_206_sub), .in1(multiplexer_102_out), .out(multiplexer_89_out),
    .sel(subtractor_1_16_borrow_out[2]));
  SUBTRACTOR_1 subtractor_1_191 (
    .B(multiplexer_137_out[4]), .BORROW_IN(subtractor_1_207_borrow_out), .A(multiplexer_89_out),
    .SUB(subtractor_1_191_sub), .BORROW_OUT(subtractor_1_191_borrow_out));
  Multiplexer multiplexer_90 (
    .in0(subtractor_1_207_sub), .in1(multiplexer_103_out), .out(multiplexer_90_out),
    .sel(subtractor_1_16_borrow_out[1]));
  SUBTRACTOR_1 subtractor_1_192 (
    .B(multiplexer_137_out[4]), .BORROW_IN(subtractor_1_208_borrow_out), .A(multiplexer_90_out),
    .SUB(subtractor_1_192_sub), .BORROW_OUT(subtractor_1_192_borrow_out));
  Multiplexer multiplexer_91 (
    .in0(subtractor_1_192_sub), .in1(multiplexer_90_out), .out(REMAINDER[4]),
    .sel(subtractor_1_16_borrow_out[0]));
  SUBTRACTOR_1 subtractor_1_193 (
    .B(multiplexer_137_out[3]), .BORROW_IN(subtractor_1_209_borrow_out), .A(1'b0),
    .BORROW_OUT(subtractor_1_193_borrow_out));  // open: SUB
  SUBTRACTOR_1 subtractor_1_194 (
    .B(multiplexer_137_out[3]), .BORROW_IN(subtractor_1_210_borrow_out), .A(1'b0),
    .BORROW_OUT(subtractor_1_194_borrow_out));  // open: SUB
  SUBTRACTOR_1 subtractor_1_195 (
    .B(multiplexer_137_out[3]), .BORROW_IN(subtractor_1_211_borrow_out), .A(1'b0),
    .BORROW_OUT(subtractor_1_195_borrow_out));  // open: SUB
  Multiplexer multiplexer_92 (
    .in0(subtractor_1_211_sub), .in1(multiplexer_106_out), .out(multiplexer_92_out),
    .sel(subtractor_1_16_borrow_out[13]));
  SUBTRACTOR_1 subtractor_1_196 (
    .B(multiplexer_137_out[3]), .BORROW_IN(subtractor_1_212_borrow_out), .A(multiplexer_92_out),
    .SUB(subtractor_1_196_sub), .BORROW_OUT(subtractor_1_196_borrow_out));
  Multiplexer multiplexer_93 (
    .in0(subtractor_1_212_sub), .in1(multiplexer_107_out), .out(multiplexer_93_out),
    .sel(subtractor_1_16_borrow_out[12]));
  SUBTRACTOR_1 subtractor_1_197 (
    .B(multiplexer_137_out[3]), .BORROW_IN(subtractor_1_213_borrow_out), .A(multiplexer_93_out),
    .SUB(subtractor_1_197_sub), .BORROW_OUT(subtractor_1_197_borrow_out));
  Multiplexer multiplexer_94 (
    .in0(subtractor_1_213_sub), .in1(multiplexer_108_out), .out(multiplexer_94_out),
    .sel(subtractor_1_16_borrow_out[11]));
  SUBTRACTOR_1 subtractor_1_198 (
    .B(multiplexer_137_out[3]), .BORROW_IN(subtractor_1_214_borrow_out), .A(multiplexer_94_out),
    .SUB(subtractor_1_198_sub), .BORROW_OUT(subtractor_1_198_borrow_out));
  Multiplexer multiplexer_95 (
    .in0(subtractor_1_214_sub), .in1(multiplexer_109_out), .out(multiplexer_95_out),
    .sel(subtractor_1_16_borrow_out[10]));
  SUBTRACTOR_1 subtractor_1_199 (
    .B(multiplexer_137_out[3]), .BORROW_IN(subtractor_1_215_borrow_out), .A(multiplexer_95_out),
    .SUB(subtractor_1_199_sub), .BORROW_OUT(subtractor_1_199_borrow_out));
  Multiplexer multiplexer_96 (
    .in0(subtractor_1_215_sub), .in1(multiplexer_110_out), .out(multiplexer_96_out),
    .sel(subtractor_1_16_borrow_out[9]));
  SUBTRACTOR_1 subtractor_1_200 (
    .B(multiplexer_137_out[3]), .BORROW_IN(subtractor_1_216_borrow_out), .A(multiplexer_96_out),
    .SUB(subtractor_1_200_sub), .BORROW_OUT(subtractor_1_200_borrow_out));
  Multiplexer multiplexer_97 (
    .in0(subtractor_1_216_sub), .in1(multiplexer_111_out), .out(multiplexer_97_out),
    .sel(subtractor_1_16_borrow_out[8]));
  SUBTRACTOR_1 subtractor_1_201 (
    .B(multiplexer_137_out[3]), .BORROW_IN(subtractor_1_217_borrow_out), .A(multiplexer_97_out),
    .SUB(subtractor_1_201_sub), .BORROW_OUT(subtractor_1_201_borrow_out));
  Multiplexer multiplexer_98 (
    .in0(subtractor_1_217_sub), .in1(multiplexer_112_out), .out(multiplexer_98_out),
    .sel(subtractor_1_16_borrow_out[7]));
  SUBTRACTOR_1 subtractor_1_202 (
    .B(multiplexer_137_out[3]), .BORROW_IN(subtractor_1_218_borrow_out), .A(multiplexer_98_out),
    .SUB(subtractor_1_202_sub), .BORROW_OUT(subtractor_1_202_borrow_out));
  Multiplexer multiplexer_99 (
    .in0(subtractor_1_218_sub), .in1(multiplexer_113_out), .out(multiplexer_99_out),
    .sel(subtractor_1_16_borrow_out[6]));
  SUBTRACTOR_1 subtractor_1_203 (
    .B(multiplexer_137_out[3]), .BORROW_IN(subtractor_1_219_borrow_out), .A(multiplexer_99_out),
    .SUB(subtractor_1_203_sub), .BORROW_OUT(subtractor_1_203_borrow_out));
  Multiplexer multiplexer_100 (
    .in0(subtractor_1_219_sub), .in1(multiplexer_114_out), .out(multiplexer_100_out),
    .sel(subtractor_1_16_borrow_out[5]));
  SUBTRACTOR_1 subtractor_1_204 (
    .B(multiplexer_137_out[3]), .BORROW_IN(subtractor_1_220_borrow_out), .A(multiplexer_100_out),
    .SUB(subtractor_1_204_sub), .BORROW_OUT(subtractor_1_204_borrow_out));
  Multiplexer multiplexer_101 (
    .in0(subtractor_1_220_sub), .in1(multiplexer_115_out), .out(multiplexer_101_out),
    .sel(subtractor_1_16_borrow_out[4]));
  SUBTRACTOR_1 subtractor_1_205 (
    .B(multiplexer_137_out[3]), .BORROW_IN(subtractor_1_221_borrow_out), .A(multiplexer_101_out),
    .SUB(subtractor_1_205_sub), .BORROW_OUT(subtractor_1_205_borrow_out));
  Multiplexer multiplexer_102 (
    .in0(subtractor_1_221_sub), .in1(multiplexer_116_out), .out(multiplexer_102_out),
    .sel(subtractor_1_16_borrow_out[3]));
  SUBTRACTOR_1 subtractor_1_206 (
    .B(multiplexer_137_out[3]), .BORROW_IN(subtractor_1_222_borrow_out), .A(multiplexer_102_out),
    .SUB(subtractor_1_206_sub), .BORROW_OUT(subtractor_1_206_borrow_out));
  Multiplexer multiplexer_103 (
    .in0(subtractor_1_222_sub), .in1(multiplexer_117_out), .out(multiplexer_103_out),
    .sel(subtractor_1_16_borrow_out[2]));
  SUBTRACTOR_1 subtractor_1_207 (
    .B(multiplexer_137_out[3]), .BORROW_IN(subtractor_1_223_borrow_out), .A(multiplexer_103_out),
    .SUB(subtractor_1_207_sub), .BORROW_OUT(subtractor_1_207_borrow_out));
  Multiplexer multiplexer_104 (
    .in0(subtractor_1_223_sub), .in1(multiplexer_118_out), .out(multiplexer_104_out),
    .sel(subtractor_1_16_borrow_out[1]));
  SUBTRACTOR_1 subtractor_1_208 (
    .B(multiplexer_137_out[3]), .BORROW_IN(subtractor_1_224_borrow_out), .A(multiplexer_104_out),
    .SUB(subtractor_1_208_sub), .BORROW_OUT(subtractor_1_208_borrow_out));
  Multiplexer multiplexer_105 (
    .in0(subtractor_1_208_sub), .in1(multiplexer_104_out), .out(REMAINDER[3]),
    .sel(subtractor_1_16_borrow_out[0]));
  SUBTRACTOR_1 subtractor_1_209 (
    .B(multiplexer_137_out[2]), .BORROW_IN(subtractor_1_225_borrow_out), .A(1'b0),
    .BORROW_OUT(subtractor_1_209_borrow_out));  // open: SUB
  SUBTRACTOR_1 subtractor_1_210 (
    .B(multiplexer_137_out[2]), .BORROW_IN(subtractor_1_226_borrow_out), .A(1'b0),
    .BORROW_OUT(subtractor_1_210_borrow_out));  // open: SUB
  Multiplexer multiplexer_106 (
    .in0(subtractor_1_226_sub), .in1(multiplexer_121_out), .out(multiplexer_106_out),
    .sel(subtractor_1_16_borrow_out[14]));
  SUBTRACTOR_1 subtractor_1_211 (
    .B(multiplexer_137_out[2]), .BORROW_IN(subtractor_1_227_borrow_out), .A(multiplexer_106_out),
    .SUB(subtractor_1_211_sub), .BORROW_OUT(subtractor_1_211_borrow_out));
  Multiplexer multiplexer_107 (
    .in0(subtractor_1_227_sub), .in1(multiplexer_122_out), .out(multiplexer_107_out),
    .sel(subtractor_1_16_borrow_out[13]));
  SUBTRACTOR_1 subtractor_1_212 (
    .B(multiplexer_137_out[2]), .BORROW_IN(subtractor_1_228_borrow_out), .A(multiplexer_107_out),
    .SUB(subtractor_1_212_sub), .BORROW_OUT(subtractor_1_212_borrow_out));
  Multiplexer multiplexer_108 (
    .in0(subtractor_1_228_sub), .in1(multiplexer_123_out), .out(multiplexer_108_out),
    .sel(subtractor_1_16_borrow_out[12]));
  SUBTRACTOR_1 subtractor_1_213 (
    .B(multiplexer_137_out[2]), .BORROW_IN(subtractor_1_229_borrow_out), .A(multiplexer_108_out),
    .SUB(subtractor_1_213_sub), .BORROW_OUT(subtractor_1_213_borrow_out));
  Multiplexer multiplexer_109 (
    .in0(subtractor_1_229_sub), .in1(multiplexer_124_out), .out(multiplexer_109_out),
    .sel(subtractor_1_16_borrow_out[11]));
  SUBTRACTOR_1 subtractor_1_214 (
    .B(multiplexer_137_out[2]), .BORROW_IN(subtractor_1_230_borrow_out), .A(multiplexer_109_out),
    .SUB(subtractor_1_214_sub), .BORROW_OUT(subtractor_1_214_borrow_out));
  Multiplexer multiplexer_110 (
    .in0(subtractor_1_230_sub), .in1(multiplexer_125_out), .out(multiplexer_110_out),
    .sel(subtractor_1_16_borrow_out[10]));
  SUBTRACTOR_1 subtractor_1_215 (
    .B(multiplexer_137_out[2]), .BORROW_IN(subtractor_1_231_borrow_out), .A(multiplexer_110_out),
    .SUB(subtractor_1_215_sub), .BORROW_OUT(subtractor_1_215_borrow_out));
  Multiplexer multiplexer_111 (
    .in0(subtractor_1_231_sub), .in1(multiplexer_126_out), .out(multiplexer_111_out),
    .sel(subtractor_1_16_borrow_out[9]));
  SUBTRACTOR_1 subtractor_1_216 (
    .B(multiplexer_137_out[2]), .BORROW_IN(subtractor_1_232_borrow_out), .A(multiplexer_111_out),
    .SUB(subtractor_1_216_sub), .BORROW_OUT(subtractor_1_216_borrow_out));
  Multiplexer multiplexer_112 (
    .in0(subtractor_1_232_sub), .in1(multiplexer_127_out), .out(multiplexer_112_out),
    .sel(subtractor_1_16_borrow_out[8]));
  SUBTRACTOR_1 subtractor_1_217 (
    .B(multiplexer_137_out[2]), .BORROW_IN(subtractor_1_233_borrow_out), .A(multiplexer_112_out),
    .SUB(subtractor_1_217_sub), .BORROW_OUT(subtractor_1_217_borrow_out));
  Multiplexer multiplexer_113 (
    .in0(subtractor_1_233_sub), .in1(multiplexer_128_out), .out(multiplexer_113_out),
    .sel(subtractor_1_16_borrow_out[7]));
  SUBTRACTOR_1 subtractor_1_218 (
    .B(multiplexer_137_out[2]), .BORROW_IN(subtractor_1_234_borrow_out), .A(multiplexer_113_out),
    .SUB(subtractor_1_218_sub), .BORROW_OUT(subtractor_1_218_borrow_out));
  Multiplexer multiplexer_114 (
    .in0(subtractor_1_234_sub), .in1(multiplexer_129_out), .out(multiplexer_114_out),
    .sel(subtractor_1_16_borrow_out[6]));
  SUBTRACTOR_1 subtractor_1_219 (
    .B(multiplexer_137_out[2]), .BORROW_IN(subtractor_1_235_borrow_out), .A(multiplexer_114_out),
    .SUB(subtractor_1_219_sub), .BORROW_OUT(subtractor_1_219_borrow_out));
  Multiplexer multiplexer_115 (
    .in0(subtractor_1_235_sub), .in1(multiplexer_130_out), .out(multiplexer_115_out),
    .sel(subtractor_1_16_borrow_out[5]));
  SUBTRACTOR_1 subtractor_1_220 (
    .B(multiplexer_137_out[2]), .BORROW_IN(subtractor_1_236_borrow_out), .A(multiplexer_115_out),
    .SUB(subtractor_1_220_sub), .BORROW_OUT(subtractor_1_220_borrow_out));
  Multiplexer multiplexer_116 (
    .in0(subtractor_1_236_sub), .in1(multiplexer_131_out), .out(multiplexer_116_out),
    .sel(subtractor_1_16_borrow_out[4]));
  SUBTRACTOR_1 subtractor_1_221 (
    .B(multiplexer_137_out[2]), .BORROW_IN(subtractor_1_237_borrow_out), .A(multiplexer_116_out),
    .SUB(subtractor_1_221_sub), .BORROW_OUT(subtractor_1_221_borrow_out));
  Multiplexer multiplexer_117 (
    .in0(subtractor_1_237_sub), .in1(multiplexer_132_out), .out(multiplexer_117_out),
    .sel(subtractor_1_16_borrow_out[3]));
  SUBTRACTOR_1 subtractor_1_222 (
    .B(multiplexer_137_out[2]), .BORROW_IN(subtractor_1_238_borrow_out), .A(multiplexer_117_out),
    .SUB(subtractor_1_222_sub), .BORROW_OUT(subtractor_1_222_borrow_out));
  Multiplexer multiplexer_118 (
    .in0(subtractor_1_238_sub), .in1(multiplexer_133_out), .out(multiplexer_118_out),
    .sel(subtractor_1_16_borrow_out[2]));
  SUBTRACTOR_1 subtractor_1_223 (
    .B(multiplexer_137_out[2]), .BORROW_IN(subtractor_1_239_borrow_out), .A(multiplexer_118_out),
    .SUB(subtractor_1_223_sub), .BORROW_OUT(subtractor_1_223_borrow_out));
  Multiplexer multiplexer_119 (
    .in0(subtractor_1_239_sub), .in1(multiplexer_134_out), .out(multiplexer_119_out),
    .sel(subtractor_1_16_borrow_out[1]));
  SUBTRACTOR_1 subtractor_1_224 (
    .B(multiplexer_137_out[2]), .BORROW_IN(subtractor_1_240_borrow_out), .A(multiplexer_119_out),
    .SUB(subtractor_1_224_sub), .BORROW_OUT(subtractor_1_224_borrow_out));
  Multiplexer multiplexer_120 (
    .in0(subtractor_1_224_sub), .in1(multiplexer_119_out), .out(REMAINDER[2]),
    .sel(subtractor_1_16_borrow_out[0]));
  SUBTRACTOR_1 subtractor_1_225 (
    .B(multiplexer_137_out[1]), .BORROW_IN(subtractor_1_241_borrow_out), .A(1'b0),
    .BORROW_OUT(subtractor_1_225_borrow_out));  // open: SUB
  Multiplexer multiplexer_121 (
    .in0(subtractor_1_241_sub), .in1(multiplexer_139_out[15]), .out(multiplexer_121_out),
    .sel(subtractor_1_16_borrow_out[15]));
  SUBTRACTOR_1 subtractor_1_226 (
    .B(multiplexer_137_out[1]), .BORROW_IN(subtractor_1_242_borrow_out), .A(multiplexer_121_out),
    .SUB(subtractor_1_226_sub), .BORROW_OUT(subtractor_1_226_borrow_out));
  Multiplexer multiplexer_122 (
    .in0(subtractor_1_242_sub), .in1(multiplexer_139_out[14]), .out(multiplexer_122_out),
    .sel(subtractor_1_16_borrow_out[14]));
  SUBTRACTOR_1 subtractor_1_227 (
    .B(multiplexer_137_out[1]), .BORROW_IN(subtractor_1_243_borrow_out), .A(multiplexer_122_out),
    .SUB(subtractor_1_227_sub), .BORROW_OUT(subtractor_1_227_borrow_out));
  Multiplexer multiplexer_123 (
    .in0(subtractor_1_243_sub), .in1(multiplexer_139_out[13]), .out(multiplexer_123_out),
    .sel(subtractor_1_16_borrow_out[13]));
  SUBTRACTOR_1 subtractor_1_228 (
    .B(multiplexer_137_out[1]), .BORROW_IN(subtractor_1_244_borrow_out), .A(multiplexer_123_out),
    .SUB(subtractor_1_228_sub), .BORROW_OUT(subtractor_1_228_borrow_out));
  Multiplexer multiplexer_124 (
    .in0(subtractor_1_244_sub), .in1(multiplexer_139_out[12]), .out(multiplexer_124_out),
    .sel(subtractor_1_16_borrow_out[12]));
  SUBTRACTOR_1 subtractor_1_229 (
    .B(multiplexer_137_out[1]), .BORROW_IN(subtractor_1_245_borrow_out), .A(multiplexer_124_out),
    .SUB(subtractor_1_229_sub), .BORROW_OUT(subtractor_1_229_borrow_out));
  Multiplexer multiplexer_125 (
    .in0(subtractor_1_245_sub), .in1(multiplexer_139_out[11]), .out(multiplexer_125_out),
    .sel(subtractor_1_16_borrow_out[11]));
  SUBTRACTOR_1 subtractor_1_230 (
    .B(multiplexer_137_out[1]), .BORROW_IN(subtractor_1_246_borrow_out), .A(multiplexer_125_out),
    .SUB(subtractor_1_230_sub), .BORROW_OUT(subtractor_1_230_borrow_out));
  Multiplexer multiplexer_126 (
    .in0(subtractor_1_246_sub), .in1(multiplexer_139_out[10]), .out(multiplexer_126_out),
    .sel(subtractor_1_16_borrow_out[10]));
  SUBTRACTOR_1 subtractor_1_231 (
    .B(multiplexer_137_out[1]), .BORROW_IN(subtractor_1_247_borrow_out), .A(multiplexer_126_out),
    .SUB(subtractor_1_231_sub), .BORROW_OUT(subtractor_1_231_borrow_out));
  Multiplexer multiplexer_127 (
    .in0(subtractor_1_247_sub), .in1(multiplexer_139_out[9]), .out(multiplexer_127_out),
    .sel(subtractor_1_16_borrow_out[9]));
  SUBTRACTOR_1 subtractor_1_232 (
    .B(multiplexer_137_out[1]), .BORROW_IN(subtractor_1_248_borrow_out), .A(multiplexer_127_out),
    .SUB(subtractor_1_232_sub), .BORROW_OUT(subtractor_1_232_borrow_out));
  Multiplexer multiplexer_128 (
    .in0(subtractor_1_248_sub), .in1(multiplexer_139_out[8]), .out(multiplexer_128_out),
    .sel(subtractor_1_16_borrow_out[8]));
  SUBTRACTOR_1 subtractor_1_233 (
    .B(multiplexer_137_out[1]), .BORROW_IN(subtractor_1_249_borrow_out), .A(multiplexer_128_out),
    .SUB(subtractor_1_233_sub), .BORROW_OUT(subtractor_1_233_borrow_out));
  Multiplexer multiplexer_129 (
    .in0(subtractor_1_249_sub), .in1(multiplexer_139_out[7]), .out(multiplexer_129_out),
    .sel(subtractor_1_16_borrow_out[7]));
  SUBTRACTOR_1 subtractor_1_234 (
    .B(multiplexer_137_out[1]), .BORROW_IN(subtractor_1_250_borrow_out), .A(multiplexer_129_out),
    .SUB(subtractor_1_234_sub), .BORROW_OUT(subtractor_1_234_borrow_out));
  Multiplexer multiplexer_130 (
    .in0(subtractor_1_250_sub), .in1(multiplexer_139_out[6]), .out(multiplexer_130_out),
    .sel(subtractor_1_16_borrow_out[6]));
  SUBTRACTOR_1 subtractor_1_235 (
    .B(multiplexer_137_out[1]), .BORROW_IN(subtractor_1_251_borrow_out), .A(multiplexer_130_out),
    .SUB(subtractor_1_235_sub), .BORROW_OUT(subtractor_1_235_borrow_out));
  Multiplexer multiplexer_131 (
    .in0(subtractor_1_251_sub), .in1(multiplexer_139_out[5]), .out(multiplexer_131_out),
    .sel(subtractor_1_16_borrow_out[5]));
  SUBTRACTOR_1 subtractor_1_236 (
    .B(multiplexer_137_out[1]), .BORROW_IN(subtractor_1_252_borrow_out), .A(multiplexer_131_out),
    .SUB(subtractor_1_236_sub), .BORROW_OUT(subtractor_1_236_borrow_out));
  Multiplexer multiplexer_132 (
    .in0(subtractor_1_252_sub), .in1(multiplexer_139_out[4]), .out(multiplexer_132_out),
    .sel(subtractor_1_16_borrow_out[4]));
  SUBTRACTOR_1 subtractor_1_237 (
    .B(multiplexer_137_out[1]), .BORROW_IN(subtractor_1_253_borrow_out), .A(multiplexer_132_out),
    .SUB(subtractor_1_237_sub), .BORROW_OUT(subtractor_1_237_borrow_out));
  Multiplexer multiplexer_133 (
    .in0(subtractor_1_253_sub), .in1(multiplexer_139_out[3]), .out(multiplexer_133_out),
    .sel(subtractor_1_16_borrow_out[3]));
  SUBTRACTOR_1 subtractor_1_238 (
    .B(multiplexer_137_out[1]), .BORROW_IN(subtractor_1_254_borrow_out), .A(multiplexer_133_out),
    .SUB(subtractor_1_238_sub), .BORROW_OUT(subtractor_1_238_borrow_out));
  Multiplexer multiplexer_134 (
    .in0(subtractor_1_254_sub), .in1(multiplexer_139_out[2]), .out(multiplexer_134_out),
    .sel(subtractor_1_16_borrow_out[2]));
  SUBTRACTOR_1 subtractor_1_239 (
    .B(multiplexer_137_out[1]), .BORROW_IN(subtractor_1_255_borrow_out), .A(multiplexer_134_out),
    .SUB(subtractor_1_239_sub), .BORROW_OUT(subtractor_1_239_borrow_out));
  Multiplexer multiplexer_135 (
    .in0(subtractor_1_255_sub), .in1(multiplexer_139_out[1]), .out(multiplexer_135_out),
    .sel(subtractor_1_16_borrow_out[1]));
  SUBTRACTOR_1 subtractor_1_240 (
    .B(multiplexer_137_out[1]), .BORROW_IN(subtractor_1_256_borrow_out), .A(multiplexer_135_out),
    .SUB(subtractor_1_240_sub), .BORROW_OUT(subtractor_1_240_borrow_out));
  Multiplexer multiplexer_136 (
    .in0(subtractor_1_240_sub), .in1(multiplexer_135_out), .out(REMAINDER[1]),
    .sel(subtractor_1_16_borrow_out[0]));
  TWOS_COMP_16_BIT twos_comp_16_bit_2 (.DATA_IN(DIVISIOR), .DATA_OUT(twos_comp_16_bit_2_data_out));
  Multiplexer #(.width(16)) multiplexer_137 (
    .in0(DIVISIOR), .in1(twos_comp_16_bit_2_data_out), .out(multiplexer_137_out), .sel(DIVISIOR[15]));
  SUBTRACTOR_1 subtractor_1_241 (
    .B(multiplexer_137_out[0]), .A(multiplexer_139_out[15]), .SUB(subtractor_1_241_sub),
    .BORROW_OUT(subtractor_1_241_borrow_out));  // open: BORROW_IN
  SUBTRACTOR_1 subtractor_1_242 (
    .B(multiplexer_137_out[0]), .A(multiplexer_139_out[14]), .SUB(subtractor_1_242_sub),
    .BORROW_OUT(subtractor_1_242_borrow_out));  // open: BORROW_IN
  SUBTRACTOR_1 subtractor_1_243 (
    .B(multiplexer_137_out[0]), .A(multiplexer_139_out[13]), .SUB(subtractor_1_243_sub),
    .BORROW_OUT(subtractor_1_243_borrow_out));  // open: BORROW_IN
  SUBTRACTOR_1 subtractor_1_244 (
    .B(multiplexer_137_out[0]), .A(multiplexer_139_out[12]), .SUB(subtractor_1_244_sub),
    .BORROW_OUT(subtractor_1_244_borrow_out));  // open: BORROW_IN
  SUBTRACTOR_1 subtractor_1_245 (
    .B(multiplexer_137_out[0]), .A(multiplexer_139_out[11]), .SUB(subtractor_1_245_sub),
    .BORROW_OUT(subtractor_1_245_borrow_out));  // open: BORROW_IN
  SUBTRACTOR_1 subtractor_1_246 (
    .B(multiplexer_137_out[0]), .A(multiplexer_139_out[10]), .SUB(subtractor_1_246_sub),
    .BORROW_OUT(subtractor_1_246_borrow_out));  // open: BORROW_IN
  SUBTRACTOR_1 subtractor_1_247 (
    .B(multiplexer_137_out[0]), .A(multiplexer_139_out[9]), .SUB(subtractor_1_247_sub),
    .BORROW_OUT(subtractor_1_247_borrow_out));  // open: BORROW_IN
  SUBTRACTOR_1 subtractor_1_248 (
    .B(multiplexer_137_out[0]), .A(multiplexer_139_out[8]), .SUB(subtractor_1_248_sub),
    .BORROW_OUT(subtractor_1_248_borrow_out));  // open: BORROW_IN
  SUBTRACTOR_1 subtractor_1_249 (
    .B(multiplexer_137_out[0]), .A(multiplexer_139_out[7]), .SUB(subtractor_1_249_sub),
    .BORROW_OUT(subtractor_1_249_borrow_out));  // open: BORROW_IN
  SUBTRACTOR_1 subtractor_1_250 (
    .B(multiplexer_137_out[0]), .A(multiplexer_139_out[6]), .SUB(subtractor_1_250_sub),
    .BORROW_OUT(subtractor_1_250_borrow_out));  // open: BORROW_IN
  SUBTRACTOR_1 subtractor_1_251 (
    .B(multiplexer_137_out[0]), .A(multiplexer_139_out[5]), .SUB(subtractor_1_251_sub),
    .BORROW_OUT(subtractor_1_251_borrow_out));  // open: BORROW_IN
  SUBTRACTOR_1 subtractor_1_252 (
    .B(multiplexer_137_out[0]), .A(multiplexer_139_out[4]), .SUB(subtractor_1_252_sub),
    .BORROW_OUT(subtractor_1_252_borrow_out));  // open: BORROW_IN
  SUBTRACTOR_1 subtractor_1_253 (
    .B(multiplexer_137_out[0]), .A(multiplexer_139_out[3]), .SUB(subtractor_1_253_sub),
    .BORROW_OUT(subtractor_1_253_borrow_out));  // open: BORROW_IN
  SUBTRACTOR_1 subtractor_1_254 (
    .B(multiplexer_137_out[0]), .A(multiplexer_139_out[2]), .SUB(subtractor_1_254_sub),
    .BORROW_OUT(subtractor_1_254_borrow_out));  // open: BORROW_IN
  SUBTRACTOR_1 subtractor_1_255 (
    .B(multiplexer_137_out[0]), .A(multiplexer_139_out[1]), .SUB(subtractor_1_255_sub),
    .BORROW_OUT(subtractor_1_255_borrow_out));  // open: BORROW_IN
  SUBTRACTOR_1 subtractor_1_256 (
    .B(multiplexer_137_out[0]), .A(multiplexer_139_out[0]), .SUB(subtractor_1_256_sub),
    .BORROW_OUT(subtractor_1_256_borrow_out));  // open: BORROW_IN
  Multiplexer multiplexer_138 (
    .in0(subtractor_1_256_sub), .in1(multiplexer_139_out[0]), .out(REMAINDER[0]),
    .sel(subtractor_1_16_borrow_out[0]));
  Multiplexer #(.width(16)) multiplexer_139 (
    .in0(DIVIDEND), .in1(twos_comp_16_bit_3_data_out), .out(multiplexer_139_out), .sel(DIVIDEND[15]));
  TWOS_COMP_16_BIT twos_comp_16_bit_3 (.DATA_IN(DIVIDEND), .DATA_OUT(twos_comp_16_bit_3_data_out));
endmodule

module COMPARATOR_16_BIT (
  input  [15:0] A,
  input  [15:0] B,
  output A_GREATER_THAN_B,
  output A_EQUAL_TO_B,
  output A_LESS_THAN_B
);

  wire not_2_out, not_3_out, or_1_out;
  wire [14:0] subtractor_16_bit_1_sub;

  SUBTRACTOR_16_BIT subtractor_16_bit_1 (
    .A(A), .B(B), .SUB({A_LESS_THAN_B, subtractor_16_bit_1_sub}));  // open: BORROW_IN, BORROW_OUT
  or or_1 (or_1_out, subtractor_16_bit_1_sub[0], subtractor_16_bit_1_sub[1], subtractor_16_bit_1_sub[2], subtractor_16_bit_1_sub[3], subtractor_16_bit_1_sub[4], subtractor_16_bit_1_sub[5], subtractor_16_bit_1_sub[6], subtractor_16_bit_1_sub[7], subtractor_16_bit_1_sub[8], subtractor_16_bit_1_sub[9], subtractor_16_bit_1_sub[10], subtractor_16_bit_1_sub[11], subtractor_16_bit_1_sub[12], subtractor_16_bit_1_sub[13], subtractor_16_bit_1_sub[14], A_LESS_THAN_B);
  not not_1 (A_EQUAL_TO_B, or_1_out);
  not not_2 (not_2_out, A_LESS_THAN_B);
  and and_1 (A_GREATER_THAN_B, not_2_out, not_3_out);
  not not_3 (not_3_out, A_EQUAL_TO_B);
endmodule

module ALU (
  input  [3:0] OPCODE,
  input  [15:0] A,
  input  [15:0] B,
  input  ALU_READ,
  output GREATER,
  output EQUAL,
  output LESSER,
  output [15:0] DATA_OUT,
  output ZERO
);

  wire or_2_out;
  wire [15:0] adder_16_bit_1_sum, and_1_out, divider_16_bit_1_quotient, divider_16_bit_1_remainder,
       multiplexer_1_out, multiplier_16_bit_1_mul, nand_1_out, nor_1_out, not_1_out, or_1_out,
       subtractor_16_bit_1_sub, xor_1_out;

  assign not_1_out = ~A;  // NOT_Gate not_1, 16 bits wide
  assign and_1_out = A & B;  // AND_Gate and_1, 16 bits wide
  assign or_1_out = A | B;  // OR_Gate or_1, 16 bits wide
  ADDER_16_BIT adder_16_bit_1 (.A(A), .B(B), .SUM(adder_16_bit_1_sum));  // open: CARRY_IN, CARRY_OUT
  SUBTRACTOR_16_BIT subtractor_16_bit_1 (.A(A), .B(B), .SUB(subtractor_16_bit_1_sub));  // open: BORROW_IN, BORROW_OUT
  MULTIPLIER_16_BIT multiplier_16_bit_1 (.A(A), .B(B), .MUL(multiplier_16_bit_1_mul));
  DIVIDER_16_BIT divider_16_bit_1 (
    .DIVISIOR(B), .DIVIDEND(A), .QUOTIENT(divider_16_bit_1_quotient), .REMAINDER(divider_16_bit_1_remainder));
  COMPARATOR_16_BIT comparator_16_bit_1 (
    .A(A), .B(B), .A_GREATER_THAN_B(GREATER), .A_EQUAL_TO_B(EQUAL), .A_LESS_THAN_B(LESSER));
  assign xor_1_out = A ^ B;  // XOR_Gate xor_1, 16 bits wide
  assign nand_1_out = ~(A & B);  // NAND_Gate nand_1, 16 bits wide
  assign nor_1_out = ~(A | B);  // NOR_Gate nor_1, 16 bits wide
  Multiplexer #(.select(4), .width(16)) multiplexer_1 (
    .in0(adder_16_bit_1_sum), .in1(subtractor_16_bit_1_sub), .in2(multiplier_16_bit_1_mul),
    .in3(divider_16_bit_1_quotient), .in4(divider_16_bit_1_remainder), .in5(not_1_out), .in6(and_1_out),
    .in7(or_1_out), .in8(xor_1_out), .in9(nand_1_out), .in10(nor_1_out), .out(multiplexer_1_out), .sel(OPCODE));  // open: in11, in12, in13, in14, in15
  assign DATA_OUT = ALU_READ ? multiplexer_1_out : 16'bz;  // Controlled_Buffer controlled_buffer_1
  or or_2 (or_2_out, multiplexer_1_out[0], multiplexer_1_out[1], multiplexer_1_out[2], multiplexer_1_out[3], multiplexer_1_out[4], multiplexer_1_out[5], multiplexer_1_out[6], multiplexer_1_out[7], multiplexer_1_out[8], multiplexer_1_out[9], multiplexer_1_out[10], multiplexer_1_out[11], multiplexer_1_out[12], multiplexer_1_out[13], multiplexer_1_out[14], multiplexer_1_out[15]);
  not not_2 (ZERO, or_2_out);
endmodule

module GENERAL_REGISTER (
  input  [15:0] DATA_IN,
  input  WRITE,
  input  CLOCK,
  input  RESET,
  input  READ,
  output [15:0] DEFAULT_OUTPUT,
  output [15:0] BUS_OUTPUT
);

  REGISTER_16_BIT register_16_bit_1 (
    .WRITE(WRITE), .CLOCK(CLOCK), .RESET(RESET), .DATA_IN(DATA_IN), .DEFAULT_OUTPUT(DEFAULT_OUTPUT));
  assign BUS_OUTPUT = READ ? DEFAULT_OUTPUT : 16'bz;  // Controlled_Buffer controlled_buffer_1
endmodule

module REGISTER_16_BIT (
  input  [15:0] DATA_IN,
  input  WRITE,
  input  CLOCK,
  input  RESET,
  output [15:0] DEFAULT_OUTPUT
);

  REGISTER_8_BIT register_8_bit_1 (
    .DATA_IN(DATA_IN[7:0]), .STORE(WRITE), .CLOCK(CLOCK), .RESET(RESET), .DATA_OUT(DEFAULT_OUTPUT[7:0]));
  REGISTER_8_BIT register_8_bit_2 (
    .DATA_IN(DATA_IN[15:8]), .STORE(CLOCK), .CLOCK(WRITE), .RESET(RESET), .DATA_OUT(DEFAULT_OUTPUT[15:8]));
endmodule

module PROGRAM_COUNTER (
  input  COUNTER_ENABLE,
  input  CLOCK,
  input  [15:0] JUMP_ADDRESS,
  input  JUMP,
  input  RESET,
  input  READ,
  output [15:0] DEFAULT_OUTPUT,
  output [15:0] BUS_OUTPUT
);

  wire not_1_out, or_1_out;
  wire [15:0] adder_16_bit_1_sum, multiplexer_1_out, register_16_bit_1_default_output;

  REGISTER_16_BIT register_16_bit_1 (
    .WRITE(COUNTER_ENABLE), .CLOCK(not_1_out), .RESET(RESET), .DATA_IN(DEFAULT_OUTPUT),
    .DEFAULT_OUTPUT(register_16_bit_1_default_output));
  not not_1 (not_1_out, CLOCK);
  ADDER_16_BIT adder_16_bit_1 (
    .A(register_16_bit_1_default_output), .B(16'h1), .SUM(adder_16_bit_1_sum));  // open: CARRY_IN, CARRY_OUT
  Multiplexer #(.width(16)) multiplexer_1 (
    .in0(adder_16_bit_1_sum), .in1(JUMP_ADDRESS), .out(multiplexer_1_out), .sel(JUMP));
  or or_1 (or_1_out, COUNTER_ENABLE, JUMP);
  REGISTER_16_BIT register_16_bit_2 (
    .WRITE(or_1_out), .CLOCK(CLOCK), .RESET(RESET), .DATA_IN(multiplexer_1_out),
    .DEFAULT_OUTPUT(DEFAULT_OUTPUT));
  assign BUS_OUTPUT = READ ? DEFAULT_OUTPUT : 16'bz;  // Controlled_Buffer controlled_buffer_1
endmodule

module CPU_CLOCK (
  input  INPUT_CLOCK,
  input  CLOCK_ENABLE,
  input  HALT,
  output CLOCK
);

  wire not_1_out;

  not not_1 (not_1_out, HALT);
  and and_1 (CLOCK, INPUT_CLOCK, CLOCK_ENABLE, not_1_out);
endmodule

module FLAGS_REGISTER (
  input  GREATER,
  input  SET_CMP_FLAGS,
  input  EQUALS,
  input  CLOCK,
  input  RESET,
  input  LESSER,
  input  ZERO,
  input  SET_ZERO_FLAG,
  output GREATER_FLAG,
  output EQUAL_FLAG,
  output LESSER_FLAG,
  output ZERO_FLAG
);

  REGISTER_1_BIT register_1_bit_1 (
    .STORE(SET_CMP_FLAGS), .DATA_IN(GREATER), .CLOCK(CLOCK), .RESET(RESET), .DATA_OUT(GREATER_FLAG));
  REGISTER_1_BIT register_1_bit_2 (
    .STORE(SET_CMP_FLAGS), .DATA_IN(EQUALS), .CLOCK(CLOCK), .RESET(RESET), .DATA_OUT(EQUAL_FLAG));
  REGISTER_1_BIT register_1_bit_3 (
    .STORE(SET_CMP_FLAGS), .DATA_IN(LESSER), .CLOCK(CLOCK), .RESET(RESET), .DATA_OUT(LESSER_FLAG));
  REGISTER_1_BIT register_1_bit_4 (
    .STORE(SET_ZERO_FLAG), .DATA_IN(ZERO), .CLOCK(CLOCK), .RESET(RESET), .DATA_OUT(ZERO_FLAG));
endmodule

module MEMORY_ADDRESS_REGISTER (
  input  ADDRESS_WRITE,
  input  CLOCK,
  input  ADDRESS_READ,
  input  [15:0] ADDRESS_IN,
  input  RESET,
  output [15:0] BUS_OUT,
  output [15:0] DEFAULT_OUT
);

  GENERAL_REGISTER general_register_1 (
    .WRITE(ADDRESS_WRITE), .CLOCK(CLOCK), .RESET(RESET), .READ(ADDRESS_READ), .DATA_IN(ADDRESS_IN),
    .DEFAULT_OUTPUT(DEFAULT_OUT), .BUS_OUTPUT(BUS_OUT));
endmodule

module STEP_COUNTER (
  input  RESET,
  input  CLOCK,
  output [3:0] DATA_OUT
);

  Counter #(.max('hf), .width(4)) counter_1 (
    .clr(RESET), .up(1'b1), .count(1'b1), .clk(CLOCK), .Q(DATA_OUT));  // open: load, D, carry
endmodule

module INSTRUCTION_REGISTER (
  input  [15:0] INSTRUCTION_IN,
  input  INSTRUCTION_WRITE,
  input  CLOCK,
  input  RESET,
  input  READ_OPERAND_TO_UPPER_BITS_OF_BUS,
  input  READ_OPERAND_TO_LOWER_BITS_OF_BUS,
  output [15:0] INSTRUCTION_OUT,
  output [7:0] OPERAND_TO_UPPER_BITS_OF_BUS,
  output [7:0] OPERAND_TO_LOWER_BITS_OF_BUS
);

  REGISTER_16_BIT register_16_bit_1 (
    .WRITE(INSTRUCTION_WRITE), .CLOCK(CLOCK), .RESET(RESET), .DATA_IN(INSTRUCTION_IN),
    .DEFAULT_OUTPUT(INSTRUCTION_OUT));
  assign OPERAND_TO_UPPER_BITS_OF_BUS = READ_OPERAND_TO_UPPER_BITS_OF_BUS ? INSTRUCTION_OUT[7:0] : 8'bz;  // Controlled_Buffer controlled_buffer_1
  assign OPERAND_TO_LOWER_BITS_OF_BUS = READ_OPERAND_TO_LOWER_BITS_OF_BUS ? INSTRUCTION_OUT[7:0] : 8'bz;  // Controlled_Buffer controlled_buffer_2
endmodule

module STACK (
  input  RESET,
  input  STACK_UP,
  input  STACK_DOWN,
  input  DATA_WRITE,
  input  [15:0] DATA_IN,
  input  CLOCK,
  input  DATA_READ,
  output [15:0] DATA_OUT
);

  wire not_1_out, not_2_out, or_1_out, or_2_out;
  wire [15:0] adder_16_bit_1_sum, multiplexer_1_out, ram_1_dout, register_16_bit_1_default_output,
       register_16_bit_2_default_output, twos_comp_16_bit_1_data_out;

  or or_1 (or_1_out, STACK_UP, STACK_DOWN);
  not not_1 (not_1_out, or_1_out);
  REGISTER_16_BIT register_16_bit_1 (
    .WRITE(not_1_out), .CLOCK(not_1_out), .RESET(RESET), .DATA_IN(register_16_bit_2_default_output),
    .DEFAULT_OUTPUT(register_16_bit_1_default_output));
  not not_2 (not_2_out, STACK_UP);
  Multiplexer #(.width(16)) multiplexer_1 (
    .in0(16'h1), .in1(twos_comp_16_bit_1_data_out), .out(multiplexer_1_out), .sel(or_2_out));
  TWOS_COMP_16_BIT twos_comp_16_bit_1 (.DATA_IN(16'h1), .DATA_OUT(twos_comp_16_bit_1_data_out));
  or or_2 (or_2_out, not_2_out, STACK_DOWN);
  ADDER_16_BIT adder_16_bit_1 (
    .A(register_16_bit_1_default_output), .B(multiplexer_1_out), .SUM(adder_16_bit_1_sum));  // open: CARRY_IN, CARRY_OUT
  REGISTER_16_BIT register_16_bit_2 (
    .WRITE(or_1_out), .CLOCK(or_1_out), .RESET(RESET), .DATA_IN(adder_16_bit_1_sum),
    .DEFAULT_OUTPUT(register_16_bit_2_default_output));
  RAM #(.addrWidth(16), .dataWidth(16), .enables("line")) ram_1 (
    .we(DATA_WRITE), .clk(CLOCK), .din(DATA_IN), .dout(ram_1_dout));  // open: addr
  assign DATA_OUT = DATA_READ ? ram_1_dout : 16'bz;  // Controlled_Buffer controlled_buffer_1
endmodule

module ALU_OPCODE_ENCODER (
  input  SUM,
  input  SUB,
  input  MUL,
  input  DIV,
  input  MODULO,
  input  A_NOT,
  input  A_AND_B,
  input  A_OR_B,
  input  A_XOR_B,
  input  A_NAND_B,
  input  A_NOR_B,
  output [3:0] out_12
);

  Pull_Resistor pull_resistor_1 (.node(SUM));
  or or_1 (out_12[0], SUB, DIV, A_NOT, A_OR_B, A_NAND_B);
  or or_2 (out_12[1], MUL, DIV, A_AND_B, A_OR_B, A_NOR_B);
  or or_3 (out_12[2], MODULO, A_NOT, A_AND_B, A_OR_B);
  or or_4 (out_12[3], A_XOR_B, A_NAND_B, A_NOR_B);
endmodule
